// Logisim project ALU32-ANES-DAVID-IAN.circ as structural Verilog
module main (
  input  Input,
  input  Write_Enable,
  output out_3
);

  wire and_1_out, and_2_out, not_1_out, not_2_out, or_1_out;

  not not_1 (not_1_out, Input);
  and and_1 (and_1_out, Input, Write_Enable);
  and and_2 (and_2_out, not_1_out, Write_Enable);
  or or_1 (or_1_out, out_3, and_1_out);
  not not_2 (not_2_out, and_2_out);
  and and_3 (out_3, or_1_out, not_2_out);

  // Notes on the sheet:
  //   Gated Latch
endmodule

module Memoria (
  input  [3:0] in_1,
  input  [3:0] in_2
);

  wire decoder_1_out0, main_1_out_3, main_2_out_3, main_3_out_3, main_4_out_3;

  Decoder #(.select(4)) decoder_1 (
    .out0(decoder_1_out0), .sel(in_2), .en(1'b1));  // open: out1, out2, out3, out4, out5, out6, out7, out8, out9, out10, out11, out12, out13, out14, out15
  main main_1 (.Input(in_1[3]), .Write_Enable(decoder_1_out0), .out_3(main_1_out_3));
  LED led_1 (.in(main_1_out_3));
  main main_2 (.Input(in_1[2]), .Write_Enable(decoder_1_out0), .out_3(main_2_out_3));
  main main_3 (.Input(in_1[1]), .Write_Enable(decoder_1_out0), .out_3(main_3_out_3));
  LED led_2 (.in(main_3_out_3));
  LED led_3 (.in(main_2_out_3));
  main main_4 (.Input(in_1[0]), .Write_Enable(decoder_1_out0), .out_3(main_4_out_3));
  LED led_4 (.in(main_4_out_3));
endmodule

module unidad_de_ram_4_bits (
);

  wire main_1_out_3, main_2_out_3, main_3_out_3, main_4_out_3, undriven;
  wire [3:0] undriven_2;

  main main_1 (.Input(undriven_2[3]), .Write_Enable(undriven), .out_3(main_1_out_3));
  main main_2 (.Input(undriven_2[2]), .Write_Enable(undriven), .out_3(main_2_out_3));
  LED led_1 (.in(main_1_out_3));
  LED led_2 (.in(main_2_out_3));
  main main_3 (.Input(undriven_2[1]), .Write_Enable(undriven), .out_3(main_3_out_3));
  LED led_3 (.in(main_3_out_3));
  main main_4 (.Input(undriven_2[0]), .Write_Enable(undriven), .out_3(main_4_out_3));
  LED led_4 (.in(main_4_out_3));
endmodule

module _32_bits_ALU (
  input  [31:0] A,
  input  [31:0] B,
  input  [4:0] in_3,
  output Overflow,
  output Negative,
  output [31:0] Low,
  output [31:0] High
);

  wire _0000_ADD__0001_SUB_negative, _0000_ADD__0001_SUB_overflow, _11000__2_s_Com__2_s_complement_overflow,
       and_1_out, decoder_1_out1, not_1_out, zeros_1_out;
  wire [31:0] _0000_ADD__0001_SUB_result, _0011__MULT_q__low, _00111__AND_out, _01000__OR_out,
       _01110__BEQ__01111__BNE__10000__BGT__10001__BLT_a___b,
       _01110__BEQ__01111__BNE__10000__BGT__10001__BLT_a___b_2,
       _01110__BEQ__01111__BNE__10000__BGT__10001__BLT_a___b_3, _10111__XOR_output, _11000__2_s_Com_out,
       not_2_out;

  // Probe on Low
  // Probe on High
  Decoder #(.select(5)) decoder_1 (
    .out1(decoder_1_out1), .sel(in_3), .en(1'b1));  // open: out0, out2, out3, out4, out5, out6, out7, out8, out9, out10, out11, out12, out13, out14, out15, out16, out17, out18, out19, out20, out21, out22, out23, out24, out25, out26, out27, out28, out29, out30, out31
  _32_bit _0000_ADD__0001_SUB (
    .A(A), .B(B), .Subtraction(decoder_1_out1), .Negative(_0000_ADD__0001_SUB_negative),
    .Result(_0000_ADD__0001_SUB_result), .Overflow(_0000_ADD__0001_SUB_overflow));
  _32_bit_2 _0011__MULT (.B(B), .Q(A), .A__High(High), .Q__Low(_0011__MULT_q__low));
  _32_bit_AND _00111__AND (.A(A), .B(B), .Out(_00111__AND_out));
  _32_bit_OR _01000__OR (.A(A), .B(B), .Out(_01000__OR_out));
  _32_bit_Comparador u_32_bit_comparador_1 (.A(A), .B(B));  // open: A___B, A___B_2, A___B_3
  _32_bit_Comparador _01110__BEQ__01111__BNE__10000__BGT__10001__BLT (
    .A(A), .B(B), .A___B(_01110__BEQ__01111__BNE__10000__BGT__10001__BLT_a___b),
    .A___B_2(_01110__BEQ__01111__BNE__10000__BGT__10001__BLT_a___b_2),
    .A___B_3(_01110__BEQ__01111__BNE__10000__BGT__10001__BLT_a___b_3));
  Zeros zeros_1 (.In(A), .Out(zeros_1_out));
  not not_1 (not_1_out, zeros_1_out);
  _2_s_complement _11000__2_s_Com (
    .In(A), .Out(_11000__2_s_Com_out), ._2_s_Complement_Overflow(_11000__2_s_Com__2_s_complement_overflow));
  _32_bit_XOR _10111__XOR (.A(A), .B(B), .Output(_10111__XOR_output));
  and and_1 (and_1_out, not_1_out, _11000__2_s_Com__2_s_complement_overflow);
  assign not_2_out = ~_01110__BEQ__01111__BNE__10000__BGT__10001__BLT_a___b_2;  // NOT_Gate not_2, 32 bits wide
  Multiplexer #(.select(5), .width(32), .disabled(0)) multiplexer_1 (
    .in0(_0000_ADD__0001_SUB_result), .in1(_0000_ADD__0001_SUB_result), .in3(_0011__MULT_q__low),
    .in7(_00111__AND_out), .in8(_01000__OR_out),
    .in14(_01110__BEQ__01111__BNE__10000__BGT__10001__BLT_a___b_2), .in15(not_2_out),
    .in16(_01110__BEQ__01111__BNE__10000__BGT__10001__BLT_a___b),
    .in17(_01110__BEQ__01111__BNE__10000__BGT__10001__BLT_a___b_3), .in25(_10111__XOR_output),
    .in26(_11000__2_s_Com_out), .out(Low), .sel(in_3), .en(1'b1));  // open: in2, in4, in5, in6, in9, in10, in11, in12, in13, in18, in19, in20, in21, in22, in23, in24, in27, in28, in29, in30, in31
  and and_2 (Negative, _0000_ADD__0001_SUB_negative, decoder_1_out1);
  or or_1 (Overflow, _0000_ADD__0001_SUB_overflow, and_1_out);
endmodule

module _32_bit_XOR (
  input  [31:0] A,
  input  [31:0] B,
  output [31:0] Output
);

  assign Output = A ^ B;  // XOR_Gate xor_1, 32 bits wide
endmodule

module _32_bit_OR (
  input  [31:0] A,
  input  [31:0] B,
  output [31:0] Out
);

  assign Out = A | B;  // OR_Gate or_1, 32 bits wide
endmodule

module _32_bit_AND (
  input  [31:0] A,
  input  [31:0] B,
  output [31:0] Out
);

  assign Out = A & B;  // AND_Gate and_1, 32 bits wide
endmodule

module _32_bit_NOR (
  input  [31:0] A,
  input  [31:0] B,
  output [31:0] A_2
);

  assign A_2 = ~(A | B);  // NOR_Gate nor_1, 32 bits wide
endmodule

module _32_bit_NOT (
  input  [31:0] In,
  output [31:0] Out
);

  assign Out = ~In;  // NOT_Gate not_1, 32 bits wide
endmodule

// +/-
module _32_bit (
  input  [31:0] A,
  input  [31:0] B,
  input  Subtraction,
  output Negative,
  output [31:0] Result,
  output Overflow
);

  wire and_1_out, and_2_out, n2_s_complement_1__2_s_complement_overflow, n8_bit_1_cout, n8_bit_2_cout,
       n8_bit_3_cout, n8_bit_4_cout, not_1_out, xor_1_out, zeros_1_out;
  wire [7:0] n8_bit_1_result, n8_bit_2_result, n8_bit_3_result, n8_bit_4_result;
  wire [31:0] n2_s_complement_1_out;

  Comparator #(.width(32)) comparator_1 (.a(A), .b(B), .lt(Negative));  // open: gt, eq
  _8_bit u_8_bit_1 (
    .Cin(n8_bit_2_cout), .B(B[31:24]), .Subtraction(Subtraction), .A(A[31:24]), .Cout(n8_bit_1_cout),
    .Result(n8_bit_1_result));
  _8_bit u_8_bit_2 (
    .Cin(n8_bit_3_cout), .B(B[23:16]), .Subtraction(Subtraction), .A(A[23:16]), .Cout(n8_bit_2_cout),
    .Result(n8_bit_2_result));
  _8_bit u_8_bit_3 (
    .Cin(n8_bit_4_cout), .B(B[15:8]), .Subtraction(Subtraction), .A(A[15:8]), .Cout(n8_bit_3_cout),
    .Result(n8_bit_3_result));
  _8_bit u_8_bit_4 (
    .Cin(1'b0), .B(B[7:0]), .Subtraction(Subtraction), .A(A[7:0]), .Cout(n8_bit_4_cout),
    .Result(n8_bit_4_result));
  and and_1 (and_1_out, Negative, Subtraction);
  _2_s_complement u_2_s_complement_1 (
    .In({n8_bit_1_result, n8_bit_2_result, n8_bit_3_result, n8_bit_4_result}), .Out(n2_s_complement_1_out),
    ._2_s_Complement_Overflow(n2_s_complement_1__2_s_complement_overflow));
  not not_1 (not_1_out, Subtraction);
  Zeros zeros_1 (.In({n8_bit_1_result, n8_bit_2_result, n8_bit_3_result, n8_bit_4_result}), .Out(zeros_1_out));
  Multiplexer #(.width(32), .enable("false")) multiplexer_1 (
    .in0({n8_bit_1_result, n8_bit_2_result, n8_bit_3_result, n8_bit_4_result}), .in1(n2_s_complement_1_out),
    .out(Result), .sel(and_1_out));
  and and_2 (and_2_out, not_1_out, n8_bit_1_cout);
  xor xor_1 (xor_1_out, n2_s_complement_1__2_s_complement_overflow, zeros_1_out);
  or or_1 (Overflow, and_2_out, xor_1_out);

  // Notes on the sheet:
  //   32 bit Adder and subtractor with 2's complement to display when negative
  //   if not subtraction and last carry out is 1 then overflow.
  //   If they are all zeros, the overflow in the 2's complement is not an overflow
  //   take what is in input 0 if subtract is 0, else take what is in input 1.
endmodule

// +/- 8
module _8_bit (
  input  Cin,
  input  [7:0] B,
  input  Subtraction,
  input  [7:0] A,
  output Cout,
  output [7:0] Result
);

  wire n1_bit_1_cout, n1_bit_2_cout, n1_bit_3_cout, n1_bit_4_cout, n1_bit_5_cout, n1_bit_6_cout,
       n1_bit_7_cout, n1_bit_8_cout, xor_2_out, xor_3_out, xor_4_out, xor_5_out, xor_6_out, xor_7_out,
       xor_8_out, xor_9_out, xor_10_out;

  xor xor_1 (Cout, n1_bit_1_cout, Subtraction);
  xor xor_2 (xor_2_out, Subtraction, B[7]);
  _1_bit u_1_bit_1 (.A(xor_2_out), .B(A[7]), .Cin(n1_bit_2_cout), .S(Result[7]), .Cout(n1_bit_1_cout));
  xor xor_3 (xor_3_out, Subtraction, B[6]);
  _1_bit u_1_bit_2 (.A(xor_3_out), .B(A[6]), .Cin(n1_bit_3_cout), .S(Result[6]), .Cout(n1_bit_2_cout));
  xor xor_4 (xor_4_out, Subtraction, B[5]);
  _1_bit u_1_bit_3 (.A(xor_4_out), .B(A[5]), .Cin(n1_bit_5_cout), .S(Result[5]), .Cout(n1_bit_3_cout));
  xor xor_5 (xor_5_out, Subtraction, B[4]);
  xor xor_6 (xor_6_out, Subtraction, B[3]);
  _1_bit u_1_bit_4 (.A(xor_6_out), .B(A[3]), .Cin(n1_bit_6_cout), .S(Result[3]), .Cout(n1_bit_4_cout));
  _1_bit u_1_bit_5 (.A(xor_5_out), .B(A[4]), .Cin(n1_bit_4_cout), .S(Result[4]), .Cout(n1_bit_5_cout));
  xor xor_7 (xor_7_out, Subtraction, B[2]);
  _1_bit u_1_bit_6 (.A(xor_7_out), .B(A[2]), .Cin(n1_bit_7_cout), .S(Result[2]), .Cout(n1_bit_6_cout));
  xor xor_8 (xor_8_out, Subtraction, B[1]);
  _1_bit u_1_bit_7 (.A(xor_8_out), .B(A[1]), .Cin(n1_bit_8_cout), .S(Result[1]), .Cout(n1_bit_7_cout));
  xor xor_9 (xor_9_out, Subtraction, B[0]);
  _1_bit u_1_bit_8 (.A(xor_9_out), .B(A[0]), .Cin(xor_10_out), .S(Result[0]), .Cout(n1_bit_8_cout));
  xor xor_10 (xor_10_out, Subtraction, Cin);

  // Notes on the sheet:
  //   A-B or A+B
endmodule

// +/-
module _4_bit (
  input  Cin,
  input  [3:0] B,
  input  Subtraction,
  input  [3:0] A,
  output Cout,
  output [3:0] Result
);

  wire n1_bit_1_cout, n1_bit_2_cout, n1_bit_3_cout, n1_bit_4_cout, xor_2_out, xor_3_out, xor_4_out,
       xor_5_out, xor_6_out;

  xor xor_1 (Cout, n1_bit_1_cout, Subtraction);
  xor xor_2 (xor_2_out, Subtraction, B[3]);
  _1_bit u_1_bit_1 (.A(xor_2_out), .B(A[3]), .Cin(n1_bit_2_cout), .S(Result[3]), .Cout(n1_bit_1_cout));
  xor xor_3 (xor_3_out, Subtraction, B[2]);
  _1_bit u_1_bit_2 (.A(xor_3_out), .B(A[2]), .Cin(n1_bit_3_cout), .S(Result[2]), .Cout(n1_bit_2_cout));
  xor xor_4 (xor_4_out, Subtraction, B[1]);
  _1_bit u_1_bit_3 (.A(xor_4_out), .B(A[1]), .Cin(n1_bit_4_cout), .S(Result[1]), .Cout(n1_bit_3_cout));
  xor xor_5 (xor_5_out, Subtraction, B[0]);
  _1_bit u_1_bit_4 (.A(xor_5_out), .B(A[0]), .Cin(xor_6_out), .S(Result[0]), .Cout(n1_bit_4_cout));
  xor xor_6 (xor_6_out, Subtraction, Cin);

  // Notes on the sheet:
  //   A-B or A+B
endmodule

// +/-
module _1_bit (
  input  A,
  input  B,
  input  Cin,
  output S,
  output Cout
);

  wire and_1_out, and_2_out, xor_1_out;

  xor xor_1 (xor_1_out, A, B);
  and and_1 (and_1_out, A, B);
  and and_2 (and_2_out, xor_1_out, Cin);
  xor xor_2 (S, xor_1_out, Cin);
  or or_1 (Cout, and_2_out, and_1_out);
endmodule

// 2's
module _2_s_complement (
  input  [31:0] In,
  output [31:0] Out,
  output _2_s_Complement_Overflow
);

  wire [31:0] not_1_out;

  assign not_1_out = ~In;  // NOT_Gate not_1, 32 bits wide
  Adder #(.width(32)) adder_1 (.a(not_1_out), .b(32'h1), .out(Out), .cin(1'b0), .cout(_2_s_Complement_Overflow));
endmodule

// 0
module Zeros (
  input  [31:0] In,
  output Out
);

  nor nor_1 (Out, In[0], In[1], In[2], In[3], In[4], In[5], In[6], In[7], In[8], In[9], In[10], In[11], In[12], In[13], In[14], In[15], In[16], In[17], In[18], In[19], In[20], In[21], In[22], In[23], In[24], In[25], In[26], In[27], In[28], In[29], In[30], In[31]);

  // Notes on the sheet:
  //   Retorna 1 si todos son ceros
endmodule

module _32_bit_2 (
  input  [31:0] B,
  input  [31:0] Q,
  output [31:0] A__High,
  output [31:0] Q__Low
);

  wire [31:0] _1_a_2, _1_b_2, _1_q_2, _2_a_2, _2_b_2, _2_q_2, _3_a_2, _3_b_2, _3_q_2, _4_a_2, _4_b_2, _4_q_2,
       _5_a_2, _5_b_2, _5_q_2, _6_a_2, _6_b_2, _6_q_2, _7_a_2, _7_b_2, _7_q_2, _8_a_2, _8_b_2, _8_q_2,
       _9_a_2, _9_b_2, _9_q_2, _10_a_2, _10_b_2, _10_q_2, _11_a_2, _11_b_2, _11_q_2, _12_a_2, _12_b_2,
       _12_q_2, _13_a_2, _13_b_2, _13_q_2, _14_a_2, _14_b_2, _14_q_2, _15_a_2, _15_b_2, _15_q_2, _16_a_2,
       _16_b_2, _16_q_2, _17_a_2, _17_b_2, _17_q_2, _18_a_2, _18_b_2, _18_q_2, _19_a_2, _19_b_2, _19_q_2,
       _20_a_2, _20_b_2, _20_q_2, _21_a_2, _21_b_2, _21_q_2, _22_a_2, _22_b_2, _22_q_2, _23_a_2, _23_b_2,
       _23_q_2, _24_a_2, _24_b_2, _24_q_2, _25_a_2, _25_b_2, _25_q_2, _26_a_2, _26_b_2, _26_q_2, _27_a_2,
       _27_b_2, _27_q_2, _28_a_2, _28_b_2, _28_q_2, _29_a_2, _29_b_2, _29_q_2, _30_a_2, _30_b_2, _30_q_2,
       _31_a_2, _31_b_2, _31_q_2, _32_b_2;

  // Probe on {32{1'b0}}
  // Probe on _32_b_2
  Cycle_32_bit _1 (.A({32{1'b0}}), .B(B), .Q(Q), .A_2(_1_a_2), .B_2(_1_b_2), .Q_2(_1_q_2));
  // Probe on _1_a_2
  // Probe on _1_q_2
  // Probe on A__High
  // Probe on Q__Low
  Cycle_32_bit _2 (.A(_1_a_2), .B(_1_b_2), .Q(_1_q_2), .A_2(_2_a_2), .B_2(_2_b_2), .Q_2(_2_q_2));
  // Probe on _2_a_2
  // Probe on _2_q_2
  Cycle_32_bit _3 (.A(_2_a_2), .B(_2_b_2), .Q(_2_q_2), .A_2(_3_a_2), .B_2(_3_b_2), .Q_2(_3_q_2));
  // Probe on _3_a_2
  // Probe on _3_q_2
  Cycle_32_bit _4 (.A(_3_a_2), .B(_3_b_2), .Q(_3_q_2), .A_2(_4_a_2), .B_2(_4_b_2), .Q_2(_4_q_2));
  // Probe on _4_a_2
  // Probe on _4_q_2
  Cycle_32_bit _5 (.A(_4_a_2), .B(_4_b_2), .Q(_4_q_2), .A_2(_5_a_2), .B_2(_5_b_2), .Q_2(_5_q_2));
  // Probe on _5_a_2
  // Probe on _5_q_2
  Cycle_32_bit _6 (.A(_5_a_2), .B(_5_b_2), .Q(_5_q_2), .A_2(_6_a_2), .B_2(_6_b_2), .Q_2(_6_q_2));
  // Probe on _6_a_2
  // Probe on _6_q_2
  Cycle_32_bit _7 (.A(_6_a_2), .B(_6_b_2), .Q(_6_q_2), .A_2(_7_a_2), .B_2(_7_b_2), .Q_2(_7_q_2));
  // Probe on _7_a_2
  // Probe on _7_q_2
  Cycle_32_bit _8 (.A(_7_a_2), .B(_7_b_2), .Q(_7_q_2), .A_2(_8_a_2), .B_2(_8_b_2), .Q_2(_8_q_2));
  // Probe on _8_a_2
  // Probe on _8_q_2
  Cycle_32_bit _9 (.A(_8_a_2), .B(_8_b_2), .Q(_8_q_2), .A_2(_9_a_2), .B_2(_9_b_2), .Q_2(_9_q_2));
  // Probe on _9_a_2
  // Probe on _9_q_2
  Cycle_32_bit _10 (.A(_9_a_2), .B(_9_b_2), .Q(_9_q_2), .A_2(_10_a_2), .B_2(_10_b_2), .Q_2(_10_q_2));
  // Probe on _10_a_2
  // Probe on _10_q_2
  Cycle_32_bit _11 (.A(_10_a_2), .B(_10_b_2), .Q(_10_q_2), .A_2(_11_a_2), .B_2(_11_b_2), .Q_2(_11_q_2));
  // Probe on _11_a_2
  // Probe on _11_q_2
  Cycle_32_bit _12 (.A(_11_a_2), .B(_11_b_2), .Q(_11_q_2), .A_2(_12_a_2), .B_2(_12_b_2), .Q_2(_12_q_2));
  // Probe on _12_a_2
  // Probe on _12_q_2
  Cycle_32_bit _13 (.A(_12_a_2), .B(_12_b_2), .Q(_12_q_2), .A_2(_13_a_2), .B_2(_13_b_2), .Q_2(_13_q_2));
  // Probe on _13_a_2
  // Probe on _13_q_2
  Cycle_32_bit _14 (.A(_13_a_2), .B(_13_b_2), .Q(_13_q_2), .A_2(_14_a_2), .B_2(_14_b_2), .Q_2(_14_q_2));
  // Probe on _14_a_2
  // Probe on _14_q_2
  Cycle_32_bit _15 (.A(_14_a_2), .B(_14_b_2), .Q(_14_q_2), .A_2(_15_a_2), .B_2(_15_b_2), .Q_2(_15_q_2));
  // Probe on _15_a_2
  // Probe on _15_q_2
  Cycle_32_bit _16 (.A(_15_a_2), .B(_15_b_2), .Q(_15_q_2), .A_2(_16_a_2), .B_2(_16_b_2), .Q_2(_16_q_2));
  // Probe on _16_a_2
  // Probe on _16_q_2
  Cycle_32_bit _17 (.A(_16_a_2), .B(_16_b_2), .Q(_16_q_2), .A_2(_17_a_2), .B_2(_17_b_2), .Q_2(_17_q_2));
  // Probe on _17_a_2
  // Probe on _17_q_2
  Cycle_32_bit _18 (.A(_17_a_2), .B(_17_b_2), .Q(_17_q_2), .A_2(_18_a_2), .B_2(_18_b_2), .Q_2(_18_q_2));
  // Probe on _18_a_2
  // Probe on _18_q_2
  Cycle_32_bit _19 (.A(_18_a_2), .B(_18_b_2), .Q(_18_q_2), .A_2(_19_a_2), .B_2(_19_b_2), .Q_2(_19_q_2));
  // Probe on _19_a_2
  // Probe on _19_q_2
  Cycle_32_bit _20 (.A(_19_a_2), .B(_19_b_2), .Q(_19_q_2), .A_2(_20_a_2), .B_2(_20_b_2), .Q_2(_20_q_2));
  // Probe on _20_a_2
  // Probe on _20_q_2
  Cycle_32_bit _21 (.A(_20_a_2), .B(_20_b_2), .Q(_20_q_2), .A_2(_21_a_2), .B_2(_21_b_2), .Q_2(_21_q_2));
  // Probe on _21_a_2
  // Probe on _21_q_2
  Cycle_32_bit _22 (.A(_21_a_2), .B(_21_b_2), .Q(_21_q_2), .A_2(_22_a_2), .B_2(_22_b_2), .Q_2(_22_q_2));
  // Probe on _22_a_2
  // Probe on _22_q_2
  Cycle_32_bit _23 (.A(_22_a_2), .B(_22_b_2), .Q(_22_q_2), .A_2(_23_a_2), .B_2(_23_b_2), .Q_2(_23_q_2));
  // Probe on _23_a_2
  // Probe on _23_q_2
  Cycle_32_bit _24 (.A(_23_a_2), .B(_23_b_2), .Q(_23_q_2), .A_2(_24_a_2), .B_2(_24_b_2), .Q_2(_24_q_2));
  // Probe on _24_a_2
  // Probe on _24_q_2
  Cycle_32_bit _25 (.A(_24_a_2), .B(_24_b_2), .Q(_24_q_2), .A_2(_25_a_2), .B_2(_25_b_2), .Q_2(_25_q_2));
  // Probe on _25_a_2
  // Probe on _25_q_2
  Cycle_32_bit _26 (.A(_25_a_2), .B(_25_b_2), .Q(_25_q_2), .A_2(_26_a_2), .B_2(_26_b_2), .Q_2(_26_q_2));
  // Probe on _26_a_2
  // Probe on _26_q_2
  Cycle_32_bit _27 (.A(_26_a_2), .B(_26_b_2), .Q(_26_q_2), .A_2(_27_a_2), .B_2(_27_b_2), .Q_2(_27_q_2));
  // Probe on _27_a_2
  // Probe on _27_q_2
  Cycle_32_bit _28 (.A(_27_a_2), .B(_27_b_2), .Q(_27_q_2), .A_2(_28_a_2), .B_2(_28_b_2), .Q_2(_28_q_2));
  // Probe on _28_a_2
  // Probe on _28_q_2
  Cycle_32_bit _29 (.A(_28_a_2), .B(_28_b_2), .Q(_28_q_2), .A_2(_29_a_2), .B_2(_29_b_2), .Q_2(_29_q_2));
  // Probe on _29_a_2
  // Probe on _29_q_2
  Cycle_32_bit _30 (.A(_29_a_2), .B(_29_b_2), .Q(_29_q_2), .A_2(_30_a_2), .B_2(_30_b_2), .Q_2(_30_q_2));
  // Probe on _30_a_2
  // Probe on _30_q_2
  Cycle_32_bit _31 (.A(_30_a_2), .B(_30_b_2), .Q(_30_q_2), .A_2(_31_a_2), .B_2(_31_b_2), .Q_2(_31_q_2));
  // Probe on _31_a_2
  // Probe on _31_q_2
  Cycle_32_bit _32 (.A(_31_a_2), .B(_31_b_2), .Q(_31_q_2), .A_2(A__High), .B_2(_32_b_2), .Q_2(Q__Low));
  // Probe on A__High
  // Probe on Q__Low
endmodule

module _8_bit_2 (
  input  [7:0] A,
  input  [7:0] B,
  output Overflow,
  output [7:0] Result
);

  wire [6:0] _6_8_out;
  wire [7:0] _7_2_out, _7_3_out, _7_4_out, _7_5_out, _7_6_out, _7_7_out, _7_out, n8_bit_6_result,
       n8_bit_7_result;

  and _0 (_7_out[7], A[7], B[0]);
  and _1 (_7_out[6], A[7], B[1]);
  and _3 (_7_out[4], A[7], B[3]);
  and _2 (_7_out[5], A[7], B[2]);
  _8_bit u_8_bit_1 (.A(_7_out));  // open: Cin, B, Subtraction, Cout, Result
  and _5 (_7_out[2], A[7], B[5]);
  and _4 (_7_out[3], A[7], B[4]);
  and _6 (_7_out[1], A[7], B[6]);
  and _7 (_7_out[0], A[7], B[7]);
  and _0_2 (_7_2_out[7], A[6], B[0]);
  and _1_2 (_7_2_out[6], A[6], B[1]);
  and _2_2 (_7_2_out[5], A[6], B[2]);
  and _3_2 (_7_2_out[4], A[6], B[3]);
  and _4_2 (_7_2_out[3], A[6], B[4]);
  and _5_2 (_7_2_out[2], A[6], B[5]);
  _8_bit u_8_bit_2 (.A(_7_2_out));  // open: Cin, B, Subtraction, Cout, Result
  and _6_2 (_7_2_out[1], A[6], B[6]);
  and _7_2 (_7_2_out[0], A[6], B[7]);
  and _1_3 (_7_3_out[6], A[5], B[1]);
  and _0_3 (_7_3_out[7], A[5], B[0]);
  and _4_3 (_7_3_out[3], A[5], B[4]);
  and _3_3 (_7_3_out[4], A[5], B[3]);
  and _2_3 (_7_3_out[5], A[5], B[2]);
  _8_bit u_8_bit_3 (.A(_7_3_out));  // open: Cin, B, Subtraction, Cout, Result
  and _5_3 (_7_3_out[2], A[5], B[5]);
  and _7_3 (_7_3_out[0], A[5], B[7]);
  and _6_3 (_7_3_out[1], A[5], B[6]);
  and _0_4 (_7_4_out[7], A[4], B[0]);
  and _1_4 (_7_4_out[6], A[4], B[1]);
  and _2_4 (_7_4_out[5], A[4], B[2]);
  and _3_4 (_7_4_out[4], A[4], B[3]);
  and _4_4 (_7_4_out[3], A[4], B[4]);
  and _5_4 (_7_4_out[2], A[4], B[5]);
  _8_bit u_8_bit_4 (.A(_7_4_out));  // open: Cin, B, Subtraction, Cout, Result
  and _7_4 (_7_4_out[0], A[4], B[7]);
  and _6_4 (_7_4_out[1], A[4], B[6]);
  and _0_5 (_7_5_out[7], A[3], B[0]);
  and _1_5 (_7_5_out[6], A[3], B[1]);
  and _2_5 (_7_5_out[5], A[3], B[2]);
  and _3_5 (_7_5_out[4], A[3], B[3]);
  and _4_5 (_7_5_out[3], A[3], B[4]);
  _8_bit u_8_bit_5 (.Cin(1'b0), .B(n8_bit_6_result), .Subtraction(1'b0), .A(_7_5_out));  // open: Cout, Result
  and _7_5 (_7_5_out[0], A[3], B[7]);
  and _6_5 (_7_5_out[1], A[3], B[6]);
  and _5_5 (_7_5_out[2], A[3], B[5]);
  and _0_6 (_7_6_out[7], A[2], B[0]);
  and _3_6 (_7_6_out[4], A[2], B[3]);
  and _2_6 (_7_6_out[5], A[2], B[2]);
  and _1_6 (_7_6_out[6], A[2], B[1]);
  and _4_6 (_7_6_out[3], A[2], B[4]);
  and _5_6 (_7_6_out[2], A[2], B[5]);
  and _6_6 (_7_6_out[1], A[2], B[6]);
  _8_bit u_8_bit_6 (
    .Cin(1'b0), .B(n8_bit_7_result), .Subtraction(1'b0), .A(_7_6_out), .Cout(Result[2]),
    .Result(n8_bit_6_result));
  and _7_6 (_7_6_out[0], A[2], B[7]);
  and _0_7 (_7_7_out[7], A[1], B[0]);
  and _2_7 (_7_7_out[5], A[1], B[2]);
  and _1_7 (_7_7_out[6], A[1], B[1]);
  and _4_7 (_7_7_out[3], A[1], B[4]);
  and _3_7 (_7_7_out[4], A[1], B[3]);
  and _5_7 (_7_7_out[2], A[1], B[5]);
  _8_bit u_8_bit_7 (
    .Cin(1'b0), .B({1'b0, _6_8_out}), .Subtraction(1'b0), .A(_7_7_out), .Cout(Result[1]),
    .Result(n8_bit_7_result));
  and _7_7 (_7_7_out[0], A[1], B[7]);
  and _6_7 (_7_7_out[1], A[1], B[6]);
  and _2_8 (_6_8_out[4], A[0], B[5]);
  and _0_8 (_6_8_out[6], A[0], B[7]);
  and _1_8 (_6_8_out[5], A[0], B[6]);
  and _3_8 (_6_8_out[3], A[0], B[4]);
  and _5_8 (_6_8_out[1], A[0], B[2]);
  and _4_8 (_6_8_out[2], A[0], B[3]);
  and _7_8 (Result[0], A[0], B[0]);
  and _6_8 (_6_8_out[0], A[0], B[1]);
  // OR_Gate or_1 has open pins: out=Overflow

  // Notes on the sheet:
  //   B1*A
  //   A0
  //   B0*A
  //   A + B = AUGEND + ADDEND
  //   A0*B0
endmodule

module _4_bit_2 (
  input  [3:0] B,
  input  [3:0] Q
);

  wire [3:0] First_Cycle_a_2, First_Cycle_b_2, First_Cycle_q_2, Fourth_Cycle_a_2, Fourth_Cycle_q_2,
       Second_Cycle_a_2, Second_Cycle_b_2, Second_Cycle_q_2, Third_Cycle_a_2, Third_Cycle_b_2,
       Third_Cycle_q_2;

  Cycles_4_bit First_Cycle (
    .A(4'b0000), .B(B), .Q(Q), .A_2(First_Cycle_a_2), .B_2(First_Cycle_b_2), .Q_2(First_Cycle_q_2));
  // Probe on First_Cycle_a_2
  // Probe on First_Cycle_q_2
  Cycles_4_bit Second_Cycle (
    .A(First_Cycle_a_2), .B(First_Cycle_b_2), .Q(First_Cycle_q_2), .A_2(Second_Cycle_a_2),
    .B_2(Second_Cycle_b_2), .Q_2(Second_Cycle_q_2));
  // Probe on Second_Cycle_a_2
  // Probe on Second_Cycle_q_2
  Cycles_4_bit Third_Cycle (
    .A(Second_Cycle_a_2), .B(Second_Cycle_b_2), .Q(Second_Cycle_q_2), .A_2(Third_Cycle_a_2),
    .B_2(Third_Cycle_b_2), .Q_2(Third_Cycle_q_2));
  // Probe on Third_Cycle_a_2
  // Probe on Third_Cycle_q_2
  Cycles_4_bit Fourth_Cycle (
    .A(Third_Cycle_a_2), .B(Third_Cycle_b_2), .Q(Third_Cycle_q_2), .A_2(Fourth_Cycle_a_2),
    .Q_2(Fourth_Cycle_q_2));  // open: B_2
  // Probe on Fourth_Cycle_a_2
  // Probe on Fourth_Cycle_q_2
endmodule

// 32 bit >>1
module _32_bit_Right_Shifterfor_1_bit (
  input  [31:0] Input,
  output [31:0] out_2
);


  assign out_2 = {Input[30:0], 1'b0};
endmodule

// >> 1
module _65_bit_shifter (
  input  [31:0] Input32_0,
  input  [31:0] Input32_1,
  input  _65th_bit_In,
  output [31:0] Output32_0,
  output [31:0] Output32_1,
  output _65th_bit_Out
);


  assign _65th_bit_Out = 1'b0;
  assign Output32_0 = {Input32_0[0], Input32_1[31:1]};
  assign Output32_1 = {_65th_bit_In, Input32_0[31:1]};
endmodule

module _33_bit_right_shifter (
  input  [31:0] Input32,
  input  _33rd_bit_In,
  output [31:0] Output32_0,
  output _33rd_bit_Out
);


  assign _33rd_bit_Out = 1'b0;
  assign Output32_0 = {_33rd_bit_In, Input32[31:1]};
endmodule

module Cycles_4_bit (
  input  [3:0] A,
  input  [3:0] B,
  input  [3:0] Q,
  output [3:0] A_2,
  output [3:0] B_2,
  output [3:0] Q_2
);

  wire adder_1_cout;
  wire [3:0] adder_1_out, multiplexer_1_out;
  wire [8:8] and_1_out, shifter_1_out;

  Adder #(.width(4)) adder_1 (.a(A), .b(B), .out(adder_1_out), .cin(1'b0), .cout(adder_1_cout));
  Multiplexer #(.width(4), .enable("false")) multiplexer_1 (
    .in0(A), .in1(adder_1_out), .out(multiplexer_1_out), .sel(Q[0]));
  and and_1 (and_1_out[8], Q[0], adder_1_cout);
  // Probe on Q
  // Probe on multiplexer_1_out
  // Probe on and_1_out[8]
  Shifter #(.width(9), .shift("lr")) shifter_1 (
    .in({and_1_out[8], multiplexer_1_out, Q}), .\dist (4'b0001), .out({shifter_1_out[8], A_2, Q_2}));

  assign B_2 = B;

  // Notes on the sheet:
  //   Before Shift
endmodule

// *
module Cycle_32_bit (
  input  [31:0] A,
  input  [31:0] B,
  input  [31:0] Q,
  output [31:0] A_2,
  output [31:0] B_2,
  output [31:0] Q_2
);

  wire adder_1_cout, and_1_out;
  wire [31:0] adder_1_out, multiplexer_1_out;

  Adder #(.width(32)) adder_1 (.a(A), .b(B), .out(adder_1_out), .cin(1'b0), .cout(adder_1_cout));
  Multiplexer #(.width(32), .enable("false")) multiplexer_1 (
    .in0(A), .in1(adder_1_out), .out(multiplexer_1_out), .sel(Q[0]));
  and and_1 (and_1_out, adder_1_cout, Q[0]);
  _65_bit_shifter u_65_bit_shifter_1 (
    .Input32_0(multiplexer_1_out), .Input32_1(Q), ._65th_bit_In(and_1_out), .Output32_0(Q_2), .Output32_1(A_2));  // open: _65th_bit_Out

  assign B_2 = B;
endmodule

module _32_bit_Comparador (
  input  [31:0] A,
  input  [31:0] B,
  output [31:0] A___B,
  output [31:0] A___B_2,
  output [31:0] A___B_3
);

  wire A___nB_2_out, A___nB_3_out, A___nB_4_out, A___nB_5_out, A___nB_6_out, A___nB_7_out, A___nB_8_out,
       A___nB_9_out, A___nB_10_out, A___nB_11_out, A___nB_12_out, A___nB_13_out, A___nB_14_out,
       A___nB_15_out, A___nB_16_out, A___nB_17_out, A___nB_18_out, A___nB_19_out, A___nB_20_out,
       A___nB_21_out, A___nB_22_out, A___nB_23_out, A___nB_24_out, A___nB_25_out, A___nB_26_out,
       A___nB_27_out, A___nB_28_out, A___nB_29_out, A___nB_30_out, A___nB_31_out, A___nB_32_out, A___nB_out,
       nA___B_2_out, nA___B_3_out, nA___B_4_out, nA___B_5_out, nA___B_6_out, nA___B_7_out, nA___B_8_out,
       nA___B_9_out, nA___B_10_out, nA___B_11_out, nA___B_12_out, nA___B_13_out, nA___B_14_out,
       nA___B_15_out, nA___B_16_out, nA___B_17_out, nA___B_18_out, nA___B_19_out, nA___B_20_out,
       nA___B_21_out, nA___B_22_out, nA___B_23_out, nA___B_24_out, nA___B_25_out, nA___B_26_out,
       nA___B_27_out, nA___B_28_out, nA___B_29_out, nA___B_30_out, nA___B_31_out, nA___B_32_out, nA___B_out,
       xnor_1_out, xnor_2_out, xnor_3_out, xnor_4_out, xnor_5_out, xnor_6_out, xnor_7_out, xnor_8_out,
       xnor_9_out, xnor_10_out, xnor_11_out, xnor_12_out, xnor_13_out, xnor_14_out, xnor_15_out, xnor_16_out,
       xnor_17_out, xnor_18_out, xnor_19_out, xnor_20_out, xnor_21_out, xnor_22_out, xnor_23_out,
       xnor_24_out, xnor_25_out, xnor_26_out, xnor_27_out, xnor_28_out, xnor_29_out, xnor_30_out,
       xnor_31_out, xnor_32_out;
  wire [31:0] not_1_out, not_2_out;

  assign not_1_out = ~A;  // NOT_Gate not_1, 32 bits wide
  and A___nB (A___nB_out, A[0], not_2_out[0]);
  and nA___B (nA___B_out, not_1_out[0], B[0]);
  and A___nB_2 (A___nB_2_out, A[2], not_2_out[2]);
  and A___nB_3 (A___nB_3_out, A[1], not_2_out[1]);
  and nA___B_2 (nA___B_2_out, not_1_out[2], B[2]);
  and nA___B_3 (nA___B_3_out, not_1_out[1], B[1]);
  and A___nB_4 (A___nB_4_out, A[4], not_2_out[4]);
  and A___nB_5 (A___nB_5_out, A[3], not_2_out[3]);
  and nA___B_4 (nA___B_4_out, not_1_out[4], B[4]);
  and nA___B_5 (nA___B_5_out, not_1_out[3], B[3]);
  and A___nB_6 (A___nB_6_out, A[5], not_2_out[5]);
  and nA___B_6 (nA___B_6_out, not_1_out[5], B[5]);
  and A___nB_7 (A___nB_7_out, A[6], not_2_out[6]);
  and A___nB_8 (A___nB_8_out, A[7], not_2_out[7]);
  and nA___B_7 (nA___B_7_out, not_1_out[7], B[7]);
  and nA___B_8 (nA___B_8_out, not_1_out[6], B[6]);
  and A___nB_9 (A___nB_9_out, A[8], not_2_out[8]);
  and nA___B_9 (nA___B_9_out, not_1_out[8], B[8]);
  and A___nB_10 (A___nB_10_out, A[10], not_2_out[10]);
  and A___nB_11 (A___nB_11_out, A[9], not_2_out[9]);
  and nA___B_10 (nA___B_10_out, not_1_out[10], B[10]);
  and nA___B_11 (nA___B_11_out, not_1_out[9], B[9]);
  and A___nB_12 (A___nB_12_out, A[11], not_2_out[11]);
  and A___nB_13 (A___nB_13_out, A[12], not_2_out[12]);
  and nA___B_12 (nA___B_12_out, not_1_out[11], B[11]);
  and nA___B_13 (nA___B_13_out, not_1_out[12], B[12]);
  and A___nB_14 (A___nB_14_out, A[13], not_2_out[13]);
  and nA___B_14 (nA___B_14_out, not_1_out[13], B[13]);
  and A___nB_15 (A___nB_15_out, A[14], not_2_out[14]);
  and A___nB_16 (A___nB_16_out, A[15], not_2_out[15]);
  and nA___B_15 (nA___B_15_out, not_1_out[14], B[14]);
  and nA___B_16 (nA___B_16_out, not_1_out[15], B[15]);
  and A___nB_17 (A___nB_17_out, A[16], not_2_out[16]);
  or u_A___B (A___B[31], A___nB_out, A___nB_3_out, A___nB_2_out, A___nB_5_out, A___nB_4_out, A___nB_6_out, A___nB_7_out, A___nB_8_out, A___nB_9_out, A___nB_11_out, A___nB_10_out, A___nB_12_out, A___nB_13_out, A___nB_14_out, A___nB_15_out, A___nB_16_out, A___nB_17_out, A___nB_18_out, A___nB_19_out, A___nB_21_out, A___nB_20_out, A___nB_22_out, A___nB_24_out, A___nB_23_out, A___nB_25_out, A___nB_26_out, A___nB_27_out, A___nB_28_out, A___nB_29_out, A___nB_30_out, A___nB_31_out, A___nB_32_out);
  or u_A___B_2 (A___B_3[31], nA___B_out, nA___B_3_out, nA___B_2_out, nA___B_5_out, nA___B_4_out, nA___B_6_out, nA___B_8_out, nA___B_7_out, nA___B_9_out, nA___B_11_out, nA___B_10_out, nA___B_12_out, nA___B_13_out, nA___B_14_out, nA___B_15_out, nA___B_16_out, nA___B_17_out, nA___B_18_out, nA___B_19_out, nA___B_20_out, nA___B_21_out, nA___B_22_out, nA___B_24_out, nA___B_23_out, nA___B_25_out, nA___B_26_out, nA___B_27_out, nA___B_28_out, nA___B_29_out, nA___B_30_out, nA___B_31_out, nA___B_32_out);
  and nA___B_17 (nA___B_17_out, not_1_out[16], B[16]);
  and A___nB_18 (A___nB_18_out, A[17], not_2_out[17]);
  and A___nB_19 (A___nB_19_out, A[18], not_2_out[18]);
  and nA___B_18 (nA___B_18_out, not_1_out[17], B[17]);
  and nA___B_19 (nA___B_19_out, not_1_out[18], B[18]);
  and A___nB_20 (A___nB_20_out, A[20], not_2_out[20]);
  and A___nB_21 (A___nB_21_out, A[19], not_2_out[19]);
  and nA___B_20 (nA___B_20_out, not_1_out[19], B[19]);
  and nA___B_21 (nA___B_21_out, not_1_out[20], B[20]);
  and A___nB_22 (A___nB_22_out, A[21], not_2_out[21]);
  and nA___B_22 (nA___B_22_out, not_1_out[21], B[21]);
  and A___nB_23 (A___nB_23_out, A[23], not_2_out[23]);
  and A___nB_24 (A___nB_24_out, A[22], not_2_out[22]);
  and nA___B_23 (nA___B_23_out, not_1_out[23], B[23]);
  and nA___B_24 (nA___B_24_out, not_1_out[22], B[22]);
  and A___nB_25 (A___nB_25_out, A[24], not_2_out[24]);
  and nA___B_25 (nA___B_25_out, not_1_out[24], B[24]);
  and A___nB_26 (A___nB_26_out, A[25], not_2_out[25]);
  and A___nB_27 (A___nB_27_out, A[26], not_2_out[26]);
  and nA___B_26 (nA___B_26_out, not_1_out[25], B[25]);
  and nA___B_27 (nA___B_27_out, not_1_out[26], B[26]);
  and A___nB_28 (A___nB_28_out, A[27], not_2_out[27]);
  and A___nB_29 (A___nB_29_out, A[28], not_2_out[28]);
  and nA___B_28 (nA___B_28_out, not_1_out[27], B[27]);
  and nA___B_29 (nA___B_29_out, not_1_out[28], B[28]);
  and A___nB_30 (A___nB_30_out, A[29], not_2_out[29]);
  and nA___B_30 (nA___B_30_out, not_1_out[29], B[29]);
  and A___nB_31 (A___nB_31_out, A[30], not_2_out[30]);
  and A___nB_32 (A___nB_32_out, A[31], not_2_out[31]);
  and nA___B_31 (nA___B_31_out, not_1_out[30], B[30]);
  and nA___B_32 (nA___B_32_out, not_1_out[31], B[31]);
  assign not_2_out = ~B;  // NOT_Gate not_2, 32 bits wide
  xnor xnor_1 (xnor_1_out, A[31], B[31]);
  xnor xnor_2 (xnor_2_out, A[30], B[30]);
  xnor xnor_3 (xnor_3_out, A[29], B[29]);
  xnor xnor_4 (xnor_4_out, A[28], B[28]);
  xnor xnor_5 (xnor_5_out, A[27], B[27]);
  xnor xnor_6 (xnor_6_out, A[26], B[26]);
  xnor xnor_7 (xnor_7_out, A[25], B[25]);
  xnor xnor_8 (xnor_8_out, A[24], B[24]);
  xnor xnor_9 (xnor_9_out, A[23], B[23]);
  xnor xnor_10 (xnor_10_out, A[22], B[22]);
  xnor xnor_11 (xnor_11_out, A[21], B[21]);
  xnor xnor_12 (xnor_12_out, A[20], B[20]);
  xnor xnor_13 (xnor_13_out, A[19], B[19]);
  xnor xnor_14 (xnor_14_out, A[18], B[18]);
  xnor xnor_15 (xnor_15_out, A[17], B[17]);
  xnor xnor_16 (xnor_16_out, A[16], B[16]);
  xnor xnor_17 (xnor_17_out, A[15], B[15]);
  xnor xnor_18 (xnor_18_out, A[14], B[14]);
  xnor xnor_19 (xnor_19_out, A[13], B[13]);
  xnor xnor_20 (xnor_20_out, A[12], B[12]);
  xnor xnor_21 (xnor_21_out, A[11], B[11]);
  xnor xnor_22 (xnor_22_out, A[10], B[10]);
  xnor xnor_23 (xnor_23_out, A[9], B[9]);
  xnor xnor_24 (xnor_24_out, A[8], B[8]);
  xnor xnor_25 (xnor_25_out, A[7], B[7]);
  xnor xnor_26 (xnor_26_out, A[6], B[6]);
  xnor xnor_27 (xnor_27_out, A[5], B[5]);
  xnor xnor_28 (xnor_28_out, A[4], B[4]);
  xnor xnor_29 (xnor_29_out, A[3], B[3]);
  xnor xnor_30 (xnor_30_out, A[2], B[2]);
  xnor xnor_31 (xnor_31_out, A[1], B[1]);
  xnor xnor_32 (xnor_32_out, A[0], B[0]);
  and and_1 (A___B_2[31], xnor_32_out, xnor_31_out, xnor_30_out, xnor_29_out, xnor_28_out, xnor_27_out, xnor_26_out, xnor_25_out, xnor_24_out, xnor_23_out, xnor_22_out, xnor_21_out, xnor_20_out, xnor_19_out, xnor_18_out, xnor_17_out, xnor_16_out, xnor_15_out, xnor_14_out, xnor_13_out, xnor_12_out, xnor_11_out, xnor_10_out, xnor_9_out, xnor_8_out, xnor_7_out, xnor_6_out, xnor_5_out, xnor_4_out, xnor_3_out, xnor_2_out, xnor_1_out);
  // Probe on A___B[31]
  // Probe on A___B_2[31]
  // Probe on A___B_3[31]

  assign A___B[30:0] = {31{A___B[31]}};
  assign A___B_2[30:0] = {31{A___B_2[31]}};
  assign A___B_3[30:0] = {31{A___B_3[31]}};

  // Notes on the sheet:
  //   A
  //   ~A
  //   ~B
endmodule

module _4_bit_Comparator (
  input  A0,
  input  A1,
  input  A2,
  input  A3,
  input  B0,
  input  B1,
  input  B2,
  input  B3,
  output A___B,
  output A___B_2,
  output A___B_3
);

  wire and_1_out, and_2_out, and_3_out, and_4_out, and_6_out, and_7_out, and_8_out, and_9_out, not_1_out,
       not_2_out, not_3_out, not_4_out, not_5_out, not_6_out, not_7_out, not_8_out, xnor_1_out, xnor_2_out,
       xnor_3_out, xnor_4_out;

  not not_1 (not_1_out, A0);
  not not_2 (not_2_out, A1);
  not not_3 (not_3_out, A2);
  not not_4 (not_4_out, A3);
  xnor xnor_1 (xnor_1_out, A3, B3);
  xnor xnor_2 (xnor_2_out, A2, B2);
  xnor xnor_3 (xnor_3_out, A1, B1);
  xnor xnor_4 (xnor_4_out, A0, B0);
  not not_5 (not_5_out, B0);
  not not_6 (not_6_out, B1);
  not not_7 (not_7_out, B2);
  not not_8 (not_8_out, B3);
  and and_1 (and_1_out, A0, not_5_out);
  and and_2 (and_2_out, A1, not_6_out);
  and and_3 (and_3_out, A2, not_7_out);
  and and_4 (and_4_out, A3, not_8_out);
  and and_5 (A___B_2, xnor_1_out, xnor_2_out, xnor_3_out, xnor_4_out);
  and and_6 (and_6_out, not_1_out, B0);
  and and_7 (and_7_out, not_2_out, B1);
  and and_8 (and_8_out, not_3_out, B2);
  and and_9 (and_9_out, not_4_out, B3);
  or or_1 (A___B, and_1_out, and_2_out, and_3_out, and_4_out);
  or or_2 (A___B_3, and_6_out, and_7_out, and_8_out, and_9_out);
endmodule

module _4_bit_2_2 (
  input  [3:0] M,
  input  [3:0] Q,
  input  [3:0] A,
  output [3:0] M_2,
  output [3:0] Q_2,
  output [3:0] A_2
);

  wire [3:0] cycle_4_bit_1_a_2, cycle_4_bit_1_m_2, cycle_4_bit_1_q_2, cycle_4_bit_2_a_2, cycle_4_bit_2_m_2,
       cycle_4_bit_2_q_2, cycle_4_bit_3_a_2, cycle_4_bit_3_m_2, cycle_4_bit_3_q_2;

  // Probe on M_2
  // Probe on Q_2
  // Probe on A_2
  // Probe on cycle_4_bit_1_m_2
  // Probe on cycle_4_bit_1_q_2
  // Probe on cycle_4_bit_1_a_2
  Cycle_4_bit cycle_4_bit_1 (
    .M(M), .Q(Q), .A(A), .M_2(cycle_4_bit_1_m_2), .Q_2(cycle_4_bit_1_q_2), .A_2(cycle_4_bit_1_a_2));
  // Probe on cycle_4_bit_2_m_2
  // Probe on cycle_4_bit_2_q_2
  // Probe on cycle_4_bit_2_a_2
  Cycle_4_bit cycle_4_bit_2 (
    .M(cycle_4_bit_1_m_2), .Q(cycle_4_bit_1_q_2), .A(cycle_4_bit_1_a_2), .M_2(cycle_4_bit_2_m_2),
    .Q_2(cycle_4_bit_2_q_2), .A_2(cycle_4_bit_2_a_2));
  Cycle_4_bit cycle_4_bit_3 (
    .M(cycle_4_bit_2_m_2), .Q(cycle_4_bit_2_q_2), .A(cycle_4_bit_2_a_2), .M_2(cycle_4_bit_3_m_2),
    .Q_2(cycle_4_bit_3_q_2), .A_2(cycle_4_bit_3_a_2));
  // Probe on cycle_4_bit_3_m_2
  // Probe on cycle_4_bit_3_q_2
  // Probe on cycle_4_bit_3_a_2
  Cycle_4_bit cycle_4_bit_4 (
    .M(cycle_4_bit_3_m_2), .Q(cycle_4_bit_3_q_2), .A(cycle_4_bit_3_a_2), .M_2(M_2), .Q_2(Q_2), .A_2(A_2));
endmodule

// ÷
module Cycle_4_bit (
  input  [3:0] M,
  input  [3:0] Q,
  input  [3:0] A,
  output [3:0] M_2,
  output [3:0] Q_2,
  output [3:0] A_2
);

  wire and_1_out, and_2_out, and_3_out, nor_1_out, nor_2_out, nor_3_out, xnor_1_out, xnor_2_out;
  wire [3:0] n4_bit_1_result;
  wire [7:0] shifter_1_out;

  // Probe on {A, Q}
  // Probe on {shifter_1_out[7:4], Q_2[3:1], shifter_1_out[0]}
  Shifter shifter_1 (.in({A, Q}), .\dist (3'b001), .out({shifter_1_out[7:4], Q_2[3:1], shifter_1_out[0]}));
  xnor xnor_1 (xnor_1_out, M[3], A[3]);
  // Probe on shifter_1_out[7:4]
  // Probe on {Q_2[3:1], shifter_1_out[0]}
  // Probe on M
  // Probe on {Q_2[3:1], shifter_1_out[0]}
  // Probe on n4_bit_1_result
  _4_bit u_4_bit_1 (
    .Cin(1'b0), .B(M), .Subtraction(xnor_1_out), .A(shifter_1_out[7:4]), .Result(n4_bit_1_result));  // open: Cout
  // Probe on n4_bit_1_result[3]
  // Probe on A[3]
  xnor xnor_2 (xnor_2_out, n4_bit_1_result[3], A[3]);
  nor nor_1 (nor_1_out, n4_bit_1_result[0], n4_bit_1_result[1], n4_bit_1_result[2], n4_bit_1_result[3]);
  nor nor_2 (nor_2_out, shifter_1_out[0], Q_2[1], Q_2[2], Q_2[3]);
  // Probe on {Q_2[3:1], shifter_1_out[0]}
  and and_1 (and_1_out, nor_1_out, nor_2_out);
  nor nor_3 (nor_3_out, nor_1_out, nor_2_out);
  Multiplexer #(.enable("false")) multiplexer_1 (.in0(shifter_1_out[0]), .in1(1'b1), .out(Q_2[0]), .sel(and_2_out));
  and and_2 (and_2_out, xnor_2_out, and_1_out);
  and and_3 (and_3_out, xnor_2_out, nor_3_out);
  Multiplexer #(.width(4), .enable("false")) multiplexer_2 (.in0(n4_bit_1_result), .in1(A), .out(A_2), .sel(and_3_out));
  // Probe on A
  // Probe on n4_bit_1_result
  // Probe on Q_2

  assign M_2 = M;

  // Notes on the sheet:
  //   Shift Left AQ By One Bit
  //   M[4]
  //   A[4]
  //   Subtract if M[4] == A[4] else add
  //   S = A[4]
  //   A = A +/- M
  //   A[4]
  //   S
  //   S == A[4]
  //   A == 0
  //   Q == 0
  //   If A != 0 or Q != 0
  //    A == 0 and Q == 0
  //   A
  //   Restore A
  //   If A == 0 and Q == 0 the Q[0] = 1
  //   If S == A[4]
  //   If S != A[4]
  //   If A != 0 and Q != 0 then Restore A
endmodule
