// Logisim project ALU4.circ as structural Verilog: 5 circuits, main circuit main
module main (
  input  [3:0] A,
  input  [3:0] B,
  input  Control0,
  input  Control1,
  output [3:0] Result,
  output Zero,
  output Negative,
  output Carry,
  output Overflow
);

  wire or_1_out;
  wire [3:0] multiplexer_1_out, n4_bit_adder_subtracter_1_result, n4_bit_and_1_result, n4_bit_or_1_result;

  _4_bit_AND u_4_bit_and_1 (.A(A), .Result(n4_bit_and_1_result), .B(B));
  _4_bit_OR u_4_bit_or_1 (.A(A), .Result(n4_bit_or_1_result), .B(B));
  _4_bit_Adder_Subtracter u_4_bit_adder_subtracter_1 (
    .Add_Sub_Control(Control0), .Result(n4_bit_adder_subtracter_1_result), .A(A), .B(B), .Carry_out(Carry),
    .Overflow(Overflow));
  Multiplexer #(.width(4), .enable("false")) multiplexer_1 (
    .in0(n4_bit_and_1_result), .in1(n4_bit_or_1_result), .out(multiplexer_1_out), .sel(Control0));
  Multiplexer #(.width(4), .enable("false")) multiplexer_2 (
    .in0(multiplexer_1_out), .in1(n4_bit_adder_subtracter_1_result), .out({Negative, Result[2:0]}),
    .sel(Control1));
  or or_1 (or_1_out, Result[0], Result[1], Result[2], Negative);
  not not_1 (Zero, or_1_out);

  assign Result[3] = Negative;

  // Notes on the sheet:
  //   AND
  //   OR
  //   +/-
  //   Select AND (0) or OR (1)
  //   Select ADD (0) or SUB (1)
  //   Full 4-bit ALU
  //   Select Logic (0) or Math (1)
endmodule

// +
module _1_bit_Adder (
  input  Carry_In,
  input  A,
  input  B,
  output Result,
  output Carry_Out
);

  wire and_1_out, and_2_out, xor_1_out;

  and and_1 (and_1_out, A, B);
  xor xor_1 (xor_1_out, A, B);
  or or_1 (Carry_Out, and_1_out, and_2_out);
  and and_2 (and_2_out, Carry_In, xor_1_out);
  xor xor_2 (Result, Carry_In, xor_1_out);

  // Notes on the sheet:
  //   Full Adder
endmodule

module _4_bit_Adder_Subtracter (
  input  Add_Sub_Control,
  input  [3:0] A,
  input  [3:0] B,
  output [3:0] Result,
  output Carry_out,
  output Overflow
);

  wire and_1_out, and_2_out, n1_bit_adder_1_carry_out, n1_bit_adder_2_carry_out, n1_bit_adder_3_carry_out,
       not_1_out, not_2_out, not_3_out, xor_1_out, xor_2_out, xor_3_out, xor_4_out;

  xor xor_1 (xor_1_out, Add_Sub_Control, B[0]);
  xor xor_2 (xor_2_out, Add_Sub_Control, B[1]);
  xor xor_3 (xor_3_out, Add_Sub_Control, B[2]);
  xor xor_4 (xor_4_out, Add_Sub_Control, B[3]);
  not not_1 (not_1_out, xor_4_out);
  not not_2 (not_2_out, A[3]);
  _1_bit_Adder u_1_bit_adder_1 (
    .A(A[0]), .B(xor_1_out), .Result(Result[0]), .Carry_Out(n1_bit_adder_1_carry_out),
    .Carry_In(Add_Sub_Control));
  _1_bit_Adder u_1_bit_adder_2 (
    .A(A[1]), .B(xor_2_out), .Result(Result[1]), .Carry_Out(n1_bit_adder_2_carry_out),
    .Carry_In(n1_bit_adder_1_carry_out));
  _1_bit_Adder u_1_bit_adder_3 (
    .A(A[2]), .B(xor_3_out), .Result(Result[2]), .Carry_Out(n1_bit_adder_3_carry_out),
    .Carry_In(n1_bit_adder_2_carry_out));
  _1_bit_Adder u_1_bit_adder_4 (
    .A(A[3]), .B(xor_4_out), .Result(Result[3]), .Carry_Out(Carry_out), .Carry_In(n1_bit_adder_3_carry_out));
  not not_3 (not_3_out, Result[3]);
  and and_1 (and_1_out, Result[3], not_2_out, not_1_out);
  and and_2 (and_2_out, not_3_out, A[3], xor_4_out);
  or or_1 (Overflow, and_1_out, and_2_out);

  // Notes on the sheet:
  //   4-bit Adder/Subtractor
endmodule

module _4_bit_AND (
  input  [3:0] A,
  input  [3:0] B,
  output [3:0] Result
);

  and AND (Result[0], A[0], B[0]);
  and AND_2 (Result[1], A[1], B[1]);
  and AND_3 (Result[2], A[2], B[2]);
  and AND_4 (Result[3], A[3], B[3]);

  // Notes on the sheet:
  //   4-bit AND
endmodule

module _4_bit_OR (
  input  [3:0] A,
  input  [3:0] B,
  output [3:0] Result
);

  or OR (Result[0], A[0], B[0]);
  or OR_2 (Result[1], A[1], B[1]);
  or OR_3 (Result[2], A[2], B[2]);
  or OR_4 (Result[3], A[3], B[3]);

  // Notes on the sheet:
  //   4-bit OR
endmodule
