// Logisim project add_sub.circ as structural Verilog: 9 circuits, main circuit 32 bit sub
module _32_bit_addu (
  input  [31:0] B,
  input  [31:0] A,
  output out_3,
  output [31:0] A___B
);

  wire n1_bit_2_cout, n1_bit_3_cout, n1_bit_4_cout, n1_bit_5_cout, n1_bit_6_cout, n1_bit_7_cout,
       n1_bit_8_cout, n1_bit_9_cout, n1_bit_10_cout, n1_bit_11_cout, n1_bit_12_cout, n1_bit_13_cout,
       n1_bit_14_cout, n1_bit_15_cout, n1_bit_16_cout, n1_bit_17_cout, n1_bit_18_cout, n1_bit_19_cout,
       n1_bit_20_cout, n1_bit_21_cout, n1_bit_22_cout, n1_bit_23_cout, n1_bit_24_cout, n1_bit_25_cout,
       n1_bit_26_cout, n1_bit_27_cout, n1_bit_28_cout, n1_bit_29_cout, n1_bit_30_cout, n1_bit_31_cout,
       n1_bit_32_cout;

  _1_bit u_1_bit_1 (.A(A[31]), .B(B[31]), .Cin(n1_bit_2_cout), .S(A___B[31]), .Cout(out_3));
  _1_bit u_1_bit_2 (.A(A[30]), .B(B[30]), .Cin(n1_bit_3_cout), .S(A___B[30]), .Cout(n1_bit_2_cout));
  _1_bit u_1_bit_3 (.A(A[29]), .B(B[29]), .Cin(n1_bit_5_cout), .S(A___B[29]), .Cout(n1_bit_3_cout));
  _1_bit u_1_bit_4 (.A(A[27]), .B(B[27]), .Cin(n1_bit_7_cout), .S(A___B[27]), .Cout(n1_bit_4_cout));
  _1_bit u_1_bit_5 (.A(A[28]), .B(B[28]), .Cin(n1_bit_4_cout), .S(A___B[28]), .Cout(n1_bit_5_cout));
  _1_bit u_1_bit_6 (.A(A[25]), .B(B[25]), .Cin(n1_bit_8_cout), .S(A___B[25]), .Cout(n1_bit_6_cout));
  _1_bit u_1_bit_7 (.A(A[26]), .B(B[26]), .Cin(n1_bit_6_cout), .S(A___B[26]), .Cout(n1_bit_7_cout));
  _1_bit u_1_bit_8 (.A(A[24]), .B(B[24]), .Cin(n1_bit_9_cout), .S(A___B[24]), .Cout(n1_bit_8_cout));
  _1_bit u_1_bit_9 (.A(A[23]), .B(B[23]), .Cin(n1_bit_11_cout), .S(A___B[23]), .Cout(n1_bit_9_cout));
  _1_bit u_1_bit_10 (.A(A[21]), .B(B[21]), .Cin(n1_bit_13_cout), .S(A___B[21]), .Cout(n1_bit_10_cout));
  _1_bit u_1_bit_11 (.A(A[22]), .B(B[22]), .Cin(n1_bit_10_cout), .S(A___B[22]), .Cout(n1_bit_11_cout));
  _1_bit u_1_bit_12 (.A(A[19]), .B(B[19]), .Cin(n1_bit_14_cout), .S(A___B[19]), .Cout(n1_bit_12_cout));
  _1_bit u_1_bit_13 (.A(A[20]), .B(B[20]), .Cin(n1_bit_12_cout), .S(A___B[20]), .Cout(n1_bit_13_cout));
  _1_bit u_1_bit_14 (.A(A[18]), .B(B[18]), .Cin(n1_bit_15_cout), .S(A___B[18]), .Cout(n1_bit_14_cout));
  _1_bit u_1_bit_15 (.A(A[17]), .B(B[17]), .Cin(n1_bit_16_cout), .S(A___B[17]), .Cout(n1_bit_15_cout));
  _1_bit u_1_bit_16 (.A(A[16]), .B(B[16]), .Cin(n1_bit_17_cout), .S(A___B[16]), .Cout(n1_bit_16_cout));
  _1_bit u_1_bit_17 (.A(A[15]), .B(B[15]), .Cin(n1_bit_19_cout), .S(A___B[15]), .Cout(n1_bit_17_cout));
  _1_bit u_1_bit_18 (.A(A[13]), .B(B[13]), .Cin(n1_bit_21_cout), .S(A___B[13]), .Cout(n1_bit_18_cout));
  _1_bit u_1_bit_19 (.A(A[14]), .B(B[14]), .Cin(n1_bit_18_cout), .S(A___B[14]), .Cout(n1_bit_19_cout));
  _1_bit u_1_bit_20 (.A(A[11]), .B(B[11]), .Cin(n1_bit_23_cout), .S(A___B[11]), .Cout(n1_bit_20_cout));
  _1_bit u_1_bit_21 (.A(A[12]), .B(B[12]), .Cin(n1_bit_20_cout), .S(A___B[12]), .Cout(n1_bit_21_cout));
  _1_bit u_1_bit_22 (.A(A[9]), .B(B[9]), .Cin(n1_bit_24_cout), .S(A___B[9]), .Cout(n1_bit_22_cout));
  _1_bit u_1_bit_23 (.A(A[10]), .B(B[10]), .Cin(n1_bit_22_cout), .S(A___B[10]), .Cout(n1_bit_23_cout));
  _1_bit u_1_bit_24 (.A(A[8]), .B(B[8]), .Cin(n1_bit_25_cout), .S(A___B[8]), .Cout(n1_bit_24_cout));
  _1_bit u_1_bit_25 (.A(A[7]), .B(B[7]), .Cin(n1_bit_26_cout), .S(A___B[7]), .Cout(n1_bit_25_cout));
  _1_bit u_1_bit_26 (.A(A[6]), .B(B[6]), .Cin(n1_bit_27_cout), .S(A___B[6]), .Cout(n1_bit_26_cout));
  _1_bit u_1_bit_27 (.A(A[5]), .B(B[5]), .Cin(n1_bit_28_cout), .S(A___B[5]), .Cout(n1_bit_27_cout));
  _1_bit u_1_bit_28 (.A(A[4]), .B(B[4]), .Cin(n1_bit_29_cout), .S(A___B[4]), .Cout(n1_bit_28_cout));
  _1_bit u_1_bit_29 (.A(A[3]), .B(B[3]), .Cin(n1_bit_30_cout), .S(A___B[3]), .Cout(n1_bit_29_cout));
  _1_bit u_1_bit_30 (.A(A[2]), .B(B[2]), .Cin(n1_bit_31_cout), .S(A___B[2]), .Cout(n1_bit_30_cout));
  _1_bit u_1_bit_31 (.A(A[1]), .B(B[1]), .Cin(n1_bit_32_cout), .S(A___B[1]), .Cout(n1_bit_31_cout));
  _1_bit u_1_bit_32 (.A(A[0]), .B(B[0]), .Cin(1'b0), .S(A___B[0]), .Cout(n1_bit_32_cout));

  // Other names for the same wires on the sheet: Cout = out_3

  // Notes on the sheet:
  //   32 bit unsigned adder
endmodule

module _32_bit_subu (
  input  [31:0] B,
  input  [31:0] A,
  output out_3,
  output [31:0] A___B
);

  wire n1_bit_2_bout, n1_bit_3_bout, n1_bit_4_bout, n1_bit_5_bout, n1_bit_6_bout, n1_bit_7_bout,
       n1_bit_8_bout, n1_bit_9_bout, n1_bit_10_bout, n1_bit_11_bout, n1_bit_12_bout, n1_bit_13_bout,
       n1_bit_14_bout, n1_bit_15_bout, n1_bit_16_bout, n1_bit_17_bout, n1_bit_18_bout, n1_bit_19_bout,
       n1_bit_20_bout, n1_bit_21_bout, n1_bit_22_bout, n1_bit_23_bout, n1_bit_24_bout, n1_bit_25_bout,
       n1_bit_26_bout, n1_bit_27_bout, n1_bit_28_bout, n1_bit_29_bout, n1_bit_30_bout, n1_bit_31_bout,
       n1_bit_32_bout;

  _1_bit_2 u_1_bit_1 (.Bin(n1_bit_3_bout), .A(A[31]), .B(B[31]), .Diff(A___B[31]), .Bout(out_3));
  _1_bit_2 u_1_bit_2 (.Bin(n1_bit_4_bout), .A(A[29]), .B(B[29]), .Diff(A___B[29]), .Bout(n1_bit_2_bout));
  _1_bit_2 u_1_bit_3 (.Bin(n1_bit_2_bout), .A(A[30]), .B(B[30]), .Diff(A___B[30]), .Bout(n1_bit_3_bout));
  _1_bit_2 u_1_bit_4 (.Bin(n1_bit_5_bout), .A(A[28]), .B(B[28]), .Diff(A___B[28]), .Bout(n1_bit_4_bout));
  _1_bit_2 u_1_bit_5 (.Bin(n1_bit_7_bout), .A(A[27]), .B(B[27]), .Diff(A___B[27]), .Bout(n1_bit_5_bout));
  _1_bit_2 u_1_bit_6 (.Bin(n1_bit_8_bout), .A(A[25]), .B(B[25]), .Diff(A___B[25]), .Bout(n1_bit_6_bout));
  _1_bit_2 u_1_bit_7 (.Bin(n1_bit_6_bout), .A(A[26]), .B(B[26]), .Diff(A___B[26]), .Bout(n1_bit_7_bout));
  _1_bit_2 u_1_bit_8 (.Bin(n1_bit_9_bout), .A(A[24]), .B(B[24]), .Diff(A___B[24]), .Bout(n1_bit_8_bout));
  _1_bit_2 u_1_bit_9 (.Bin(n1_bit_11_bout), .A(A[23]), .B(B[23]), .Diff(A___B[23]), .Bout(n1_bit_9_bout));
  _1_bit_2 u_1_bit_10 (.Bin(n1_bit_12_bout), .A(A[21]), .B(B[21]), .Diff(A___B[21]), .Bout(n1_bit_10_bout));
  _1_bit_2 u_1_bit_11 (.Bin(n1_bit_10_bout), .A(A[22]), .B(B[22]), .Diff(A___B[22]), .Bout(n1_bit_11_bout));
  _1_bit_2 u_1_bit_12 (.Bin(n1_bit_13_bout), .A(A[20]), .B(B[20]), .Diff(A___B[20]), .Bout(n1_bit_12_bout));
  _1_bit_2 u_1_bit_13 (.Bin(n1_bit_14_bout), .A(A[19]), .B(B[19]), .Diff(A___B[19]), .Bout(n1_bit_13_bout));
  _1_bit_2 u_1_bit_14 (.Bin(n1_bit_15_bout), .A(A[18]), .B(B[18]), .Diff(A___B[18]), .Bout(n1_bit_14_bout));
  _1_bit_2 u_1_bit_15 (.Bin(n1_bit_17_bout), .A(A[17]), .B(B[17]), .Diff(A___B[17]), .Bout(n1_bit_15_bout));
  _1_bit_2 u_1_bit_16 (.Bin(n1_bit_19_bout), .A(A[15]), .B(B[15]), .Diff(A___B[15]), .Bout(n1_bit_16_bout));
  _1_bit_2 u_1_bit_17 (.Bin(n1_bit_16_bout), .A(A[16]), .B(B[16]), .Diff(A___B[16]), .Bout(n1_bit_17_bout));
  _1_bit_2 u_1_bit_18 (.Bin(n1_bit_21_bout), .A(A[13]), .B(B[13]), .Diff(A___B[13]), .Bout(n1_bit_18_bout));
  _1_bit_2 u_1_bit_19 (.Bin(n1_bit_18_bout), .A(A[14]), .B(B[14]), .Diff(A___B[14]), .Bout(n1_bit_19_bout));
  _1_bit_2 u_1_bit_20 (.Bin(n1_bit_22_bout), .A(A[11]), .B(B[11]), .Diff(A___B[11]), .Bout(n1_bit_20_bout));
  _1_bit_2 u_1_bit_21 (.Bin(n1_bit_20_bout), .A(A[12]), .B(B[12]), .Diff(A___B[12]), .Bout(n1_bit_21_bout));
  _1_bit_2 u_1_bit_22 (.Bin(n1_bit_23_bout), .A(A[10]), .B(B[10]), .Diff(A___B[10]), .Bout(n1_bit_22_bout));
  _1_bit_2 u_1_bit_23 (.Bin(n1_bit_25_bout), .A(A[9]), .B(B[9]), .Diff(A___B[9]), .Bout(n1_bit_23_bout));
  _1_bit_2 u_1_bit_24 (.Bin(n1_bit_27_bout), .A(A[7]), .B(B[7]), .Diff(A___B[7]), .Bout(n1_bit_24_bout));
  _1_bit_2 u_1_bit_25 (.Bin(n1_bit_24_bout), .A(A[8]), .B(B[8]), .Diff(A___B[8]), .Bout(n1_bit_25_bout));
  _1_bit_2 u_1_bit_26 (.Bin(n1_bit_28_bout), .A(A[5]), .B(B[5]), .Diff(A___B[5]), .Bout(n1_bit_26_bout));
  _1_bit_2 u_1_bit_27 (.Bin(n1_bit_26_bout), .A(A[6]), .B(B[6]), .Diff(A___B[6]), .Bout(n1_bit_27_bout));
  _1_bit_2 u_1_bit_28 (.Bin(n1_bit_29_bout), .A(A[4]), .B(B[4]), .Diff(A___B[4]), .Bout(n1_bit_28_bout));
  _1_bit_2 u_1_bit_29 (.Bin(n1_bit_31_bout), .A(A[3]), .B(B[3]), .Diff(A___B[3]), .Bout(n1_bit_29_bout));
  _1_bit_2 u_1_bit_30 (.Bin(n1_bit_32_bout), .A(A[1]), .B(B[1]), .Diff(A___B[1]), .Bout(n1_bit_30_bout));
  _1_bit_2 u_1_bit_31 (.Bin(n1_bit_30_bout), .A(A[2]), .B(B[2]), .Diff(A___B[2]), .Bout(n1_bit_31_bout));
  _1_bit_2 u_1_bit_32 (.Bin(1'b0), .A(A[0]), .B(B[0]), .Diff(A___B[0]), .Bout(n1_bit_32_bout));

  // Other names for the same wires on the sheet: Cout = out_3

  // Notes on the sheet:
  //   32 bit unsigned subtractor
endmodule

module _32_bit_add (
  input  [31:0] B,
  input  [31:0] A,
  output out_3,
  output [31:0] A___B
);

  wire A_31, and_1_out, B_31, comparator_1_eq, comparator_1_gt, comparator_1_lt, multiplexer_1_out,
       multiplexer_2_out, multiplexer_3_out, multiplexer_4_out, n1_bit_2_cout, n1_bit_3_cout, n1_bit_4_cout,
       n1_bit_5_cout, n1_bit_6_cout, n1_bit_7_cout, n1_bit_8_cout, n1_bit_9_cout, n1_bit_10_cout,
       n1_bit_11_cout, n1_bit_12_cout, n1_bit_13_cout, n1_bit_14_cout, n1_bit_15_cout, n1_bit_16_cout,
       n1_bit_17_cout, n1_bit_18_cout, n1_bit_19_cout, n1_bit_20_cout, n1_bit_21_cout, n1_bit_22_cout,
       n1_bit_23_cout, n1_bit_24_cout, n1_bit_25_cout, n1_bit_26_cout, n1_bit_27_cout, n1_bit_28_cout,
       n1_bit_29_cout, n1_bit_30_cout, n1_bit_31_cout, not_1_out, xnor_1_out;
  wire [30:0] A_0_30, B_0_30;
  wire [31:0] n1_bit_30_s;

  _2_s_complement u_2_s_complement_1 (.In(B), .Out({B_31, B_0_30}));  // open: _2_s_Complement_Overflow
  _2_s_complement u_2_s_complement_2 (.In(A), .Out({A_31, A_0_30}));  // open: _2_s_Complement_Overflow
  _1_bit u_1_bit_1 (.A(A_0_30[30]), .B(B_0_30[30]), .Cin(n1_bit_3_cout), .S(n1_bit_30_s[30]), .Cout(out_3));
  _1_bit u_1_bit_2 (.A(A_0_30[28]), .B(B_0_30[28]), .Cin(n1_bit_4_cout), .S(n1_bit_30_s[28]), .Cout(n1_bit_2_cout));
  _1_bit u_1_bit_3 (.A(A_0_30[29]), .B(B_0_30[29]), .Cin(n1_bit_2_cout), .S(n1_bit_30_s[29]), .Cout(n1_bit_3_cout));
  _1_bit u_1_bit_4 (.A(A_0_30[27]), .B(B_0_30[27]), .Cin(n1_bit_5_cout), .S(n1_bit_30_s[27]), .Cout(n1_bit_4_cout));
  _1_bit u_1_bit_5 (.A(A_0_30[26]), .B(B_0_30[26]), .Cin(n1_bit_6_cout), .S(n1_bit_30_s[26]), .Cout(n1_bit_5_cout));
  _1_bit u_1_bit_6 (.A(A_0_30[25]), .B(B_0_30[25]), .Cin(n1_bit_7_cout), .S(n1_bit_30_s[25]), .Cout(n1_bit_6_cout));
  _1_bit u_1_bit_7 (.A(A_0_30[24]), .B(B_0_30[24]), .Cin(n1_bit_8_cout), .S(n1_bit_30_s[24]), .Cout(n1_bit_7_cout));
  _1_bit u_1_bit_8 (.A(A_0_30[23]), .B(B_0_30[23]), .Cin(n1_bit_9_cout), .S(n1_bit_30_s[23]), .Cout(n1_bit_8_cout));
  _1_bit u_1_bit_9 (.A(A_0_30[22]), .B(B_0_30[22]), .Cin(n1_bit_11_cout), .S(n1_bit_30_s[22]), .Cout(n1_bit_9_cout));
  _1_bit u_1_bit_10 (.A(A_0_30[20]), .B(B_0_30[20]), .Cin(n1_bit_12_cout), .S(n1_bit_30_s[20]), .Cout(n1_bit_10_cout));
  _1_bit u_1_bit_11 (.A(A_0_30[21]), .B(B_0_30[21]), .Cin(n1_bit_10_cout), .S(n1_bit_30_s[21]), .Cout(n1_bit_11_cout));
  _1_bit u_1_bit_12 (.A(A_0_30[19]), .B(B_0_30[19]), .Cin(n1_bit_13_cout), .S(n1_bit_30_s[19]), .Cout(n1_bit_12_cout));
  _1_bit u_1_bit_13 (.A(A_0_30[18]), .B(B_0_30[18]), .Cin(n1_bit_15_cout), .S(n1_bit_30_s[18]), .Cout(n1_bit_13_cout));
  _1_bit u_1_bit_14 (.A(A_0_30[16]), .B(B_0_30[16]), .Cin(n1_bit_17_cout), .S(n1_bit_30_s[16]), .Cout(n1_bit_14_cout));
  _1_bit u_1_bit_15 (.A(A_0_30[17]), .B(B_0_30[17]), .Cin(n1_bit_14_cout), .S(n1_bit_30_s[17]), .Cout(n1_bit_15_cout));
  _1_bit u_1_bit_16 (.A(A_0_30[14]), .B(B_0_30[14]), .Cin(n1_bit_19_cout), .S(n1_bit_30_s[14]), .Cout(n1_bit_16_cout));
  _1_bit u_1_bit_17 (.A(A_0_30[15]), .B(B_0_30[15]), .Cin(n1_bit_16_cout), .S(n1_bit_30_s[15]), .Cout(n1_bit_17_cout));
  _1_bit u_1_bit_18 (.A(A_0_30[12]), .B(B_0_30[12]), .Cin(n1_bit_20_cout), .S(n1_bit_30_s[12]), .Cout(n1_bit_18_cout));
  _1_bit u_1_bit_19 (.A(A_0_30[13]), .B(B_0_30[13]), .Cin(n1_bit_18_cout), .S(n1_bit_30_s[13]), .Cout(n1_bit_19_cout));
  Comparator #(.width(31)) comparator_1 (
    .a(A_0_30), .b(B_0_30), .gt(comparator_1_gt), .eq(comparator_1_eq), .lt(comparator_1_lt));
  _1_bit u_1_bit_20 (.A(A_0_30[11]), .B(B_0_30[11]), .Cin(n1_bit_21_cout), .S(n1_bit_30_s[11]), .Cout(n1_bit_20_cout));
  _1_bit u_1_bit_21 (.A(A_0_30[10]), .B(B_0_30[10]), .Cin(n1_bit_22_cout), .S(n1_bit_30_s[10]), .Cout(n1_bit_21_cout));
  _1_bit u_1_bit_22 (.A(A_0_30[9]), .B(B_0_30[9]), .Cin(n1_bit_23_cout), .S(n1_bit_30_s[9]), .Cout(n1_bit_22_cout));
  _1_bit u_1_bit_23 (.A(A_0_30[8]), .B(B_0_30[8]), .Cin(n1_bit_24_cout), .S(n1_bit_30_s[8]), .Cout(n1_bit_23_cout));
  Multiplexer #(.enable("false")) multiplexer_1 (
    .in0(B_31), .in1(A_31), .out(multiplexer_1_out), .sel(comparator_1_gt));
  _1_bit u_1_bit_24 (.A(A_0_30[7]), .B(B_0_30[7]), .Cin(n1_bit_25_cout), .S(n1_bit_30_s[7]), .Cout(n1_bit_24_cout));
  _1_bit u_1_bit_25 (.A(A_0_30[6]), .B(B_0_30[6]), .Cin(n1_bit_26_cout), .S(n1_bit_30_s[6]), .Cout(n1_bit_25_cout));
  Multiplexer #(.enable("false")) multiplexer_2 (
    .in0(multiplexer_1_out), .in1(1'b0), .out(multiplexer_2_out), .sel(comparator_1_eq));
  Multiplexer #(.enable("false")) multiplexer_3 (
    .in0(multiplexer_2_out), .in1(B_31), .out(multiplexer_3_out), .sel(comparator_1_lt));
  _1_bit u_1_bit_26 (.A(A_0_30[5]), .B(B_0_30[5]), .Cin(n1_bit_27_cout), .S(n1_bit_30_s[5]), .Cout(n1_bit_26_cout));
  _1_bit u_1_bit_27 (.A(A_0_30[4]), .B(B_0_30[4]), .Cin(n1_bit_29_cout), .S(n1_bit_30_s[4]), .Cout(n1_bit_27_cout));
  xnor xnor_1 (xnor_1_out, A_31, B_31);
  _1_bit u_1_bit_28 (.A(A_0_30[2]), .B(B_0_30[2]), .Cin(n1_bit_31_cout), .S(n1_bit_30_s[2]), .Cout(n1_bit_28_cout));
  _1_bit u_1_bit_29 (.A(A_0_30[3]), .B(B_0_30[3]), .Cin(n1_bit_28_cout), .S(n1_bit_30_s[3]), .Cout(n1_bit_29_cout));
  Multiplexer #(.enable("false")) multiplexer_4 (
    .in0(multiplexer_3_out), .in1(A_31), .out(multiplexer_4_out), .sel(and_1_out));
  and and_1 (and_1_out, xnor_1_out, A_31);
  not not_1 (not_1_out, and_1_out);
  _1_bit u_1_bit_30 (.A(A_0_30[0]), .B(B_0_30[0]), .Cin(1'b0), .S(n1_bit_30_s[0]), .Cout(n1_bit_30_cout));
  _1_bit u_1_bit_31 (.A(A_0_30[1]), .B(B_0_30[1]), .Cin(n1_bit_30_cout), .S(n1_bit_30_s[1]), .Cout(n1_bit_31_cout));
  Multiplexer #(.enable("false")) multiplexer_5 (
    .in0(multiplexer_4_out), .in1(B_31), .out(n1_bit_30_s[31]), .sel(not_1_out));
  _2_s_complement u_2_s_complement_3 (.In(n1_bit_30_s), .Out(A___B));  // open: _2_s_Complement_Overflow

  // Other names for the same wires on the sheet: Cout = out_3

  // Notes on the sheet:
  //   32 bit signed adder
endmodule

module _32_bit_sub (
  input  [31:0] B,
  input  [31:0] A,
  output Overflow_Exception,
  output [31:0] A___B
);

  wire A_31, and_1_out, B_31, comparator_1_eq, comparator_1_gt, comparator_1_lt, Cout, multiplexer_1_out,
       multiplexer_2_out, multiplexer_3_out, multiplexer_4_out, n1_bit_2_bout, n1_bit_3_bout, n1_bit_4_bout,
       n1_bit_5_bout, n1_bit_6_bout, n1_bit_7_bout, n1_bit_8_bout, n1_bit_9_bout, n1_bit_10_bout,
       n1_bit_11_bout, n1_bit_12_bout, n1_bit_13_bout, n1_bit_14_bout, n1_bit_15_bout, n1_bit_16_bout,
       n1_bit_17_bout, n1_bit_18_bout, n1_bit_19_bout, n1_bit_20_bout, n1_bit_21_bout, n1_bit_22_bout,
       n1_bit_23_bout, n1_bit_24_bout, n1_bit_25_bout, n1_bit_26_bout, n1_bit_27_bout, n1_bit_28_bout,
       n1_bit_29_bout, n1_bit_30_bout, n1_bit_31_bout, not_1_out, Overflow_1, Overflow_2, Overflow_3,
       xnor_1_out;
  wire [30:0] A_0_30, B_0_30;
  wire [31:0] n1_bit_31_diff;

  _2_s_complement u_2_s_complement_1 (.In(B), .Out({B_31, B_0_30}), ._2_s_Complement_Overflow(Overflow_1));
  _2_s_complement u_2_s_complement_2 (.In(A), .Out({A_31, A_0_30}), ._2_s_Complement_Overflow(Overflow_2));
  _1_bit_2 u_1_bit_1 (.Bin(n1_bit_3_bout), .A(A_0_30[30]), .B(B_0_30[30]), .Diff(n1_bit_31_diff[30]), .Bout(Cout));
  _1_bit_2 u_1_bit_2 (
    .Bin(n1_bit_5_bout), .A(A_0_30[28]), .B(B_0_30[28]), .Diff(n1_bit_31_diff[28]), .Bout(n1_bit_2_bout));
  _1_bit_2 u_1_bit_3 (
    .Bin(n1_bit_2_bout), .A(A_0_30[29]), .B(B_0_30[29]), .Diff(n1_bit_31_diff[29]), .Bout(n1_bit_3_bout));
  _1_bit_2 u_1_bit_4 (
    .Bin(n1_bit_6_bout), .A(A_0_30[26]), .B(B_0_30[26]), .Diff(n1_bit_31_diff[26]), .Bout(n1_bit_4_bout));
  _1_bit_2 u_1_bit_5 (
    .Bin(n1_bit_4_bout), .A(A_0_30[27]), .B(B_0_30[27]), .Diff(n1_bit_31_diff[27]), .Bout(n1_bit_5_bout));
  _1_bit_2 u_1_bit_6 (
    .Bin(n1_bit_7_bout), .A(A_0_30[25]), .B(B_0_30[25]), .Diff(n1_bit_31_diff[25]), .Bout(n1_bit_6_bout));
  _1_bit_2 u_1_bit_7 (
    .Bin(n1_bit_8_bout), .A(A_0_30[24]), .B(B_0_30[24]), .Diff(n1_bit_31_diff[24]), .Bout(n1_bit_7_bout));
  _1_bit_2 u_1_bit_8 (
    .Bin(n1_bit_9_bout), .A(A_0_30[23]), .B(B_0_30[23]), .Diff(n1_bit_31_diff[23]), .Bout(n1_bit_8_bout));
  _1_bit_2 u_1_bit_9 (
    .Bin(n1_bit_11_bout), .A(A_0_30[22]), .B(B_0_30[22]), .Diff(n1_bit_31_diff[22]), .Bout(n1_bit_9_bout));
  _1_bit_2 u_1_bit_10 (
    .Bin(n1_bit_13_bout), .A(A_0_30[20]), .B(B_0_30[20]), .Diff(n1_bit_31_diff[20]), .Bout(n1_bit_10_bout));
  _1_bit_2 u_1_bit_11 (
    .Bin(n1_bit_10_bout), .A(A_0_30[21]), .B(B_0_30[21]), .Diff(n1_bit_31_diff[21]), .Bout(n1_bit_11_bout));
  _1_bit_2 u_1_bit_12 (
    .Bin(n1_bit_15_bout), .A(A_0_30[18]), .B(B_0_30[18]), .Diff(n1_bit_31_diff[18]), .Bout(n1_bit_12_bout));
  _1_bit_2 u_1_bit_13 (
    .Bin(n1_bit_12_bout), .A(A_0_30[19]), .B(B_0_30[19]), .Diff(n1_bit_31_diff[19]), .Bout(n1_bit_13_bout));
  _1_bit_2 u_1_bit_14 (
    .Bin(n1_bit_16_bout), .A(A_0_30[16]), .B(B_0_30[16]), .Diff(n1_bit_31_diff[16]), .Bout(n1_bit_14_bout));
  _1_bit_2 u_1_bit_15 (
    .Bin(n1_bit_14_bout), .A(A_0_30[17]), .B(B_0_30[17]), .Diff(n1_bit_31_diff[17]), .Bout(n1_bit_15_bout));
  _1_bit_2 u_1_bit_16 (
    .Bin(n1_bit_17_bout), .A(A_0_30[15]), .B(B_0_30[15]), .Diff(n1_bit_31_diff[15]), .Bout(n1_bit_16_bout));
  _1_bit_2 u_1_bit_17 (
    .Bin(n1_bit_19_bout), .A(A_0_30[14]), .B(B_0_30[14]), .Diff(n1_bit_31_diff[14]), .Bout(n1_bit_17_bout));
  _1_bit_2 u_1_bit_18 (
    .Bin(n1_bit_21_bout), .A(A_0_30[12]), .B(B_0_30[12]), .Diff(n1_bit_31_diff[12]), .Bout(n1_bit_18_bout));
  _1_bit_2 u_1_bit_19 (
    .Bin(n1_bit_18_bout), .A(A_0_30[13]), .B(B_0_30[13]), .Diff(n1_bit_31_diff[13]), .Bout(n1_bit_19_bout));
  Comparator #(.width(31)) comparator_1 (
    .a(A_0_30), .b(B_0_30), .gt(comparator_1_gt), .eq(comparator_1_eq), .lt(comparator_1_lt));
  _1_bit_2 u_1_bit_20 (
    .Bin(n1_bit_23_bout), .A(A_0_30[10]), .B(B_0_30[10]), .Diff(n1_bit_31_diff[10]), .Bout(n1_bit_20_bout));
  _1_bit_2 u_1_bit_21 (
    .Bin(n1_bit_20_bout), .A(A_0_30[11]), .B(B_0_30[11]), .Diff(n1_bit_31_diff[11]), .Bout(n1_bit_21_bout));
  Multiplexer #(.enable("false")) multiplexer_1 (
    .in0(B_31), .in1(A_31), .out(multiplexer_1_out), .sel(comparator_1_gt));
  _1_bit_2 u_1_bit_22 (
    .Bin(n1_bit_25_bout), .A(A_0_30[8]), .B(B_0_30[8]), .Diff(n1_bit_31_diff[8]), .Bout(n1_bit_22_bout));
  _1_bit_2 u_1_bit_23 (
    .Bin(n1_bit_22_bout), .A(A_0_30[9]), .B(B_0_30[9]), .Diff(n1_bit_31_diff[9]), .Bout(n1_bit_23_bout));
  Multiplexer #(.enable("false")) multiplexer_2 (
    .in0(multiplexer_1_out), .in1(1'b0), .out(multiplexer_2_out), .sel(comparator_1_eq));
  _1_bit_2 u_1_bit_24 (
    .Bin(n1_bit_26_bout), .A(A_0_30[6]), .B(B_0_30[6]), .Diff(n1_bit_31_diff[6]), .Bout(n1_bit_24_bout));
  _1_bit_2 u_1_bit_25 (
    .Bin(n1_bit_24_bout), .A(A_0_30[7]), .B(B_0_30[7]), .Diff(n1_bit_31_diff[7]), .Bout(n1_bit_25_bout));
  Multiplexer #(.enable("false")) multiplexer_3 (
    .in0(multiplexer_2_out), .in1(B_31), .out(multiplexer_3_out), .sel(comparator_1_lt));
  _1_bit_2 u_1_bit_26 (
    .Bin(n1_bit_27_bout), .A(A_0_30[5]), .B(B_0_30[5]), .Diff(n1_bit_31_diff[5]), .Bout(n1_bit_26_bout));
  _1_bit_2 u_1_bit_27 (
    .Bin(n1_bit_29_bout), .A(A_0_30[4]), .B(B_0_30[4]), .Diff(n1_bit_31_diff[4]), .Bout(n1_bit_27_bout));
  xnor xnor_1 (xnor_1_out, A_31, B_31);
  and and_1 (and_1_out, xnor_1_out, A_31);
  _1_bit_2 u_1_bit_28 (
    .Bin(n1_bit_30_bout), .A(A_0_30[2]), .B(B_0_30[2]), .Diff(n1_bit_31_diff[2]), .Bout(n1_bit_28_bout));
  _1_bit_2 u_1_bit_29 (
    .Bin(n1_bit_28_bout), .A(A_0_30[3]), .B(B_0_30[3]), .Diff(n1_bit_31_diff[3]), .Bout(n1_bit_29_bout));
  Multiplexer #(.enable("false")) multiplexer_4 (
    .in0(multiplexer_3_out), .in1(A_31), .out(multiplexer_4_out), .sel(and_1_out));
  not not_1 (not_1_out, and_1_out);
  _1_bit_2 u_1_bit_30 (
    .Bin(n1_bit_31_bout), .A(A_0_30[1]), .B(B_0_30[1]), .Diff(n1_bit_31_diff[1]), .Bout(n1_bit_30_bout));
  _1_bit_2 u_1_bit_31 (.Bin(1'b0), .A(A_0_30[0]), .B(B_0_30[0]), .Diff(n1_bit_31_diff[0]), .Bout(n1_bit_31_bout));
  Multiplexer #(.enable("false")) multiplexer_5 (
    .in0(multiplexer_4_out), .in1(B_31), .out(n1_bit_31_diff[31]), .sel(not_1_out));
  _2_s_complement u_2_s_complement_3 (.In(n1_bit_31_diff), .Out(A___B), ._2_s_Complement_Overflow(Overflow_3));
  or or_1 (Overflow_Exception, Overflow_1, Overflow_2, Overflow_3, Cout);

  // Notes on the sheet:
  //   32 bit signed subtractor
endmodule

// +
module _1_bit (
  input  Cin,
  input  A,
  input  B,
  output S,
  output Cout
);

  wire and_1_out, and_2_out, xor_1_out;

  xor xor_1 (xor_1_out, A, B);
  and and_1 (and_1_out, A, B);
  and and_2 (and_2_out, xor_1_out, Cin);
  xor xor_2 (S, xor_1_out, Cin);
  or or_1 (Cout, and_2_out, and_1_out);
endmodule

// -
module _1_bit_2 (
  input  Bin,
  input  A,
  input  B,
  output Diff,
  output Bout
);

  wire and_1_out, and_2_out, not_1_out, not_2_out, xor_1_out;

  not not_1 (not_1_out, A);
  xor xor_1 (xor_1_out, A, B);
  and and_1 (and_1_out, B, not_1_out);
  not not_2 (not_2_out, xor_1_out);
  and and_2 (and_2_out, not_2_out, Bin);
  xor xor_2 (Diff, Bin, xor_1_out);
  or or_1 (Bout, and_2_out, and_1_out);
endmodule

// 2's
module _2_s_complement (
  input  [31:0] In,
  output [31:0] Out,
  output _2_s_Complement_Overflow
);

  wire adder_1_cout, not_2_out, zeros_1_out;
  wire [30:0] adder_1_out, not_1_out;

  assign not_1_out = ~In[30:0];  // NOT_Gate not_1, 31 bits wide
  Multiplexer #(.width(31), .enable("false")) multiplexer_1 (
    .in0(In[30:0]), .in1(adder_1_out), .out(Out[30:0]), .sel(In[31]));
  Adder #(.width(31)) adder_1 (.a(not_1_out), .b(31'h1), .out(adder_1_out), .cin(1'b0), .cout(adder_1_cout));
  not not_2 (not_2_out, zeros_1_out);
  Zeros zeros_1 (.In(In), .Out(zeros_1_out));
  and and_1 (_2_s_Complement_Overflow, adder_1_cout, not_2_out);

  assign Out[31] = In[31];
endmodule

// 0
module Zeros (
  input  [31:0] In,
  output Out
);

  nor nor_1 (Out, In[0], In[1], In[2], In[3], In[4], In[5], In[6], In[7], In[8], In[9], In[10], In[11], In[12], In[13], In[14], In[15], In[16], In[17], In[18], In[19], In[20], In[21], In[22], In[23], In[24], In[25], In[26], In[27], In[28], In[29], In[30], In[31]);

  // Notes on the sheet:
  //   Retorna 1 si todos son ceros
endmodule

module things_i_might_use_later (
  input  [31:0] B,
  input  [31:0] A,
  output out_3,
  output [31:0] A___B
);

  wire n1_bit_2_cout, n1_bit_3_cout, n1_bit_4_cout, n1_bit_5_cout, n1_bit_6_cout, n1_bit_7_cout,
       n1_bit_8_cout, n1_bit_9_cout, n1_bit_10_cout, n1_bit_11_cout, n1_bit_12_cout, n1_bit_13_cout,
       n1_bit_14_cout, n1_bit_15_cout, n1_bit_16_cout, n1_bit_17_cout, n1_bit_18_cout, n1_bit_19_cout,
       n1_bit_20_cout, n1_bit_21_cout, n1_bit_22_cout, n1_bit_23_cout, n1_bit_24_cout, n1_bit_25_cout,
       n1_bit_26_cout, n1_bit_27_cout, n1_bit_28_cout, n1_bit_29_cout, n1_bit_30_cout, n1_bit_31_cout,
       xor_1_out, xor_2_out, xor_3_out, xor_4_out, xor_5_out, xor_6_out, xor_7_out, xor_8_out, xor_9_out,
       xor_10_out, xor_11_out, xor_12_out, xor_13_out, xor_14_out, xor_15_out, xor_16_out, xor_17_out,
       xor_18_out, xor_19_out, xor_20_out, xor_21_out, xor_22_out, xor_23_out, xor_24_out, xor_25_out,
       xor_26_out, xor_27_out, xor_28_out, xor_29_out, xor_30_out, xor_31_out, xor_32_out, xor_33_out,
       xor_34_out, xor_35_out, xor_36_out, xor_37_out, xor_38_out, xor_39_out, xor_40_out, xor_41_out,
       xor_42_out, xor_43_out, xor_44_out, xor_45_out, xor_46_out, xor_47_out, xor_48_out, xor_49_out,
       xor_50_out, xor_51_out, xor_52_out, xor_53_out, xor_54_out, xor_55_out, xor_56_out, xor_57_out,
       xor_58_out, xor_59_out, xor_60_out, xor_61_out, xor_62_out;

  // Probe on A___B
  xor xor_1 (xor_1_out, B[31], B[30]);
  xor xor_2 (xor_2_out, A[31], A[30]);
  _1_bit u_1_bit_1 (.A(xor_2_out), .B(xor_1_out), .Cin(n1_bit_2_cout), .S(A___B[30]), .Cout(out_3));
  Comparator #(.width(32)) comparator_1 (.a(A), .b(B));  // open: gt, eq, lt
  xor xor_3 (xor_3_out, B[31], B[28]);
  xor xor_4 (xor_4_out, B[31], B[29]);
  xor xor_5 (xor_5_out, A[31], A[29]);
  xor xor_6 (xor_6_out, A[31], A[28]);
  _1_bit u_1_bit_2 (.A(xor_5_out), .B(xor_4_out), .Cin(n1_bit_3_cout), .S(A___B[29]), .Cout(n1_bit_2_cout));
  _1_bit u_1_bit_3 (.A(xor_6_out), .B(xor_3_out), .Cin(n1_bit_4_cout), .S(A___B[28]), .Cout(n1_bit_3_cout));
  xor xor_7 (xor_7_out, B[31], B[27]);
  xor xor_8 (xor_8_out, B[31], B[26]);
  xor xor_9 (xor_9_out, A[31], A[26]);
  xor xor_10 (xor_10_out, A[31], A[27]);
  _1_bit u_1_bit_4 (.A(xor_10_out), .B(xor_7_out), .Cin(n1_bit_5_cout), .S(A___B[27]), .Cout(n1_bit_4_cout));
  _1_bit u_1_bit_5 (.A(xor_9_out), .B(xor_8_out), .Cin(n1_bit_6_cout), .S(A___B[26]), .Cout(n1_bit_5_cout));
  xor xor_11 (xor_11_out, B[31], B[25]);
  xor xor_12 (xor_12_out, B[31], B[24]);
  xor xor_13 (xor_13_out, A[31], A[24]);
  xor xor_14 (xor_14_out, A[31], A[25]);
  _1_bit u_1_bit_6 (.A(xor_14_out), .B(xor_11_out), .Cin(n1_bit_7_cout), .S(A___B[25]), .Cout(n1_bit_6_cout));
  _1_bit u_1_bit_7 (.A(xor_13_out), .B(xor_12_out), .Cin(n1_bit_9_cout), .S(A___B[24]), .Cout(n1_bit_7_cout));
  xor xor_15 (xor_15_out, B[31], B[22]);
  xor xor_16 (xor_16_out, B[31], B[23]);
  xor xor_17 (xor_17_out, A[31], A[22]);
  xor xor_18 (xor_18_out, A[31], A[23]);
  _1_bit u_1_bit_8 (.A(xor_17_out), .B(xor_15_out), .Cin(n1_bit_11_cout), .S(A___B[22]), .Cout(n1_bit_8_cout));
  _1_bit u_1_bit_9 (.A(xor_18_out), .B(xor_16_out), .Cin(n1_bit_8_cout), .S(A___B[23]), .Cout(n1_bit_9_cout));
  xor xor_19 (xor_19_out, B[31], B[20]);
  xor xor_20 (xor_20_out, B[31], B[21]);
  xor xor_21 (xor_21_out, A[31], A[21]);
  xor xor_22 (xor_22_out, A[31], A[20]);
  _1_bit u_1_bit_10 (.A(xor_22_out), .B(xor_19_out), .Cin(n1_bit_13_cout), .S(A___B[20]), .Cout(n1_bit_10_cout));
  _1_bit u_1_bit_11 (.A(xor_21_out), .B(xor_20_out), .Cin(n1_bit_10_cout), .S(A___B[21]), .Cout(n1_bit_11_cout));
  xor xor_23 (xor_23_out, B[31], B[18]);
  xor xor_24 (xor_24_out, B[31], B[19]);
  xor xor_25 (xor_25_out, A[31], A[18]);
  xor xor_26 (xor_26_out, A[31], A[19]);
  _1_bit u_1_bit_12 (.A(xor_25_out), .B(xor_23_out), .Cin(n1_bit_14_cout), .S(A___B[18]), .Cout(n1_bit_12_cout));
  _1_bit u_1_bit_13 (.A(xor_26_out), .B(xor_24_out), .Cin(n1_bit_12_cout), .S(A___B[19]), .Cout(n1_bit_13_cout));
  xor xor_27 (xor_27_out, B[31], B[16]);
  xor xor_28 (xor_28_out, B[31], B[17]);
  xor xor_29 (xor_29_out, A[31], A[17]);
  xor xor_30 (xor_30_out, A[31], A[16]);
  _1_bit u_1_bit_14 (.A(xor_29_out), .B(xor_28_out), .Cin(n1_bit_15_cout), .S(A___B[17]), .Cout(n1_bit_14_cout));
  _1_bit u_1_bit_15 (.A(xor_30_out), .B(xor_27_out), .Cin(n1_bit_16_cout), .S(A___B[16]), .Cout(n1_bit_15_cout));
  xor xor_31 (xor_31_out, B[31], B[14]);
  xor xor_32 (xor_32_out, B[31], B[15]);
  xor xor_33 (xor_33_out, A[31], A[14]);
  xor xor_34 (xor_34_out, A[31], A[15]);
  _1_bit u_1_bit_16 (.A(xor_34_out), .B(xor_32_out), .Cin(n1_bit_17_cout), .S(A___B[15]), .Cout(n1_bit_16_cout));
  _1_bit u_1_bit_17 (.A(xor_33_out), .B(xor_31_out), .Cin(n1_bit_18_cout), .S(A___B[14]), .Cout(n1_bit_17_cout));
  xor xor_35 (xor_35_out, B[31], B[12]);
  xor xor_36 (xor_36_out, B[31], B[13]);
  xor xor_37 (xor_37_out, A[31], A[13]);
  xor xor_38 (xor_38_out, A[31], A[12]);
  _1_bit u_1_bit_18 (.A(xor_37_out), .B(xor_36_out), .Cin(n1_bit_19_cout), .S(A___B[13]), .Cout(n1_bit_18_cout));
  _1_bit u_1_bit_19 (.A(xor_38_out), .B(xor_35_out), .Cin(n1_bit_21_cout), .S(A___B[12]), .Cout(n1_bit_19_cout));
  xor xor_39 (xor_39_out, B[31], B[10]);
  xor xor_40 (xor_40_out, B[31], B[11]);
  xor xor_41 (xor_41_out, A[31], A[10]);
  xor xor_42 (xor_42_out, A[31], A[11]);
  _1_bit u_1_bit_20 (.A(xor_41_out), .B(xor_39_out), .Cin(n1_bit_22_cout), .S(A___B[10]), .Cout(n1_bit_20_cout));
  _1_bit u_1_bit_21 (.A(xor_42_out), .B(xor_40_out), .Cin(n1_bit_20_cout), .S(A___B[11]), .Cout(n1_bit_21_cout));
  xor xor_43 (xor_43_out, B[31], B[8]);
  xor xor_44 (xor_44_out, B[31], B[9]);
  xor xor_45 (xor_45_out, A[31], A[8]);
  xor xor_46 (xor_46_out, A[31], A[9]);
  _1_bit u_1_bit_22 (.A(xor_46_out), .B(xor_44_out), .Cin(n1_bit_23_cout), .S(A___B[9]), .Cout(n1_bit_22_cout));
  _1_bit u_1_bit_23 (.A(xor_45_out), .B(xor_43_out), .Cin(n1_bit_24_cout), .S(A___B[8]), .Cout(n1_bit_23_cout));
  xor xor_47 (xor_47_out, B[31], B[7]);
  xor xor_48 (xor_48_out, B[31], B[6]);
  xor xor_49 (xor_49_out, A[31], A[6]);
  xor xor_50 (xor_50_out, A[31], A[7]);
  _1_bit u_1_bit_24 (.A(xor_50_out), .B(xor_47_out), .Cin(n1_bit_25_cout), .S(A___B[7]), .Cout(n1_bit_24_cout));
  _1_bit u_1_bit_25 (.A(xor_49_out), .B(xor_48_out), .Cin(n1_bit_26_cout), .S(A___B[6]), .Cout(n1_bit_25_cout));
  xor xor_51 (xor_51_out, B[31], B[5]);
  xor xor_52 (xor_52_out, B[31], B[4]);
  xor xor_53 (xor_53_out, A[31], A[4]);
  xor xor_54 (xor_54_out, A[31], A[5]);
  _1_bit u_1_bit_26 (.A(xor_54_out), .B(xor_51_out), .Cin(n1_bit_27_cout), .S(A___B[5]), .Cout(n1_bit_26_cout));
  _1_bit u_1_bit_27 (.A(xor_53_out), .B(xor_52_out), .Cin(n1_bit_29_cout), .S(A___B[4]), .Cout(n1_bit_27_cout));
  xor xor_55 (xor_55_out, B[31], B[2]);
  xor xor_56 (xor_56_out, B[31], B[3]);
  xor xor_57 (xor_57_out, A[31], A[2]);
  xor xor_58 (xor_58_out, A[31], A[3]);
  _1_bit u_1_bit_28 (.A(xor_57_out), .B(xor_55_out), .Cin(n1_bit_30_cout), .S(A___B[2]), .Cout(n1_bit_28_cout));
  _1_bit u_1_bit_29 (.A(xor_58_out), .B(xor_56_out), .Cin(n1_bit_28_cout), .S(A___B[3]), .Cout(n1_bit_29_cout));
  xor xor_59 (xor_59_out, B[31], B[1]);
  xor xor_60 (xor_60_out, B[31], B[0]);
  xor xor_61 (xor_61_out, A[31], A[0]);
  xor xor_62 (xor_62_out, A[31], A[1]);
  _1_bit u_1_bit_30 (.A(xor_62_out), .B(xor_59_out), .Cin(n1_bit_31_cout), .S(A___B[1]), .Cout(n1_bit_30_cout));
  _1_bit u_1_bit_31 (.A(xor_61_out), .B(xor_60_out), .Cin(1'b0), .S(A___B[0]), .Cout(n1_bit_31_cout));

  // Other names for the same wires on the sheet: Cout = out_3

  // Notes on the sheet:
  //   32 bit signed adder
endmodule
