// Logisim project div.circ as structural Verilog: 3 circuits, main circuit Zeros
// 0
module Zeros (
  input  [31:0] In,
  output Out
);

  nor nor_1 (Out, In[0], In[1], In[2], In[3], In[4], In[5], In[6], In[7], In[8], In[9], In[10], In[11], In[12], In[13], In[14], In[15], In[16], In[17], In[18], In[19], In[20], In[21], In[22], In[23], In[24], In[25], In[26], In[27], In[28], In[29], In[30], In[31]);

  // Notes on the sheet:
  //   Retorna 1 si todos son ceros
endmodule

// <<64
module _64_bit_sl (
  input  [31:0] Second_In,
  input  [31:0] First_In,
  output [31:0] Second_Out,
  output [31:0] First_Out
);


  assign First_Out = {First_In[30:0], 1'b0};
  assign Second_Out = {Second_In[30:0], First_In[31]};
endmodule

module div (
  input  Clock
);
endmodule
