// Logisim project div_hecho_verga.circ as structural Verilog: 9 circuits, main circuit 32 bit divu
module main (
  input  [31:0] in_1,
  input  [31:0] in_2,
  output [31:0] out_3,
  output [31:0] out_4,
  output out_5
);

  _32_bit_div u_32_bit_div_1 (.Qout(out_3), .Aout(out_4), .DivisionByZeroException(out_5), .Qin(in_1), .Min(in_2));
endmodule

module _32_bit_divu (
  input  [31:0] Q,
  input  [31:0] M,
  output DivisionByZeroException,
  output [31:0] Low,
  output [31:0] High,
  output [31:0] M_2
);

  wire [31:0] divu_cycle_1_a_2, divu_cycle_1_m_2, divu_cycle_1_q_2, divu_cycle_2_a_2, divu_cycle_2_m_2,
       divu_cycle_2_q_2, divu_cycle_3_a_2, divu_cycle_3_m_2, divu_cycle_3_q_2, divu_cycle_4_a_2,
       divu_cycle_4_m_2, divu_cycle_4_q_2, divu_cycle_5_a_2, divu_cycle_5_m_2, divu_cycle_5_q_2,
       divu_cycle_6_a_2, divu_cycle_6_m_2, divu_cycle_6_q_2, divu_cycle_7_a_2, divu_cycle_7_m_2,
       divu_cycle_7_q_2, divu_cycle_8_a_2, divu_cycle_8_m_2, divu_cycle_8_q_2, divu_cycle_9_a_2,
       divu_cycle_9_m_2, divu_cycle_9_q_2, divu_cycle_10_a_2, divu_cycle_10_m_2, divu_cycle_10_q_2,
       divu_cycle_11_a_2, divu_cycle_11_m_2, divu_cycle_11_q_2, divu_cycle_12_a_2, divu_cycle_12_m_2,
       divu_cycle_12_q_2, divu_cycle_13_a_2, divu_cycle_13_m_2, divu_cycle_13_q_2, divu_cycle_14_a_2,
       divu_cycle_14_m_2, divu_cycle_14_q_2, divu_cycle_15_a_2, divu_cycle_15_m_2, divu_cycle_15_q_2,
       divu_cycle_16_a_2, divu_cycle_16_m_2, divu_cycle_16_q_2, divu_cycle_17_a_2, divu_cycle_17_m_2,
       divu_cycle_17_q_2, divu_cycle_18_a_2, divu_cycle_18_m_2, divu_cycle_18_q_2, divu_cycle_19_a_2,
       divu_cycle_19_m_2, divu_cycle_19_q_2, divu_cycle_20_a_2, divu_cycle_20_m_2, divu_cycle_20_q_2,
       divu_cycle_21_a_2, divu_cycle_21_m_2, divu_cycle_21_q_2, divu_cycle_22_a_2, divu_cycle_22_m_2,
       divu_cycle_22_q_2, divu_cycle_23_a_2, divu_cycle_23_m_2, divu_cycle_23_q_2, divu_cycle_24_a_2,
       divu_cycle_24_m_2, divu_cycle_24_q_2, divu_cycle_25_a_2, divu_cycle_25_m_2, divu_cycle_25_q_2,
       divu_cycle_26_a_2, divu_cycle_26_m_2, divu_cycle_26_q_2, divu_cycle_27_a_2, divu_cycle_27_m_2,
       divu_cycle_27_q_2, divu_cycle_28_a_2, divu_cycle_28_m_2, divu_cycle_28_q_2, divu_cycle_29_a_2,
       divu_cycle_29_m_2, divu_cycle_29_q_2, divu_cycle_30_a_2, divu_cycle_30_m_2, divu_cycle_30_q_2,
       divu_cycle_31_a_2, divu_cycle_31_m_2, divu_cycle_31_q_2, multiplexer_1_out, multiplexer_2_out,
       not_1_out, not_2_out;

  assign not_1_out = ~Q;  // NOT_Gate not_1, 32 bits wide
  Multiplexer #(.width(32), .enable("false")) multiplexer_1 (
    .in0(Q), .in1(not_1_out), .out(multiplexer_1_out), .sel(DivisionByZeroException));
  assign not_2_out = ~M;  // NOT_Gate not_2, 32 bits wide
  divu_cycle divu_cycle_1 (
    .Q(multiplexer_1_out), .A({32{1'b0}}), .M(multiplexer_2_out), .Q_2(divu_cycle_1_q_2),
    .A_2(divu_cycle_1_a_2), .M_2(divu_cycle_1_m_2));
  Multiplexer #(.width(32), .enable("false")) multiplexer_2 (
    .in0(M), .in1(not_2_out), .out(multiplexer_2_out), .sel(DivisionByZeroException));
  // Probe on divu_cycle_1_m_2
  // Probe on divu_cycle_1_a_2
  // Probe on divu_cycle_1_q_2
  Zeros zeros_1 (.In(M), .Out(DivisionByZeroException));
  divu_cycle divu_cycle_2 (
    .Q(divu_cycle_1_q_2), .A(divu_cycle_1_a_2), .M(divu_cycle_1_m_2), .Q_2(divu_cycle_2_q_2),
    .A_2(divu_cycle_2_a_2), .M_2(divu_cycle_2_m_2));
  // Probe on divu_cycle_2_m_2
  // Probe on divu_cycle_2_a_2
  // Probe on divu_cycle_2_q_2
  divu_cycle divu_cycle_3 (
    .Q(divu_cycle_2_q_2), .A(divu_cycle_2_a_2), .M(divu_cycle_2_m_2), .Q_2(divu_cycle_3_q_2),
    .A_2(divu_cycle_3_a_2), .M_2(divu_cycle_3_m_2));
  // Probe on divu_cycle_3_m_2
  // Probe on divu_cycle_3_a_2
  // Probe on divu_cycle_3_q_2
  divu_cycle divu_cycle_4 (
    .Q(divu_cycle_3_q_2), .A(divu_cycle_3_a_2), .M(divu_cycle_3_m_2), .Q_2(divu_cycle_4_q_2),
    .A_2(divu_cycle_4_a_2), .M_2(divu_cycle_4_m_2));
  // Probe on divu_cycle_4_m_2
  // Probe on divu_cycle_4_a_2
  // Probe on divu_cycle_4_q_2
  divu_cycle divu_cycle_5 (
    .Q(divu_cycle_4_q_2), .A(divu_cycle_4_a_2), .M(divu_cycle_4_m_2), .Q_2(divu_cycle_5_q_2),
    .A_2(divu_cycle_5_a_2), .M_2(divu_cycle_5_m_2));
  // Probe on divu_cycle_5_m_2
  // Probe on divu_cycle_5_a_2
  // Probe on divu_cycle_5_q_2
  divu_cycle divu_cycle_6 (
    .Q(divu_cycle_5_q_2), .A(divu_cycle_5_a_2), .M(divu_cycle_5_m_2), .Q_2(divu_cycle_6_q_2),
    .A_2(divu_cycle_6_a_2), .M_2(divu_cycle_6_m_2));
  // Probe on divu_cycle_6_m_2
  // Probe on divu_cycle_6_a_2
  // Probe on divu_cycle_6_q_2
  divu_cycle divu_cycle_7 (
    .Q(divu_cycle_6_q_2), .A(divu_cycle_6_a_2), .M(divu_cycle_6_m_2), .Q_2(divu_cycle_7_q_2),
    .A_2(divu_cycle_7_a_2), .M_2(divu_cycle_7_m_2));
  // Probe on divu_cycle_7_m_2
  // Probe on divu_cycle_7_a_2
  // Probe on divu_cycle_7_q_2
  divu_cycle divu_cycle_8 (
    .Q(divu_cycle_7_q_2), .A(divu_cycle_7_a_2), .M(divu_cycle_7_m_2), .Q_2(divu_cycle_8_q_2),
    .A_2(divu_cycle_8_a_2), .M_2(divu_cycle_8_m_2));
  // Probe on divu_cycle_8_m_2
  // Probe on divu_cycle_8_a_2
  // Probe on divu_cycle_8_q_2
  divu_cycle divu_cycle_9 (
    .Q(divu_cycle_8_q_2), .A(divu_cycle_8_a_2), .M(divu_cycle_8_m_2), .Q_2(divu_cycle_9_q_2),
    .A_2(divu_cycle_9_a_2), .M_2(divu_cycle_9_m_2));
  // Probe on divu_cycle_9_m_2
  // Probe on divu_cycle_9_a_2
  // Probe on divu_cycle_9_q_2
  divu_cycle divu_cycle_10 (
    .Q(divu_cycle_9_q_2), .A(divu_cycle_9_a_2), .M(divu_cycle_9_m_2), .Q_2(divu_cycle_10_q_2),
    .A_2(divu_cycle_10_a_2), .M_2(divu_cycle_10_m_2));
  // Probe on divu_cycle_10_m_2
  // Probe on divu_cycle_10_a_2
  // Probe on divu_cycle_10_q_2
  divu_cycle divu_cycle_11 (
    .Q(divu_cycle_10_q_2), .A(divu_cycle_10_a_2), .M(divu_cycle_10_m_2), .Q_2(divu_cycle_11_q_2),
    .A_2(divu_cycle_11_a_2), .M_2(divu_cycle_11_m_2));
  // Probe on divu_cycle_11_m_2
  // Probe on divu_cycle_11_a_2
  // Probe on divu_cycle_11_q_2
  divu_cycle divu_cycle_12 (
    .Q(divu_cycle_11_q_2), .A(divu_cycle_11_a_2), .M(divu_cycle_11_m_2), .Q_2(divu_cycle_12_q_2),
    .A_2(divu_cycle_12_a_2), .M_2(divu_cycle_12_m_2));
  // Probe on divu_cycle_12_m_2
  // Probe on divu_cycle_12_a_2
  // Probe on divu_cycle_12_q_2
  divu_cycle divu_cycle_13 (
    .Q(divu_cycle_12_q_2), .A(divu_cycle_12_a_2), .M(divu_cycle_12_m_2), .Q_2(divu_cycle_13_q_2),
    .A_2(divu_cycle_13_a_2), .M_2(divu_cycle_13_m_2));
  // Probe on divu_cycle_13_m_2
  // Probe on divu_cycle_13_a_2
  // Probe on divu_cycle_13_q_2
  divu_cycle divu_cycle_14 (
    .Q(divu_cycle_13_q_2), .A(divu_cycle_13_a_2), .M(divu_cycle_13_m_2), .Q_2(divu_cycle_14_q_2),
    .A_2(divu_cycle_14_a_2), .M_2(divu_cycle_14_m_2));
  // Probe on divu_cycle_14_m_2
  // Probe on divu_cycle_14_a_2
  // Probe on divu_cycle_14_q_2
  divu_cycle divu_cycle_15 (
    .Q(divu_cycle_14_q_2), .A(divu_cycle_14_a_2), .M(divu_cycle_14_m_2), .Q_2(divu_cycle_15_q_2),
    .A_2(divu_cycle_15_a_2), .M_2(divu_cycle_15_m_2));
  // Probe on divu_cycle_15_m_2
  // Probe on divu_cycle_15_a_2
  // Probe on divu_cycle_15_q_2
  divu_cycle divu_cycle_16 (
    .Q(divu_cycle_15_q_2), .A(divu_cycle_15_a_2), .M(divu_cycle_15_m_2), .Q_2(divu_cycle_16_q_2),
    .A_2(divu_cycle_16_a_2), .M_2(divu_cycle_16_m_2));
  // Probe on divu_cycle_16_m_2
  // Probe on divu_cycle_16_a_2
  // Probe on divu_cycle_16_q_2
  divu_cycle divu_cycle_17 (
    .Q(divu_cycle_16_q_2), .A(divu_cycle_16_a_2), .M(divu_cycle_16_m_2), .Q_2(divu_cycle_17_q_2),
    .A_2(divu_cycle_17_a_2), .M_2(divu_cycle_17_m_2));
  // Probe on divu_cycle_17_m_2
  // Probe on divu_cycle_17_a_2
  // Probe on divu_cycle_17_q_2
  divu_cycle divu_cycle_18 (
    .Q(divu_cycle_17_q_2), .A(divu_cycle_17_a_2), .M(divu_cycle_17_m_2), .Q_2(divu_cycle_18_q_2),
    .A_2(divu_cycle_18_a_2), .M_2(divu_cycle_18_m_2));
  // Probe on divu_cycle_18_m_2
  // Probe on divu_cycle_18_a_2
  // Probe on divu_cycle_18_q_2
  divu_cycle divu_cycle_19 (
    .Q(divu_cycle_18_q_2), .A(divu_cycle_18_a_2), .M(divu_cycle_18_m_2), .Q_2(divu_cycle_19_q_2),
    .A_2(divu_cycle_19_a_2), .M_2(divu_cycle_19_m_2));
  // Probe on divu_cycle_19_m_2
  // Probe on divu_cycle_19_a_2
  // Probe on divu_cycle_19_q_2
  divu_cycle divu_cycle_20 (
    .Q(divu_cycle_19_q_2), .A(divu_cycle_19_a_2), .M(divu_cycle_19_m_2), .Q_2(divu_cycle_20_q_2),
    .A_2(divu_cycle_20_a_2), .M_2(divu_cycle_20_m_2));
  // Probe on divu_cycle_20_m_2
  // Probe on divu_cycle_20_a_2
  // Probe on divu_cycle_20_q_2
  divu_cycle divu_cycle_21 (
    .Q(divu_cycle_20_q_2), .A(divu_cycle_20_a_2), .M(divu_cycle_20_m_2), .Q_2(divu_cycle_21_q_2),
    .A_2(divu_cycle_21_a_2), .M_2(divu_cycle_21_m_2));
  // Probe on divu_cycle_21_m_2
  // Probe on divu_cycle_21_a_2
  // Probe on divu_cycle_21_q_2
  divu_cycle divu_cycle_22 (
    .Q(divu_cycle_21_q_2), .A(divu_cycle_21_a_2), .M(divu_cycle_21_m_2), .Q_2(divu_cycle_22_q_2),
    .A_2(divu_cycle_22_a_2), .M_2(divu_cycle_22_m_2));
  // Probe on divu_cycle_22_m_2
  // Probe on divu_cycle_22_a_2
  // Probe on divu_cycle_22_q_2
  divu_cycle divu_cycle_23 (
    .Q(divu_cycle_22_q_2), .A(divu_cycle_22_a_2), .M(divu_cycle_22_m_2), .Q_2(divu_cycle_23_q_2),
    .A_2(divu_cycle_23_a_2), .M_2(divu_cycle_23_m_2));
  // Probe on divu_cycle_23_m_2
  // Probe on divu_cycle_23_a_2
  // Probe on divu_cycle_23_q_2
  divu_cycle divu_cycle_24 (
    .Q(divu_cycle_23_q_2), .A(divu_cycle_23_a_2), .M(divu_cycle_23_m_2), .Q_2(divu_cycle_24_q_2),
    .A_2(divu_cycle_24_a_2), .M_2(divu_cycle_24_m_2));
  // Probe on divu_cycle_24_m_2
  // Probe on divu_cycle_24_a_2
  // Probe on divu_cycle_24_q_2
  divu_cycle divu_cycle_25 (
    .Q(divu_cycle_24_q_2), .A(divu_cycle_24_a_2), .M(divu_cycle_24_m_2), .Q_2(divu_cycle_25_q_2),
    .A_2(divu_cycle_25_a_2), .M_2(divu_cycle_25_m_2));
  // Probe on divu_cycle_25_m_2
  // Probe on divu_cycle_25_a_2
  // Probe on divu_cycle_25_q_2
  divu_cycle divu_cycle_26 (
    .Q(divu_cycle_25_q_2), .A(divu_cycle_25_a_2), .M(divu_cycle_25_m_2), .Q_2(divu_cycle_26_q_2),
    .A_2(divu_cycle_26_a_2), .M_2(divu_cycle_26_m_2));
  // Probe on divu_cycle_26_m_2
  // Probe on divu_cycle_26_a_2
  // Probe on divu_cycle_26_q_2
  divu_cycle divu_cycle_27 (
    .Q(divu_cycle_26_q_2), .A(divu_cycle_26_a_2), .M(divu_cycle_26_m_2), .Q_2(divu_cycle_27_q_2),
    .A_2(divu_cycle_27_a_2), .M_2(divu_cycle_27_m_2));
  // Probe on divu_cycle_27_m_2
  // Probe on divu_cycle_27_a_2
  // Probe on divu_cycle_27_q_2
  divu_cycle divu_cycle_28 (
    .Q(divu_cycle_27_q_2), .A(divu_cycle_27_a_2), .M(divu_cycle_27_m_2), .Q_2(divu_cycle_28_q_2),
    .A_2(divu_cycle_28_a_2), .M_2(divu_cycle_28_m_2));
  // Probe on divu_cycle_28_m_2
  // Probe on divu_cycle_28_a_2
  // Probe on divu_cycle_28_q_2
  divu_cycle divu_cycle_29 (
    .Q(divu_cycle_28_q_2), .A(divu_cycle_28_a_2), .M(divu_cycle_28_m_2), .Q_2(divu_cycle_29_q_2),
    .A_2(divu_cycle_29_a_2), .M_2(divu_cycle_29_m_2));
  // Probe on divu_cycle_29_m_2
  // Probe on divu_cycle_29_a_2
  // Probe on divu_cycle_29_q_2
  divu_cycle divu_cycle_30 (
    .Q(divu_cycle_29_q_2), .A(divu_cycle_29_a_2), .M(divu_cycle_29_m_2), .Q_2(divu_cycle_30_q_2),
    .A_2(divu_cycle_30_a_2), .M_2(divu_cycle_30_m_2));
  // Probe on divu_cycle_30_m_2
  // Probe on divu_cycle_30_a_2
  // Probe on divu_cycle_30_q_2
  divu_cycle divu_cycle_31 (
    .Q(divu_cycle_30_q_2), .A(divu_cycle_30_a_2), .M(divu_cycle_30_m_2), .Q_2(divu_cycle_31_q_2),
    .A_2(divu_cycle_31_a_2), .M_2(divu_cycle_31_m_2));
  // Probe on divu_cycle_31_m_2
  // Probe on divu_cycle_31_a_2
  // Probe on divu_cycle_31_q_2
  divu_cycle divu_cycle_32 (
    .Q(divu_cycle_31_q_2), .A(divu_cycle_31_a_2), .M(divu_cycle_31_m_2), .Q_2(Low), .A_2(High), .M_2(M_2));
  // Probe on M_2
  // Probe on High
  // Probe on Low

  // Other names for the same wires on the sheet: Aout[31:0] = High; Min[31:0] = M; Mout[31:0] = M_2; Qin[31:0] = Q;
  //   Qout[31:0] = Low
endmodule

module divu_cycle (
  input  [31:0] Q,
  input  [31:0] A,
  input  [31:0] M,
  output [31:0] Q_2,
  output [31:0] A_2,
  output [31:0] M_2
);

  wire comparator_1_lt;
  wire [0:0] n64_bit_sl_1_first_out;
  wire [31:0] adder_1_out, n2_s_complement_1_out, n64_bit_sl_1_second_out, subtractor_1_out;

  // Probe on n64_bit_sl_1_second_out
  _64_bit_sl u_64_bit_sl_1 (
    .Second_In(A), .First_In(Q), .Second_Out(n64_bit_sl_1_second_out),
    .First_Out({Q_2[31:1], n64_bit_sl_1_first_out[0]}));
  // Probe on {Q_2[31:1], n64_bit_sl_1_first_out[0]}
  Subtractor #(.width(32)) subtractor_1 (
    .a(n64_bit_sl_1_second_out), .b(M), .out(subtractor_1_out), .bin(1'b0));  // open: bout
  // Probe on n2_s_complement_1_out
  _2_s_complement u_2_s_complement_1 (
    .In(subtractor_1_out), .Out(n2_s_complement_1_out));  // open: _2_s_Complement_Overflow
  // Probe on subtractor_1_out
  Comparator #(.width(32)) comparator_1 (.a(subtractor_1_out), .b({32{1'b0}}), .lt(comparator_1_lt));  // open: gt, eq
  Adder #(.width(32)) adder_1 (.a(subtractor_1_out), .b(M), .out(adder_1_out), .cin(1'b0));  // open: cout
  // Probe on adder_1_out
  // Probe on {Q_2[31:1], n64_bit_sl_1_first_out[0]}
  not not_1 (Q_2[0], comparator_1_lt);
  Multiplexer #(.width(32), .enable("false")) multiplexer_1 (
    .in0(subtractor_1_out), .in1(adder_1_out), .out(A_2), .sel(comparator_1_lt));

  assign M_2 = M;

  // Notes on the sheet:
  //   A < 0?
  //   if A < 0: Q_0 = 0
  //   else: Q_0 = 1
endmodule

module _32_bit_div (
  input  [31:0] Qin,
  input  [31:0] Min,
  output DivisionByZeroException,
  output [31:0] Qout,
  output [31:0] Aout
);

  wire [31:0] div_cycle_1_a_2, div_cycle_1_m_2, div_cycle_1_m_3, div_cycle_2_a_2, div_cycle_2_m_2,
       div_cycle_2_m_3, div_cycle_3_a_2, div_cycle_3_m_2, div_cycle_3_m_3, div_cycle_4_a_2, div_cycle_4_m_2,
       div_cycle_4_m_3, div_cycle_5_a_2, div_cycle_5_m_2, div_cycle_5_m_3, div_cycle_6_a_2, div_cycle_6_m_2,
       div_cycle_6_m_3, div_cycle_7_a_2, div_cycle_7_m_2, div_cycle_7_m_3, div_cycle_8_a_2, div_cycle_8_m_2,
       div_cycle_8_m_3, div_cycle_9_a_2, div_cycle_9_m_2, div_cycle_9_m_3, div_cycle_10_a_2,
       div_cycle_10_m_2, div_cycle_10_m_3, div_cycle_11_a_2, div_cycle_11_m_2, div_cycle_11_m_3,
       div_cycle_12_a_2, div_cycle_12_m_2, div_cycle_12_m_3, div_cycle_13_a_2, div_cycle_13_m_2,
       div_cycle_13_m_3, div_cycle_14_a_2, div_cycle_14_m_2, div_cycle_14_m_3, div_cycle_15_a_2,
       div_cycle_15_m_2, div_cycle_15_m_3, div_cycle_16_a_2, div_cycle_16_m_2, div_cycle_16_m_3,
       divu_cycle_1_a_2, divu_cycle_1_m_2, divu_cycle_1_q_2, divu_cycle_2_a_2, divu_cycle_2_m_2,
       divu_cycle_2_q_2, divu_cycle_3_a_2, divu_cycle_3_m_2, divu_cycle_3_q_2, divu_cycle_4_a_2,
       divu_cycle_4_m_2, divu_cycle_4_q_2, divu_cycle_5_a_2, divu_cycle_5_m_2, divu_cycle_5_q_2,
       divu_cycle_6_a_2, divu_cycle_6_m_2, divu_cycle_6_q_2, divu_cycle_7_a_2, divu_cycle_7_m_2,
       divu_cycle_7_q_2, divu_cycle_8_a_2, divu_cycle_8_m_2, divu_cycle_8_q_2, divu_cycle_9_a_2,
       divu_cycle_9_m_2, divu_cycle_9_q_2, divu_cycle_10_a_2, divu_cycle_10_m_2, divu_cycle_10_q_2,
       divu_cycle_11_a_2, divu_cycle_11_m_2, divu_cycle_11_q_2, divu_cycle_12_a_2, divu_cycle_12_m_2,
       divu_cycle_12_q_2, divu_cycle_13_a_2, divu_cycle_13_m_2, divu_cycle_13_q_2, divu_cycle_14_a_2,
       divu_cycle_14_m_2, divu_cycle_14_q_2, divu_cycle_15_a_2, divu_cycle_15_m_2, divu_cycle_15_q_2, Mout,
       multiplexer_1_out, multiplexer_2_out, not_1_out, not_2_out;

  assign not_1_out = ~Qin;  // NOT_Gate not_1, 32 bits wide
  Multiplexer #(.width(32), .enable("false")) multiplexer_1 (
    .in0(Qin), .in1(not_1_out), .out(multiplexer_1_out), .sel(DivisionByZeroException));
  assign not_2_out = ~Min;  // NOT_Gate not_2, 32 bits wide
  div_cycle div_cycle_1 (
    .Q(multiplexer_1_out), .A({32{1'b0}}), .M(multiplexer_2_out), .M_2(div_cycle_1_m_2),
    .A_2(div_cycle_1_a_2), .M_3(div_cycle_1_m_3));
  divu_cycle divu_cycle_1 (
    .Q(div_cycle_1_m_2), .A(div_cycle_1_a_2), .M(div_cycle_1_m_3), .Q_2(divu_cycle_1_q_2),
    .A_2(divu_cycle_1_a_2), .M_2(divu_cycle_1_m_2));
  Multiplexer #(.width(32), .enable("false")) multiplexer_2 (
    .in0(Min), .in1(not_2_out), .out(multiplexer_2_out), .sel(DivisionByZeroException));
  div_cycle div_cycle_2 (
    .Q(divu_cycle_1_q_2), .A(divu_cycle_1_a_2), .M(divu_cycle_1_m_2), .M_2(div_cycle_2_m_2),
    .A_2(div_cycle_2_a_2), .M_3(div_cycle_2_m_3));
  divu_cycle divu_cycle_2 (
    .Q(div_cycle_2_m_2), .A(div_cycle_2_a_2), .M(div_cycle_2_m_3), .Q_2(divu_cycle_2_q_2),
    .A_2(divu_cycle_2_a_2), .M_2(divu_cycle_2_m_2));
  Zeros zeros_1 (.In(Min), .Out(DivisionByZeroException));
  div_cycle div_cycle_3 (
    .Q(divu_cycle_3_q_2), .A(divu_cycle_3_a_2), .M(divu_cycle_3_m_2), .M_2(div_cycle_3_m_2),
    .A_2(div_cycle_3_a_2), .M_3(div_cycle_3_m_3));
  divu_cycle divu_cycle_3 (
    .Q(div_cycle_4_m_2), .A(div_cycle_4_a_2), .M(div_cycle_4_m_3), .Q_2(divu_cycle_3_q_2),
    .A_2(divu_cycle_3_a_2), .M_2(divu_cycle_3_m_2));
  div_cycle div_cycle_4 (
    .Q(divu_cycle_2_q_2), .A(divu_cycle_2_a_2), .M(divu_cycle_2_m_2), .M_2(div_cycle_4_m_2),
    .A_2(div_cycle_4_a_2), .M_3(div_cycle_4_m_3));
  divu_cycle divu_cycle_4 (
    .Q(div_cycle_5_m_2), .A(div_cycle_5_a_2), .M(div_cycle_5_m_3), .Q_2(divu_cycle_4_q_2),
    .A_2(divu_cycle_4_a_2), .M_2(divu_cycle_4_m_2));
  divu_cycle divu_cycle_5 (
    .Q(div_cycle_3_m_2), .A(div_cycle_3_a_2), .M(div_cycle_3_m_3), .Q_2(divu_cycle_5_q_2),
    .A_2(divu_cycle_5_a_2), .M_2(divu_cycle_5_m_2));
  div_cycle div_cycle_5 (
    .Q(divu_cycle_5_q_2), .A(divu_cycle_5_a_2), .M(divu_cycle_5_m_2), .M_2(div_cycle_5_m_2),
    .A_2(div_cycle_5_a_2), .M_3(div_cycle_5_m_3));
  div_cycle div_cycle_6 (
    .Q(divu_cycle_4_q_2), .A(divu_cycle_4_a_2), .M(divu_cycle_4_m_2), .M_2(div_cycle_6_m_2),
    .A_2(div_cycle_6_a_2), .M_3(div_cycle_6_m_3));
  divu_cycle divu_cycle_6 (
    .Q(div_cycle_6_m_2), .A(div_cycle_6_a_2), .M(div_cycle_6_m_3), .Q_2(divu_cycle_6_q_2),
    .A_2(divu_cycle_6_a_2), .M_2(divu_cycle_6_m_2));
  div_cycle div_cycle_7 (
    .Q(divu_cycle_7_q_2), .A(divu_cycle_7_a_2), .M(divu_cycle_7_m_2), .M_2(div_cycle_7_m_2),
    .A_2(div_cycle_7_a_2), .M_3(div_cycle_7_m_3));
  divu_cycle divu_cycle_7 (
    .Q(div_cycle_8_m_2), .A(div_cycle_8_a_2), .M(div_cycle_8_m_3), .Q_2(divu_cycle_7_q_2),
    .A_2(divu_cycle_7_a_2), .M_2(divu_cycle_7_m_2));
  div_cycle div_cycle_8 (
    .Q(divu_cycle_6_q_2), .A(divu_cycle_6_a_2), .M(divu_cycle_6_m_2), .M_2(div_cycle_8_m_2),
    .A_2(div_cycle_8_a_2), .M_3(div_cycle_8_m_3));
  divu_cycle divu_cycle_8 (
    .Q(div_cycle_7_m_2), .A(div_cycle_7_a_2), .M(div_cycle_7_m_3), .Q_2(divu_cycle_8_q_2),
    .A_2(divu_cycle_8_a_2), .M_2(divu_cycle_8_m_2));
  div_cycle div_cycle_9 (
    .Q(divu_cycle_8_q_2), .A(divu_cycle_8_a_2), .M(divu_cycle_8_m_2), .M_2(div_cycle_9_m_2),
    .A_2(div_cycle_9_a_2), .M_3(div_cycle_9_m_3));
  divu_cycle divu_cycle_9 (
    .Q(div_cycle_9_m_2), .A(div_cycle_9_a_2), .M(div_cycle_9_m_3), .Q_2(divu_cycle_9_q_2),
    .A_2(divu_cycle_9_a_2), .M_2(divu_cycle_9_m_2));
  div_cycle div_cycle_10 (
    .Q(divu_cycle_9_q_2), .A(divu_cycle_9_a_2), .M(divu_cycle_9_m_2), .M_2(div_cycle_10_m_2),
    .A_2(div_cycle_10_a_2), .M_3(div_cycle_10_m_3));
  divu_cycle divu_cycle_10 (
    .Q(div_cycle_10_m_2), .A(div_cycle_10_a_2), .M(div_cycle_10_m_3), .Q_2(divu_cycle_10_q_2),
    .A_2(divu_cycle_10_a_2), .M_2(divu_cycle_10_m_2));
  divu_cycle divu_cycle_11 (
    .Q(div_cycle_11_m_2), .A(div_cycle_11_a_2), .M(div_cycle_11_m_3), .Q_2(divu_cycle_11_q_2),
    .A_2(divu_cycle_11_a_2), .M_2(divu_cycle_11_m_2));
  div_cycle div_cycle_11 (
    .Q(divu_cycle_10_q_2), .A(divu_cycle_10_a_2), .M(divu_cycle_10_m_2), .M_2(div_cycle_11_m_2),
    .A_2(div_cycle_11_a_2), .M_3(div_cycle_11_m_3));
  div_cycle div_cycle_12 (
    .Q(divu_cycle_11_q_2), .A(divu_cycle_11_a_2), .M(divu_cycle_11_m_2), .M_2(div_cycle_12_m_2),
    .A_2(div_cycle_12_a_2), .M_3(div_cycle_12_m_3));
  divu_cycle divu_cycle_12 (
    .Q(div_cycle_13_m_2), .A(div_cycle_13_a_2), .M(div_cycle_13_m_3), .Q_2(divu_cycle_12_q_2),
    .A_2(divu_cycle_12_a_2), .M_2(divu_cycle_12_m_2));
  div_cycle div_cycle_13 (
    .Q(divu_cycle_13_q_2), .A(divu_cycle_13_a_2), .M(divu_cycle_13_m_2), .M_2(div_cycle_13_m_2),
    .A_2(div_cycle_13_a_2), .M_3(div_cycle_13_m_3));
  divu_cycle divu_cycle_13 (
    .Q(div_cycle_12_m_2), .A(div_cycle_12_a_2), .M(div_cycle_12_m_3), .Q_2(divu_cycle_13_q_2),
    .A_2(divu_cycle_13_a_2), .M_2(divu_cycle_13_m_2));
  div_cycle div_cycle_14 (
    .Q(divu_cycle_12_q_2), .A(divu_cycle_12_a_2), .M(divu_cycle_12_m_2), .M_2(div_cycle_14_m_2),
    .A_2(div_cycle_14_a_2), .M_3(div_cycle_14_m_3));
  divu_cycle divu_cycle_14 (
    .Q(div_cycle_14_m_2), .A(div_cycle_14_a_2), .M(div_cycle_14_m_3), .Q_2(divu_cycle_14_q_2),
    .A_2(divu_cycle_14_a_2), .M_2(divu_cycle_14_m_2));
  div_cycle div_cycle_15 (
    .Q(divu_cycle_14_q_2), .A(divu_cycle_14_a_2), .M(divu_cycle_14_m_2), .M_2(div_cycle_15_m_2),
    .A_2(div_cycle_15_a_2), .M_3(div_cycle_15_m_3));
  div_cycle div_cycle_16 (
    .Q(divu_cycle_15_q_2), .A(divu_cycle_15_a_2), .M(divu_cycle_15_m_2), .M_2(div_cycle_16_m_2),
    .A_2(div_cycle_16_a_2), .M_3(div_cycle_16_m_3));
  divu_cycle divu_cycle_15 (
    .Q(div_cycle_15_m_2), .A(div_cycle_15_a_2), .M(div_cycle_15_m_3), .Q_2(divu_cycle_15_q_2),
    .A_2(divu_cycle_15_a_2), .M_2(divu_cycle_15_m_2));
  divu_cycle divu_cycle_16 (
    .Q(div_cycle_16_m_2), .A(div_cycle_16_a_2), .M(div_cycle_16_m_3), .Q_2(Qout), .A_2(Aout), .M_2(Mout));
endmodule

module div_cycle (
  input  [31:0] Q,
  input  [31:0] A,
  input  [31:0] M,
  output [31:0] M_2,
  output [31:0] A_2,
  output [31:0] M_3
);

  wire and_1_out, and_2_out, and_3_out, not_1_out, not_2_out, not_3_out, or_1_out, xnor_1_out, xnor_2_out,
       zeros_1_out, zeros_2_out;
  wire [31:0] adder_1_out, n64_bit_sl_1_second_out, New_A, New_Q, subtractor_1_out;

  _64_bit_sl u_64_bit_sl_1 (.Second_In(A), .First_In(Q), .Second_Out(n64_bit_sl_1_second_out), .First_Out(New_Q));
  // Probe on M_2
  // Probe on A_2
  // Probe on M
  // Probe on n64_bit_sl_1_second_out
  // Probe on New_Q
  // Probe on subtractor_1_out
  // Probe on adder_1_out
  Adder #(.width(32)) adder_1 (.a(n64_bit_sl_1_second_out), .b(M), .out(adder_1_out), .cin(1'b0));  // open: cout
  Subtractor #(.width(32)) subtractor_1 (
    .a(n64_bit_sl_1_second_out), .b(M), .out(subtractor_1_out), .bin(1'b0));  // open: bout
  xnor xnor_1 (xnor_1_out, n64_bit_sl_1_second_out[31], M[31]);
  Multiplexer #(.width(32), .enable("false")) multiplexer_1 (
    .in0(adder_1_out), .in1(subtractor_1_out), .out(New_A), .sel(xnor_1_out));
  Zeros zeros_1 (.In(New_Q), .Out(zeros_1_out));
  Zeros zeros_2 (.In(New_A), .Out(zeros_2_out));
  xnor xnor_2 (xnor_2_out, New_A[31], n64_bit_sl_1_second_out[31]);
  // Probe on New_A
  // Probe on New_Q
  not not_1 (not_1_out, zeros_1_out);
  not not_2 (not_2_out, zeros_2_out);
  and and_1 (and_1_out, zeros_2_out, zeros_1_out);
  or or_1 (or_1_out, not_1_out, not_2_out);
  not not_3 (not_3_out, xnor_2_out);
  and and_2 (and_2_out, xnor_2_out, and_1_out);
  and and_3 (and_3_out, not_3_out, or_1_out);
  Multiplexer #(.width(32), .enable("false")) multiplexer_2 (.in0(New_A), .in1(A), .out(A_2), .sel(and_3_out));
  Multiplexer #(.width(32), .enable("false")) multiplexer_3 (.in0(New_Q), .in1(32'h1), .out(M_2), .sel(and_2_out));

  assign M_3 = M;

  // Other names for the same wires on the sheet: A_t[31:0] = A_2; Q_t[31:0] = M_2; Restore_A[31:0] = A

  // Notes on the sheet:
  //   S=A_31
  //   M_31
  //   A = A + M
  //   A = A - M
  //   if M_31 == A_31
  //   Q == 0
  //   A == 0
  //   if S == A_31
  //   IF (A == 0 and Q == 0) Q_0 = 1, else leave Q alone.
  //   Q=0 => Q_1 = 1 => 000...1
  //   IF (A != 0 or Q != 0) Restore A; else leave A
endmodule

// 0
module Zeros (
  input  [31:0] In,
  output Out
);

  nor nor_1 (Out, In[0], In[1], In[2], In[3], In[4], In[5], In[6], In[7], In[8], In[9], In[10], In[11], In[12], In[13], In[14], In[15], In[16], In[17], In[18], In[19], In[20], In[21], In[22], In[23], In[24], In[25], In[26], In[27], In[28], In[29], In[30], In[31]);

  // Notes on the sheet:
  //   Retorna 1 si todos son ceros
endmodule

// <<64
module _64_bit_sl (
  input  [31:0] Second_In,
  input  [31:0] First_In,
  output [31:0] Second_Out,
  output [31:0] First_Out
);


  assign First_Out = {First_In[30:0], 1'b0};
  assign Second_Out = {Second_In[30:0], First_In[31]};
endmodule

module trial (
  input  [31:0] Rem_in,
  input  [31:0] Div_in,
  input  [31:0] Quo_in,
  output [31:0] Rem_out,
  output [31:0] Div_out,
  output [31:0] Quo_out
);

  wire comparator_1_eq, comparator_1_gt, comparator_1_lt;
  wire [0:0] shifter_2_out;
  wire [31:0] adder_1_out, subtractor_1_out;

  Subtractor #(.width(32)) subtractor_1 (.a(Rem_in), .b(Div_in), .out(subtractor_1_out), .bin(1'b0));  // open: bout
  or or_1 (Quo_out[0], comparator_1_gt, comparator_1_eq);
  Comparator #(.width(32)) comparator_1 (
    .a(subtractor_1_out), .b({32{1'b0}}), .gt(comparator_1_gt), .eq(comparator_1_eq), .lt(comparator_1_lt));
  Multiplexer #(.width(32), .enable("false")) multiplexer_1 (
    .in0(Rem_in), .in1(adder_1_out), .out(Rem_out), .sel(comparator_1_lt));
  Adder #(.width(32)) adder_1 (.a(subtractor_1_out), .b(Rem_in), .out(adder_1_out), .cin(1'b0));  // open: cout
  Shifter #(.width(32), .shift("lr")) shifter_1 (.in(Div_in), .\dist (5'b00001), .out(Div_out));
  Shifter #(.width(32)) shifter_2 (.in(Quo_in), .\dist (5'b00001), .out({Quo_out[31:1], shifter_2_out[0]}));

  // Notes on the sheet:
  //   Remainder register
  //   Rem < 0: restore Rem and sl Quo and Q_0 = 1.
  //    Restore the original value by adding
  //   the Divisor register to the Remainder
  //   register and placing the sum in the
  //   New rem if Rem < 0
  //   Rem <= 0: sl Quo and Q_0 = 1
endmodule

module main_trail (
  input  [31:0] Rem_in,
  input  [31:0] Div_in,
  input  [31:0] Quo_in,
  output DivisionByZeroException,
  output [31:0] Rem_out,
  output [31:0] Div_out,
  output [31:0] Quo_out
);

  wire [31:0] _1_div_out, _1_quo_out, _1_rem_out, _2_div_out, _2_quo_out, _2_rem_out, _3_div_out, _3_quo_out,
       _3_rem_out, _4_div_out, _4_quo_out, _4_rem_out, _5_div_out, _5_quo_out, _5_rem_out, _6_div_out,
       _6_quo_out, _6_rem_out, _7_div_out, _7_quo_out, _7_rem_out, _8_div_out, _8_quo_out, _8_rem_out,
       _9_div_out, _9_quo_out, _9_rem_out, _10_div_out, _10_quo_out, _10_rem_out, _11_div_out, _11_quo_out,
       _11_rem_out, _12_div_out, _12_quo_out, _12_rem_out, _13_div_out, _13_quo_out, _13_rem_out,
       _14_div_out, _14_quo_out, _14_rem_out, _15_div_out, _15_quo_out, _15_rem_out, _16_div_out,
       _16_quo_out, _16_rem_out, _17_div_out, _17_quo_out, _17_rem_out, _18_div_out, _18_quo_out,
       _18_rem_out, _19_div_out, _19_quo_out, _19_rem_out, _20_div_out, _20_quo_out, _20_rem_out,
       _21_div_out, _21_quo_out, _21_rem_out, _22_div_out, _22_quo_out, _22_rem_out, _23_div_out,
       _23_quo_out, _23_rem_out, _24_div_out, _24_quo_out, _24_rem_out, _25_div_out, _25_quo_out,
       _25_rem_out, _26_div_out, _26_quo_out, _26_rem_out, _27_div_out, _27_quo_out, _27_rem_out,
       _28_div_out, _28_quo_out, _28_rem_out, _29_div_out, _29_quo_out, _29_rem_out, _30_div_out,
       _30_quo_out, _30_rem_out, _31_div_out, _31_quo_out, _31_rem_out;

  trial _1 (
    .Rem_in(Rem_in), .Div_in(Div_in), .Quo_in(Quo_in), .Rem_out(_1_rem_out), .Div_out(_1_div_out),
    .Quo_out(_1_quo_out));
  // Probe on _1_rem_out
  // Probe on _1_div_out
  // Probe on _1_quo_out
  trial _2 (
    .Rem_in(_1_rem_out), .Div_in(_1_div_out), .Quo_in(_1_quo_out), .Rem_out(_2_rem_out),
    .Div_out(_2_div_out), .Quo_out(_2_quo_out));
  // Probe on _2_rem_out
  // Probe on _2_div_out
  // Probe on _2_quo_out
  trial _3 (
    .Rem_in(_2_rem_out), .Div_in(_2_div_out), .Quo_in(_2_quo_out), .Rem_out(_3_rem_out),
    .Div_out(_3_div_out), .Quo_out(_3_quo_out));
  // Probe on _3_rem_out
  // Probe on _3_div_out
  // Probe on _3_quo_out
  Zeros zeros_1 (.In(Div_in), .Out(DivisionByZeroException));
  // Probe on _4_rem_out
  // Probe on _4_div_out
  // Probe on _4_quo_out
  trial _4 (
    .Rem_in(_3_rem_out), .Div_in(_3_div_out), .Quo_in(_3_quo_out), .Rem_out(_4_rem_out),
    .Div_out(_4_div_out), .Quo_out(_4_quo_out));
  trial _5 (
    .Rem_in(_4_rem_out), .Div_in(_4_div_out), .Quo_in(_4_quo_out), .Rem_out(_5_rem_out),
    .Div_out(_5_div_out), .Quo_out(_5_quo_out));
  // Probe on _5_rem_out
  // Probe on _5_div_out
  // Probe on _5_quo_out
  trial _6 (
    .Rem_in(_5_rem_out), .Div_in(_5_div_out), .Quo_in(_5_quo_out), .Rem_out(_6_rem_out),
    .Div_out(_6_div_out), .Quo_out(_6_quo_out));
  // Probe on _6_rem_out
  // Probe on _6_div_out
  // Probe on _6_quo_out
  trial _7 (
    .Rem_in(_6_rem_out), .Div_in(_6_div_out), .Quo_in(_6_quo_out), .Rem_out(_7_rem_out),
    .Div_out(_7_div_out), .Quo_out(_7_quo_out));
  // Probe on _7_rem_out
  // Probe on _7_div_out
  // Probe on _7_quo_out
  // Probe on _8_rem_out
  // Probe on _8_div_out
  // Probe on _8_quo_out
  trial _8 (
    .Rem_in(_7_rem_out), .Div_in(_7_div_out), .Quo_in(_7_quo_out), .Rem_out(_8_rem_out),
    .Div_out(_8_div_out), .Quo_out(_8_quo_out));
  trial _9 (
    .Rem_in(_8_rem_out), .Div_in(_8_div_out), .Quo_in(_8_quo_out), .Rem_out(_9_rem_out),
    .Div_out(_9_div_out), .Quo_out(_9_quo_out));
  // Probe on _9_rem_out
  // Probe on _9_div_out
  // Probe on _9_quo_out
  // Probe on _10_rem_out
  // Probe on _10_div_out
  // Probe on _10_quo_out
  trial _10 (
    .Rem_in(_9_rem_out), .Div_in(_9_div_out), .Quo_in(_9_quo_out), .Rem_out(_10_rem_out),
    .Div_out(_10_div_out), .Quo_out(_10_quo_out));
  trial _11 (
    .Rem_in(_10_rem_out), .Div_in(_10_div_out), .Quo_in(_10_quo_out), .Rem_out(_11_rem_out),
    .Div_out(_11_div_out), .Quo_out(_11_quo_out));
  // Probe on _11_rem_out
  // Probe on _11_div_out
  // Probe on _11_quo_out
  // Probe on _12_rem_out
  // Probe on _12_div_out
  // Probe on _12_quo_out
  trial _12 (
    .Rem_in(_11_rem_out), .Div_in(_11_div_out), .Quo_in(_11_quo_out), .Rem_out(_12_rem_out),
    .Div_out(_12_div_out), .Quo_out(_12_quo_out));
  trial _13 (
    .Rem_in(_12_rem_out), .Div_in(_12_div_out), .Quo_in(_12_quo_out), .Rem_out(_13_rem_out),
    .Div_out(_13_div_out), .Quo_out(_13_quo_out));
  // Probe on _13_rem_out
  // Probe on _13_div_out
  // Probe on _13_quo_out
  // Probe on _14_rem_out
  // Probe on _14_div_out
  // Probe on _14_quo_out
  trial _14 (
    .Rem_in(_13_rem_out), .Div_in(_13_div_out), .Quo_in(_13_quo_out), .Rem_out(_14_rem_out),
    .Div_out(_14_div_out), .Quo_out(_14_quo_out));
  trial _15 (
    .Rem_in(_14_rem_out), .Div_in(_14_div_out), .Quo_in(_14_quo_out), .Rem_out(_15_rem_out),
    .Div_out(_15_div_out), .Quo_out(_15_quo_out));
  // Probe on _15_rem_out
  // Probe on _15_div_out
  // Probe on _15_quo_out
  // Probe on _16_rem_out
  // Probe on _16_div_out
  // Probe on _16_quo_out
  trial _16 (
    .Rem_in(_15_rem_out), .Div_in(_15_div_out), .Quo_in(_15_quo_out), .Rem_out(_16_rem_out),
    .Div_out(_16_div_out), .Quo_out(_16_quo_out));
  trial _17 (
    .Rem_in(_16_rem_out), .Div_in(_16_div_out), .Quo_in(_16_quo_out), .Rem_out(_17_rem_out),
    .Div_out(_17_div_out), .Quo_out(_17_quo_out));
  // Probe on _17_rem_out
  // Probe on _17_div_out
  // Probe on _17_quo_out
  // Probe on _18_rem_out
  // Probe on _18_div_out
  // Probe on _18_quo_out
  trial _18 (
    .Rem_in(_17_rem_out), .Div_in(_17_div_out), .Quo_in(_17_quo_out), .Rem_out(_18_rem_out),
    .Div_out(_18_div_out), .Quo_out(_18_quo_out));
  trial _19 (
    .Rem_in(_18_rem_out), .Div_in(_18_div_out), .Quo_in(_18_quo_out), .Rem_out(_19_rem_out),
    .Div_out(_19_div_out), .Quo_out(_19_quo_out));
  trial _20 (
    .Rem_in(_19_rem_out), .Div_in(_19_div_out), .Quo_in(_19_quo_out), .Rem_out(_20_rem_out),
    .Div_out(_20_div_out), .Quo_out(_20_quo_out));
  // Probe on _19_rem_out
  // Probe on _19_div_out
  // Probe on _19_quo_out
  // Probe on _20_rem_out
  // Probe on _20_div_out
  // Probe on _20_quo_out
  trial _21 (
    .Rem_in(_20_rem_out), .Div_in(_20_div_out), .Quo_in(_20_quo_out), .Rem_out(_21_rem_out),
    .Div_out(_21_div_out), .Quo_out(_21_quo_out));
  // Probe on _21_rem_out
  // Probe on _21_div_out
  // Probe on _21_quo_out
  // Probe on _22_rem_out
  // Probe on _22_div_out
  // Probe on _22_quo_out
  trial _22 (
    .Rem_in(_21_rem_out), .Div_in(_21_div_out), .Quo_in(_21_quo_out), .Rem_out(_22_rem_out),
    .Div_out(_22_div_out), .Quo_out(_22_quo_out));
  trial _23 (
    .Rem_in(_22_rem_out), .Div_in(_22_div_out), .Quo_in(_22_quo_out), .Rem_out(_23_rem_out),
    .Div_out(_23_div_out), .Quo_out(_23_quo_out));
  trial _24 (
    .Rem_in(_23_rem_out), .Div_in(_23_div_out), .Quo_in(_23_quo_out), .Rem_out(_24_rem_out),
    .Div_out(_24_div_out), .Quo_out(_24_quo_out));
  // Probe on _23_rem_out
  // Probe on _23_div_out
  // Probe on _23_quo_out
  // Probe on _24_rem_out
  // Probe on _24_div_out
  // Probe on _24_quo_out
  trial _25 (
    .Rem_in(_24_rem_out), .Div_in(_24_div_out), .Quo_in(_24_quo_out), .Rem_out(_25_rem_out),
    .Div_out(_25_div_out), .Quo_out(_25_quo_out));
  // Probe on _25_rem_out
  // Probe on _25_div_out
  // Probe on _25_quo_out
  // Probe on _26_rem_out
  // Probe on _26_div_out
  // Probe on _26_quo_out
  trial _26 (
    .Rem_in(_25_rem_out), .Div_in(_25_div_out), .Quo_in(_25_quo_out), .Rem_out(_26_rem_out),
    .Div_out(_26_div_out), .Quo_out(_26_quo_out));
  trial _27 (
    .Rem_in(_26_rem_out), .Div_in(_26_div_out), .Quo_in(_26_quo_out), .Rem_out(_27_rem_out),
    .Div_out(_27_div_out), .Quo_out(_27_quo_out));
  // Probe on _27_rem_out
  // Probe on _27_div_out
  // Probe on _27_quo_out
  trial _28 (
    .Rem_in(_27_rem_out), .Div_in(_27_div_out), .Quo_in(_27_quo_out), .Rem_out(_28_rem_out),
    .Div_out(_28_div_out), .Quo_out(_28_quo_out));
  // Probe on _28_rem_out
  // Probe on _28_div_out
  // Probe on _28_quo_out
  trial _29 (
    .Rem_in(_28_rem_out), .Div_in(_28_div_out), .Quo_in(_28_quo_out), .Rem_out(_29_rem_out),
    .Div_out(_29_div_out), .Quo_out(_29_quo_out));
  // Probe on _29_rem_out
  // Probe on _29_div_out
  // Probe on _29_quo_out
  // Probe on _30_rem_out
  // Probe on _30_div_out
  // Probe on _30_quo_out
  trial _30 (
    .Rem_in(_29_rem_out), .Div_in(_29_div_out), .Quo_in(_29_quo_out), .Rem_out(_30_rem_out),
    .Div_out(_30_div_out), .Quo_out(_30_quo_out));
  trial _31 (
    .Rem_in(_30_rem_out), .Div_in(_30_div_out), .Quo_in(_30_quo_out), .Rem_out(_31_rem_out),
    .Div_out(_31_div_out), .Quo_out(_31_quo_out));
  // Probe on _31_rem_out
  // Probe on _31_div_out
  // Probe on _31_quo_out
  trial _32 (
    .Rem_in(_31_rem_out), .Div_in(_31_div_out), .Quo_in(_31_quo_out), .Rem_out(Rem_out), .Div_out(Div_out),
    .Quo_out(Quo_out));
  // Probe on Rem_out
  // Probe on Div_out
  // Probe on Quo_out

  // Notes on the sheet:
  //   divisor = denominator
endmodule
