// Logisim project mult.circ as structural Verilog: 5 circuits, main circuit 2's complement
module _32_bit_multu (
  input  [31:0] B,
  input  [31:0] Q,
  output [31:0] B_2,
  output [31:0] Low,
  output [31:0] High
);

  wire [31:0] _1_a_2, _1_b_2, _1_q_2, _2_a_2, _2_b_2, _2_q_2, _3_a_2, _3_b_2, _3_q_2, _4_a_2, _4_b_2, _4_q_2,
       _5_a_2, _5_b_2, _5_q_2, _6_a_2, _6_b_2, _6_q_2, _7_a_2, _7_b_2, _7_q_2, _8_a_2, _8_b_2, _8_q_2,
       _9_a_2, _9_b_2, _9_q_2, _10_a_2, _10_b_2, _10_q_2, _11_a_2, _11_b_2, _11_q_2, _12_a_2, _12_b_2,
       _12_q_2, _13_a_2, _13_b_2, _13_q_2, _14_a_2, _14_b_2, _14_q_2, _15_a_2, _15_b_2, _15_q_2, _16_a_2,
       _16_b_2, _16_q_2, _17_a_2, _17_b_2, _17_q_2, _18_a_2, _18_b_2, _18_q_2, _19_a_2, _19_b_2, _19_q_2,
       _20_a_2, _20_b_2, _20_q_2, _21_a_2, _21_b_2, _21_q_2, _22_a_2, _22_b_2, _22_q_2, _23_a_2, _23_b_2,
       _23_q_2, _24_a_2, _24_b_2, _24_q_2, _25_a_2, _25_b_2, _25_q_2, _26_a_2, _26_b_2, _26_q_2, _27_a_2,
       _27_b_2, _27_q_2, _28_a_2, _28_b_2, _28_q_2, _29_a_2, _29_b_2, _29_q_2, _30_a_2, _30_b_2, _30_q_2,
       _31_a_2, _31_b_2, _31_q_2;

  multu_cycle _1 (.A({32{1'b0}}), .B(B), .Q(Q), .A_2(_1_a_2), .B_2(_1_b_2), .Q_2(_1_q_2));
  // Probe on _1_a_2
  // Probe on _1_q_2
  multu_cycle _2 (.A(_1_a_2), .B(_1_b_2), .Q(_1_q_2), .A_2(_2_a_2), .B_2(_2_b_2), .Q_2(_2_q_2));
  // Probe on _2_a_2
  // Probe on _2_q_2
  multu_cycle _3 (.A(_2_a_2), .B(_2_b_2), .Q(_2_q_2), .A_2(_3_a_2), .B_2(_3_b_2), .Q_2(_3_q_2));
  // Probe on _3_a_2
  // Probe on _3_q_2
  multu_cycle _4 (.A(_3_a_2), .B(_3_b_2), .Q(_3_q_2), .A_2(_4_a_2), .B_2(_4_b_2), .Q_2(_4_q_2));
  // Probe on _4_a_2
  // Probe on _4_q_2
  multu_cycle _5 (.A(_4_a_2), .B(_4_b_2), .Q(_4_q_2), .A_2(_5_a_2), .B_2(_5_b_2), .Q_2(_5_q_2));
  // Probe on _5_a_2
  // Probe on _5_q_2
  multu_cycle _6 (.A(_5_a_2), .B(_5_b_2), .Q(_5_q_2), .A_2(_6_a_2), .B_2(_6_b_2), .Q_2(_6_q_2));
  // Probe on _6_a_2
  // Probe on _6_q_2
  multu_cycle _7 (.A(_6_a_2), .B(_6_b_2), .Q(_6_q_2), .A_2(_7_a_2), .B_2(_7_b_2), .Q_2(_7_q_2));
  // Probe on _7_a_2
  // Probe on _7_q_2
  multu_cycle _8 (.A(_7_a_2), .B(_7_b_2), .Q(_7_q_2), .A_2(_8_a_2), .B_2(_8_b_2), .Q_2(_8_q_2));
  // Probe on _8_a_2
  // Probe on _8_q_2
  multu_cycle _9 (.A(_8_a_2), .B(_8_b_2), .Q(_8_q_2), .A_2(_9_a_2), .B_2(_9_b_2), .Q_2(_9_q_2));
  // Probe on _9_a_2
  // Probe on _9_q_2
  multu_cycle _10 (.A(_9_a_2), .B(_9_b_2), .Q(_9_q_2), .A_2(_10_a_2), .B_2(_10_b_2), .Q_2(_10_q_2));
  // Probe on _10_a_2
  // Probe on _10_q_2
  multu_cycle _11 (.A(_10_a_2), .B(_10_b_2), .Q(_10_q_2), .A_2(_11_a_2), .B_2(_11_b_2), .Q_2(_11_q_2));
  // Probe on _11_a_2
  // Probe on _11_q_2
  multu_cycle _12 (.A(_11_a_2), .B(_11_b_2), .Q(_11_q_2), .A_2(_12_a_2), .B_2(_12_b_2), .Q_2(_12_q_2));
  // Probe on _12_a_2
  // Probe on _12_q_2
  multu_cycle _13 (.A(_12_a_2), .B(_12_b_2), .Q(_12_q_2), .A_2(_13_a_2), .B_2(_13_b_2), .Q_2(_13_q_2));
  // Probe on _13_a_2
  // Probe on _13_q_2
  multu_cycle _14 (.A(_13_a_2), .B(_13_b_2), .Q(_13_q_2), .A_2(_14_a_2), .B_2(_14_b_2), .Q_2(_14_q_2));
  // Probe on _14_a_2
  // Probe on _14_q_2
  multu_cycle _15 (.A(_14_a_2), .B(_14_b_2), .Q(_14_q_2), .A_2(_15_a_2), .B_2(_15_b_2), .Q_2(_15_q_2));
  // Probe on _15_a_2
  // Probe on _15_q_2
  multu_cycle _16 (.A(_15_a_2), .B(_15_b_2), .Q(_15_q_2), .A_2(_16_a_2), .B_2(_16_b_2), .Q_2(_16_q_2));
  // Probe on _16_a_2
  // Probe on _16_q_2
  multu_cycle _17 (.A(_16_a_2), .B(_16_b_2), .Q(_16_q_2), .A_2(_17_a_2), .B_2(_17_b_2), .Q_2(_17_q_2));
  // Probe on _17_a_2
  // Probe on _17_q_2
  multu_cycle _18 (.A(_17_a_2), .B(_17_b_2), .Q(_17_q_2), .A_2(_18_a_2), .B_2(_18_b_2), .Q_2(_18_q_2));
  // Probe on _18_a_2
  // Probe on _18_q_2
  multu_cycle _19 (.A(_18_a_2), .B(_18_b_2), .Q(_18_q_2), .A_2(_19_a_2), .B_2(_19_b_2), .Q_2(_19_q_2));
  // Probe on _19_a_2
  // Probe on _19_q_2
  multu_cycle _20 (.A(_19_a_2), .B(_19_b_2), .Q(_19_q_2), .A_2(_20_a_2), .B_2(_20_b_2), .Q_2(_20_q_2));
  // Probe on _20_a_2
  // Probe on _20_q_2
  multu_cycle _21 (.A(_20_a_2), .B(_20_b_2), .Q(_20_q_2), .A_2(_21_a_2), .B_2(_21_b_2), .Q_2(_21_q_2));
  // Probe on _21_a_2
  // Probe on _21_q_2
  multu_cycle _22 (.A(_21_a_2), .B(_21_b_2), .Q(_21_q_2), .A_2(_22_a_2), .B_2(_22_b_2), .Q_2(_22_q_2));
  // Probe on _22_a_2
  // Probe on _22_q_2
  multu_cycle _23 (.A(_22_a_2), .B(_22_b_2), .Q(_22_q_2), .A_2(_23_a_2), .B_2(_23_b_2), .Q_2(_23_q_2));
  // Probe on _23_a_2
  // Probe on _23_q_2
  multu_cycle _24 (.A(_23_a_2), .B(_23_b_2), .Q(_23_q_2), .A_2(_24_a_2), .B_2(_24_b_2), .Q_2(_24_q_2));
  // Probe on _24_a_2
  // Probe on _24_q_2
  multu_cycle _25 (.A(_24_a_2), .B(_24_b_2), .Q(_24_q_2), .A_2(_25_a_2), .B_2(_25_b_2), .Q_2(_25_q_2));
  // Probe on _25_a_2
  // Probe on _25_q_2
  multu_cycle _26 (.A(_25_a_2), .B(_25_b_2), .Q(_25_q_2), .A_2(_26_a_2), .B_2(_26_b_2), .Q_2(_26_q_2));
  // Probe on _26_a_2
  // Probe on _26_q_2
  multu_cycle _27 (.A(_26_a_2), .B(_26_b_2), .Q(_26_q_2), .A_2(_27_a_2), .B_2(_27_b_2), .Q_2(_27_q_2));
  // Probe on _27_a_2
  // Probe on _27_q_2
  multu_cycle _28 (.A(_27_a_2), .B(_27_b_2), .Q(_27_q_2), .A_2(_28_a_2), .B_2(_28_b_2), .Q_2(_28_q_2));
  // Probe on _28_a_2
  // Probe on _28_q_2
  multu_cycle _29 (.A(_28_a_2), .B(_28_b_2), .Q(_28_q_2), .A_2(_29_a_2), .B_2(_29_b_2), .Q_2(_29_q_2));
  // Probe on _29_a_2
  // Probe on _29_q_2
  multu_cycle _30 (.A(_29_a_2), .B(_29_b_2), .Q(_29_q_2), .A_2(_30_a_2), .B_2(_30_b_2), .Q_2(_30_q_2));
  // Probe on _30_a_2
  // Probe on _30_q_2
  multu_cycle _31 (.A(_30_a_2), .B(_30_b_2), .Q(_30_q_2), .A_2(_31_a_2), .B_2(_31_b_2), .Q_2(_31_q_2));
  // Probe on _31_a_2
  // Probe on _31_q_2
  multu_cycle _32 (.A(_31_a_2), .B(_31_b_2), .Q(_31_q_2), .A_2(High), .B_2(B_2), .Q_2(Low));
  // Probe on High
  // Probe on Low

  // Other names for the same wires on the sheet: Aout[31:0] = High; Bin[31:0] = B; Bout[31:0] = B_2; Qin[31:0] = Q;
  //   Qout[31:0] = Low

  // Notes on the sheet:
  //   A=0
  //   Q es el low
  //   A es el High
endmodule

module multu_cycle (
  input  [31:0] A,
  input  [31:0] B,
  input  [31:0] Q,
  output [31:0] A_2,
  output [31:0] B_2,
  output [31:0] Q_2
);

  wire adder_1_cout, and_1_out;
  wire [31:0] adder_1_out, multiplexer_1_out;

  Adder #(.width(32)) adder_1 (.a(A), .b(B), .out(adder_1_out), .cin(1'b0), .cout(adder_1_cout));
  Multiplexer #(.width(32), .enable("false")) multiplexer_1 (
    .in0(A), .in1(adder_1_out), .out(multiplexer_1_out), .sel(Q[0]));
  and and_1 (and_1_out, adder_1_cout, Q[0]);
  _65_bit_shifter u_65_bit_shifter_1 (
    .Input32_0(multiplexer_1_out), .Input32_1(Q), ._65th_bit_In(and_1_out), .Output32_0(Q_2), .Output32_1(A_2));  // open: _65th_bit_Out

  assign B_2 = B;
endmodule

// >> 1
module _65_bit_shifter (
  input  [31:0] Input32_0,
  input  [31:0] Input32_1,
  input  _65th_bit_In,
  output [31:0] Output32_0,
  output [31:0] Output32_1,
  output _65th_bit_Out
);


  assign _65th_bit_Out = 1'b0;
  assign Output32_0 = {Input32_0[0], Input32_1[31:1]};
  assign Output32_1 = {_65th_bit_In, Input32_0[31:1]};
endmodule

// 0
module Zeros (
  input  [31:0] In,
  output Out
);

  nor nor_1 (Out, In[0], In[1], In[2], In[3], In[4], In[5], In[6], In[7], In[8], In[9], In[10], In[11], In[12], In[13], In[14], In[15], In[16], In[17], In[18], In[19], In[20], In[21], In[22], In[23], In[24], In[25], In[26], In[27], In[28], In[29], In[30], In[31]);

  // Notes on the sheet:
  //   Retorna 1 si todos son ceros
endmodule

// 2's
module _2_s_complement (
  input  [31:0] In,
  output [31:0] Out,
  output _2_s_Complement_Overflow
);

  wire adder_1_cout, not_2_out, zeros_1_out;
  wire [31:0] not_1_out;

  assign not_1_out = ~In;  // NOT_Gate not_1, 32 bits wide
  Zeros zeros_1 (.In(In), .Out(zeros_1_out));
  Adder #(.width(32)) adder_1 (.a(not_1_out), .b(32'h1), .out(Out), .cin(1'b0), .cout(adder_1_cout));
  not not_2 (not_2_out, zeros_1_out);
  and and_1 (_2_s_Complement_Overflow, adder_1_cout, not_2_out);
endmodule
