// Logisim project GatedLatch.circ as structural Verilog: 3 circuits, main circuit main
module main (
  input  Input,
  input  Write_Enable,
  output out_3
);

  wire and_1_out, and_2_out, not_1_out, not_2_out, or_1_out;

  not not_1 (not_1_out, Input);
  and and_1 (and_1_out, Input, Write_Enable);
  and and_2 (and_2_out, not_1_out, Write_Enable);
  or or_1 (or_1_out, out_3, and_1_out);
  not not_2 (not_2_out, and_2_out);
  and and_3 (out_3, or_1_out, not_2_out);

  // Notes on the sheet:
  //   Gated Latch
endmodule

module Memoria (
  input  [3:0] in_1,
  input  [3:0] in_2
);

  wire decoder_1_out0, main_1_out_3, main_2_out_3, main_3_out_3, main_4_out_3;

  Decoder #(.select(4)) decoder_1 (
    .out0(decoder_1_out0), .sel(in_2), .en(1'b1));  // open: out1, out2, out3, out4, out5, out6, out7, out8, out9, out10, out11, out12, out13, out14, out15
  main main_1 (.Input(in_1[3]), .Write_Enable(decoder_1_out0), .out_3(main_1_out_3));
  LED led_1 (.in(main_1_out_3));
  main main_2 (.Input(in_1[2]), .Write_Enable(decoder_1_out0), .out_3(main_2_out_3));
  main main_3 (.Input(in_1[1]), .Write_Enable(decoder_1_out0), .out_3(main_3_out_3));
  LED led_2 (.in(main_2_out_3));
  LED led_3 (.in(main_3_out_3));
  main main_4 (.Input(in_1[0]), .Write_Enable(decoder_1_out0), .out_3(main_4_out_3));
  LED led_4 (.in(main_4_out_3));
endmodule

module unidad_de_ram_4_bits (
);

  wire main_1_out_3, main_2_out_3, main_3_out_3, main_4_out_3, undriven;
  wire [3:0] undriven_2;

  main main_1 (.Input(undriven_2[3]), .Write_Enable(undriven), .out_3(main_1_out_3));
  main main_2 (.Input(undriven_2[2]), .Write_Enable(undriven), .out_3(main_2_out_3));
  LED led_1 (.in(main_1_out_3));
  LED led_2 (.in(main_2_out_3));
  main main_3 (.Input(undriven_2[1]), .Write_Enable(undriven), .out_3(main_3_out_3));
  LED led_3 (.in(main_3_out_3));
  main main_4 (.Input(undriven_2[0]), .Write_Enable(undriven), .out_3(main_4_out_3));
  LED led_4 (.in(main_4_out_3));
endmodule
