// Logisim project encoder.circ as structural Verilog: 1 circuit, main circuit main
module main (
  input  A,
  input  B,
  input  C,
  input  D,
  output O_0,
  output _0_1,
  output O_2
);

  or or_1 (O_0, A, C);
  or or_2 (_0_1, B, C);

  assign O_2 = D;
endmodule
