// Logisim project multiplex.circ as structural Verilog: 1 circuit, main circuit main
module main (
  input  B,
  input  D,
  input  A,
  output out_4
);

  wire and_1_out, and_2_out, not_1_out;

  not not_1 (not_1_out, D);
  and and_1 (and_1_out, B, D);
  and and_2 (and_2_out, not_1_out, A);
  or or_1 (out_4, and_1_out, and_2_out);
endmodule
