// Logisim project nots.circ as structural Verilog: 1 circuit, main circuit main
module main (
  input  _0,
  input  _1,
  input  _2,
  input  _3,
  input  _4,
  input  _5,
  input  _6,
  input  _7,
  output out_9,
  output out_10,
  output out_11,
  output out_12,
  output out_13,
  output out_14,
  output out_15,
  output out_16
);

  not not_1 (out_9, _0);
  not not_2 (out_10, _1);
  not not_3 (out_11, _2);
  not not_4 (out_12, _3);
  not not_5 (out_13, _4);
  not not_6 (out_14, _5);
  not not_7 (out_15, _6);
  not not_8 (out_16, _7);
endmodule
