// Logisim project Ram-Lab-davidcorzo.circ as structural Verilog
module main (
  input  Input,
  input  Write_Enable,
  output out
);

  wire and_1_out, and_2_out, not_1_out, not_2_out, or_1_out;

  not not_1 (not_1_out, Input);
  and and_1 (and_1_out, Input, Write_Enable);
  and and_2 (and_2_out, not_1_out, Write_Enable);
  or or_1 (or_1_out, out, and_1_out);
  not not_2 (not_2_out, and_2_out);
  and and_3 (out, or_1_out, not_2_out);

  // Notes on the sheet:
  //   Gated Latch
endmodule

module Memoria (
  input  [3:0] in_1,
  input  [3:0] in_2
);

  wire decoder_1_out0, main_1_out, main_2_out, main_3_out, main_4_out;

  Decoder #(.select(4)) decoder_1 (
    .out0(decoder_1_out0), .sel(in_2), .en(1'b1));  // open: out1, out2, out3, out4, out5, out6, out7, out8, out9, out10, out11, out12, out13, out14, out15
  main main_1 (.Input(in_1[3]), .Write_Enable(decoder_1_out0), .out(main_1_out));
  LED led_1 (.in(main_1_out));
  main main_2 (.Input(in_1[1]), .Write_Enable(decoder_1_out0), .out(main_2_out));
  main main_3 (.Input(in_1[2]), .Write_Enable(decoder_1_out0), .out(main_3_out));
  LED led_2 (.in(main_3_out));
  LED led_3 (.in(main_2_out));
  main main_4 (.Input(in_1[0]), .Write_Enable(decoder_1_out0), .out(main_4_out));
  LED led_4 (.in(main_4_out));
endmodule

module unidad_de_un_byte (
  input  [7:0] _8_bit_in,
  input  WriteEnable,
  output [7:0] _8_bit_out
);

  main main_1 (.Input(_8_bit_in[6]), .Write_Enable(WriteEnable), .out(_8_bit_out[6]));
  main main_2 (.Input(_8_bit_in[7]), .Write_Enable(WriteEnable), .out(_8_bit_out[7]));
  main main_3 (.Input(_8_bit_in[5]), .Write_Enable(WriteEnable), .out(_8_bit_out[5]));
  main main_4 (.Input(_8_bit_in[4]), .Write_Enable(WriteEnable), .out(_8_bit_out[4]));
  main main_5 (.Input(_8_bit_in[3]), .Write_Enable(WriteEnable), .out(_8_bit_out[3]));
  main main_6 (.Input(_8_bit_in[2]), .Write_Enable(WriteEnable), .out(_8_bit_out[2]));
  main main_7 (.Input(_8_bit_in[1]), .Write_Enable(WriteEnable), .out(_8_bit_out[1]));
  main main_8 (.Input(_8_bit_in[0]), .Write_Enable(WriteEnable), .out(_8_bit_out[0]));

  // Notes on the sheet:
  //   WriteEnable: pull=up
endmodule

module ram (
  input  RE,
  input  [7:0] Input,
  input  WE,
  input  [4:0] Puntero,
  output [7:0] out_5
);

  wire decoder_1_out0, decoder_1_out1, decoder_1_out2, decoder_1_out3, decoder_1_out4, decoder_1_out5,
       decoder_1_out6, decoder_1_out7, decoder_1_out8, decoder_1_out9, decoder_1_out10, decoder_1_out11,
       decoder_1_out12, decoder_1_out13, decoder_1_out14, decoder_1_out15, decoder_1_out16, decoder_1_out17,
       decoder_1_out18, decoder_1_out19, decoder_1_out20, decoder_1_out21, decoder_1_out22, decoder_1_out23,
       decoder_1_out24, decoder_1_out25, decoder_1_out26, decoder_1_out27, decoder_1_out28, decoder_1_out29,
       decoder_1_out30, decoder_1_out31;
  wire [7:0] _0__8_bit_out, _1__8_bit_out, _2__8_bit_out, _3__8_bit_out, _4__8_bit_out, _5__8_bit_out,
       _6__8_bit_out, _7__8_bit_out, _8__8_bit_out, _9__8_bit_out, _10__8_bit_out, _11__8_bit_out,
       _12__8_bit_out, _13__8_bit_out, _14__8_bit_out, _15__8_bit_out, _16__8_bit_out, _17__8_bit_out,
       _18__8_bit_out, _19__8_bit_out, _20__8_bit_out, _21__8_bit_out, _22__8_bit_out, _23__8_bit_out,
       _24__8_bit_out, _25__8_bit_out, _26__8_bit_out, _27__8_bit_out, _28__8_bit_out, _29__8_bit_out,
       _30__8_bit_out, _31__8_bit_out;

  Decoder #(.select(5), .disabled(0)) decoder_1 (
    .out0(decoder_1_out0), .out1(decoder_1_out1), .out2(decoder_1_out2), .out3(decoder_1_out3),
    .out4(decoder_1_out4), .out5(decoder_1_out5), .out6(decoder_1_out6), .out7(decoder_1_out7),
    .out8(decoder_1_out8), .out9(decoder_1_out9), .out10(decoder_1_out10), .out11(decoder_1_out11),
    .out12(decoder_1_out12), .out13(decoder_1_out13), .out14(decoder_1_out14), .out15(decoder_1_out15),
    .out16(decoder_1_out16), .out17(decoder_1_out17), .out18(decoder_1_out18), .out19(decoder_1_out19),
    .out20(decoder_1_out20), .out21(decoder_1_out21), .out22(decoder_1_out22), .out23(decoder_1_out23),
    .out24(decoder_1_out24), .out25(decoder_1_out25), .out26(decoder_1_out26), .out27(decoder_1_out27),
    .out28(decoder_1_out28), .out29(decoder_1_out29), .out30(decoder_1_out30), .out31(decoder_1_out31),
    .sel(Puntero), .en(WE));
  unidad_de_un_byte _0 (._8_bit_in(Input), .WriteEnable(decoder_1_out0), ._8_bit_out(_0__8_bit_out));
  unidad_de_un_byte _1 (._8_bit_in(Input), .WriteEnable(decoder_1_out1), ._8_bit_out(_1__8_bit_out));
  unidad_de_un_byte _2 (._8_bit_in(Input), .WriteEnable(decoder_1_out2), ._8_bit_out(_2__8_bit_out));
  unidad_de_un_byte _3 (._8_bit_in(Input), .WriteEnable(decoder_1_out3), ._8_bit_out(_3__8_bit_out));
  unidad_de_un_byte _4 (._8_bit_in(Input), .WriteEnable(decoder_1_out4), ._8_bit_out(_4__8_bit_out));
  unidad_de_un_byte _5 (._8_bit_in(Input), .WriteEnable(decoder_1_out5), ._8_bit_out(_5__8_bit_out));
  unidad_de_un_byte _6 (._8_bit_in(Input), .WriteEnable(decoder_1_out6), ._8_bit_out(_6__8_bit_out));
  unidad_de_un_byte _7 (._8_bit_in(Input), .WriteEnable(decoder_1_out7), ._8_bit_out(_7__8_bit_out));
  unidad_de_un_byte _8 (._8_bit_in(Input), .WriteEnable(decoder_1_out8), ._8_bit_out(_8__8_bit_out));
  unidad_de_un_byte _9 (._8_bit_in(Input), .WriteEnable(decoder_1_out9), ._8_bit_out(_9__8_bit_out));
  unidad_de_un_byte _10 (._8_bit_in(Input), .WriteEnable(decoder_1_out10), ._8_bit_out(_10__8_bit_out));
  unidad_de_un_byte _11 (._8_bit_in(Input), .WriteEnable(decoder_1_out11), ._8_bit_out(_11__8_bit_out));
  unidad_de_un_byte _12 (._8_bit_in(Input), .WriteEnable(decoder_1_out12), ._8_bit_out(_12__8_bit_out));
  unidad_de_un_byte _13 (._8_bit_in(Input), .WriteEnable(decoder_1_out13), ._8_bit_out(_13__8_bit_out));
  unidad_de_un_byte _14 (._8_bit_in(Input), .WriteEnable(decoder_1_out14), ._8_bit_out(_14__8_bit_out));
  unidad_de_un_byte _15 (._8_bit_in(Input), .WriteEnable(decoder_1_out15), ._8_bit_out(_15__8_bit_out));
  unidad_de_un_byte _16 (._8_bit_in(Input), .WriteEnable(decoder_1_out16), ._8_bit_out(_16__8_bit_out));
  unidad_de_un_byte _17 (._8_bit_in(Input), .WriteEnable(decoder_1_out17), ._8_bit_out(_17__8_bit_out));
  unidad_de_un_byte _18 (._8_bit_in(Input), .WriteEnable(decoder_1_out18), ._8_bit_out(_18__8_bit_out));
  unidad_de_un_byte _19 (._8_bit_in(Input), .WriteEnable(decoder_1_out19), ._8_bit_out(_19__8_bit_out));
  unidad_de_un_byte _20 (._8_bit_in(Input), .WriteEnable(decoder_1_out20), ._8_bit_out(_20__8_bit_out));
  unidad_de_un_byte _21 (._8_bit_in(Input), .WriteEnable(decoder_1_out21), ._8_bit_out(_21__8_bit_out));
  unidad_de_un_byte _22 (._8_bit_in(Input), .WriteEnable(decoder_1_out22), ._8_bit_out(_22__8_bit_out));
  unidad_de_un_byte _23 (._8_bit_in(Input), .WriteEnable(decoder_1_out23), ._8_bit_out(_23__8_bit_out));
  unidad_de_un_byte _24 (._8_bit_in(Input), .WriteEnable(decoder_1_out24), ._8_bit_out(_24__8_bit_out));
  unidad_de_un_byte _25 (._8_bit_in(Input), .WriteEnable(decoder_1_out25), ._8_bit_out(_25__8_bit_out));
  unidad_de_un_byte _26 (._8_bit_in(Input), .WriteEnable(decoder_1_out26), ._8_bit_out(_26__8_bit_out));
  unidad_de_un_byte _27 (._8_bit_in(Input), .WriteEnable(decoder_1_out27), ._8_bit_out(_27__8_bit_out));
  unidad_de_un_byte _28 (._8_bit_in(Input), .WriteEnable(decoder_1_out28), ._8_bit_out(_28__8_bit_out));
  unidad_de_un_byte _29 (._8_bit_in(Input), .WriteEnable(decoder_1_out29), ._8_bit_out(_29__8_bit_out));
  unidad_de_un_byte _30 (._8_bit_in(Input), .WriteEnable(decoder_1_out30), ._8_bit_out(_30__8_bit_out));
  unidad_de_un_byte _31 (._8_bit_in(Input), .WriteEnable(decoder_1_out31), ._8_bit_out(_31__8_bit_out));
  Multiplexer #(.select(5), .width(8)) multiplexer_1 (
    .in0(_0__8_bit_out), .in1(_1__8_bit_out), .in2(_2__8_bit_out), .in3(_3__8_bit_out), .in4(_4__8_bit_out),
    .in5(_5__8_bit_out), .in6(_6__8_bit_out), .in7(_7__8_bit_out), .in8(_8__8_bit_out), .in9(_9__8_bit_out),
    .in10(_10__8_bit_out), .in11(_11__8_bit_out), .in12(_12__8_bit_out), .in13(_13__8_bit_out),
    .in14(_14__8_bit_out), .in15(_15__8_bit_out), .in16(_16__8_bit_out), .in17(_17__8_bit_out),
    .in18(_18__8_bit_out), .in19(_19__8_bit_out), .in20(_20__8_bit_out), .in21(_21__8_bit_out),
    .in22(_22__8_bit_out), .in23(_23__8_bit_out), .in24(_24__8_bit_out), .in25(_25__8_bit_out),
    .in26(_26__8_bit_out), .in27(_27__8_bit_out), .in28(_28__8_bit_out), .in29(_29__8_bit_out),
    .in30(_30__8_bit_out), .in31(_31__8_bit_out), .out(out_5), .sel(Puntero), .en(RE));
  // Probe on _0__8_bit_out
  // Probe on _1__8_bit_out
  // Probe on _2__8_bit_out
  // Probe on _3__8_bit_out
  // Probe on _4__8_bit_out
  // Probe on _5__8_bit_out
  // Probe on _6__8_bit_out
  // Probe on _7__8_bit_out
  // Probe on _8__8_bit_out
  // Probe on _9__8_bit_out
  // Probe on _10__8_bit_out
  // Probe on _11__8_bit_out
  // Probe on _12__8_bit_out
  // Probe on _13__8_bit_out
  // Probe on _14__8_bit_out
  // Probe on _15__8_bit_out
  // Probe on _16__8_bit_out
  // Probe on _17__8_bit_out
  // Probe on _18__8_bit_out
  // Probe on _19__8_bit_out
  // Probe on _20__8_bit_out
  // Probe on _21__8_bit_out
  // Probe on _22__8_bit_out
  // Probe on _23__8_bit_out
  // Probe on _24__8_bit_out
  // Probe on _25__8_bit_out
  // Probe on _26__8_bit_out
  // Probe on _27__8_bit_out
  // Probe on _28__8_bit_out
  // Probe on _29__8_bit_out
  // Probe on _30__8_bit_out
  // Probe on _31__8_bit_out
endmodule
