// Logisim project Registros-DavidCorzo.circ as structural Verilog: 6 circuits, main circuit main
module main (
  input  Input,
  input  Write_Enable,
  output out_3
);

  wire and_1_out, and_2_out, not_1_out, not_2_out, or_1_out;

  not not_1 (not_1_out, Input);
  and and_1 (and_1_out, Input, Write_Enable);
  and and_2 (and_2_out, not_1_out, Write_Enable);
  or or_1 (or_1_out, out_3, and_1_out);
  not not_2 (not_2_out, and_2_out);
  and and_3 (out_3, or_1_out, not_2_out);

  // Notes on the sheet:
  //   Gated Latch
endmodule

module Memoria (
  input  [3:0] in_1,
  input  [3:0] in_2
);

  wire decoder_1_out0, main_1_out_3, main_2_out_3, main_3_out_3, main_4_out_3;

  Decoder #(.select(4)) decoder_1 (
    .out0(decoder_1_out0), .sel(in_2), .en(1'b1));  // open: out1, out2, out3, out4, out5, out6, out7, out8, out9, out10, out11, out12, out13, out14, out15
  main main_1 (.Input(in_1[3]), .Write_Enable(decoder_1_out0), .out_3(main_1_out_3));
  LED led_1 (.in(main_1_out_3));
  main main_2 (.Input(in_1[2]), .Write_Enable(decoder_1_out0), .out_3(main_2_out_3));
  main main_3 (.Input(in_1[1]), .Write_Enable(decoder_1_out0), .out_3(main_3_out_3));
  LED led_2 (.in(main_2_out_3));
  LED led_3 (.in(main_3_out_3));
  main main_4 (.Input(in_1[0]), .Write_Enable(decoder_1_out0), .out_3(main_4_out_3));
  LED led_4 (.in(main_4_out_3));
endmodule

module unidad_de_ram_4_bits (
);

  wire main_1_out_3, main_2_out_3, main_3_out_3, main_4_out_3, undriven;
  wire [3:0] undriven_2;

  main main_1 (.Input(undriven_2[2]), .Write_Enable(undriven), .out_3(main_1_out_3));
  main main_2 (.Input(undriven_2[3]), .Write_Enable(undriven), .out_3(main_2_out_3));
  LED led_1 (.in(main_2_out_3));
  LED led_2 (.in(main_1_out_3));
  main main_3 (.Input(undriven_2[1]), .Write_Enable(undriven), .out_3(main_3_out_3));
  LED led_3 (.in(main_3_out_3));
  main main_4 (.Input(undriven_2[0]), .Write_Enable(undriven), .out_3(main_4_out_3));
  LED led_4 (.in(main_4_out_3));
endmodule

module Register_file (
  input  [3:0] in_1,
  input  [1:0] in_2,
  output [3:0] out_3,
  output [3:0] out_4,
  output [3:0] out_5,
  output [3:0] out_6
);

  wire clock_1_out, decoder_1_out0, decoder_1_out1, decoder_1_out2, decoder_1_out3;

  Clock clock_1 (.out(clock_1_out));
  Decoder #(.select(2), .enable("false")) decoder_1 (
    .out0(decoder_1_out0), .out1(decoder_1_out1), .out2(decoder_1_out2), .out3(decoder_1_out3), .sel(in_2));
  _4_bit_register u_4_bit_register_1 (.D(in_1), .WE(decoder_1_out0), .Clock(clock_1_out), .Q(out_3));  // open: nQ
  _4_bit_register u_4_bit_register_2 (.D(in_1), .WE(decoder_1_out1), .Clock(clock_1_out), .Q(out_4));  // open: nQ
  _4_bit_register u_4_bit_register_3 (.D(in_1), .WE(decoder_1_out2), .Clock(clock_1_out), .Q(out_5));  // open: nQ
  _4_bit_register u_4_bit_register_4 (.D(in_1), .WE(decoder_1_out3), .Clock(clock_1_out), .Q(out_6));  // open: nQ
endmodule

module FlipFlop_D (
  input  D,
  input  Clock,
  input  WE,
  output Q,
  output nQ
);

  wire and_1_out, nand_1_out, nand_2_out, not_1_out;

  not not_1 (not_1_out, D);
  and and_1 (and_1_out, Clock, WE);
  nand nand_1 (nand_1_out, D, and_1_out);
  nand nand_2 (nand_2_out, and_1_out, not_1_out);
  nand nand_3 (Q, nand_1_out, nQ);
  nand nand_4 (nQ, Q, nand_2_out);
endmodule

module _4_bit_register (
  input  [3:0] D,
  input  WE,
  input  Clock,
  output [3:0] Q,
  output [3:0] nQ
);

  FlipFlop_D flipflop_d_1 (.D(D[3]), .Clock(Clock), .WE(WE), .Q(Q[3]), .nQ(nQ[3]));
  FlipFlop_D flipflop_d_2 (.D(D[1]), .Clock(Clock), .WE(WE), .Q(Q[1]), .nQ(nQ[1]));
  FlipFlop_D flipflop_d_3 (.D(D[2]), .Clock(Clock), .WE(WE), .Q(Q[2]), .nQ(nQ[2]));
  FlipFlop_D flipflop_d_4 (.D(D[0]), .Clock(Clock), .WE(WE), .Q(Q[0]), .nQ(nQ[0]));
endmodule
