// Logisim project lab3-registros-Anesveth.circ as structural Verilog: 3 circuits, main circuit Register File (RF)
module Register_File__RF (
  input  in_1,
  input  [1:0] in_2,
  input  [3:0] in_3,
  output [3:0] out_4,
  output [3:0] out_5,
  output [3:0] out_6,
  output [3:0] out_7
);

  wire clock_1_out, decoder_1_out0, decoder_1_out1, decoder_1_out2, decoder_1_out3;

  Clock clock_1 (.out(clock_1_out));
  registro_de_4_bits registro_de_4_bits_1 (
    .D(in_3), .WE(decoder_1_out0), .Reloj(clock_1_out), .Qs(out_4));  // open: nQs
  Decoder #(.select(2)) decoder_1 (
    .out0(decoder_1_out0), .out1(decoder_1_out1), .out2(decoder_1_out2), .out3(decoder_1_out3), .sel(in_2),
    .en(in_1));
  registro_de_4_bits registro_de_4_bits_2 (
    .D(in_3), .WE(decoder_1_out1), .Reloj(clock_1_out), .Qs(out_5));  // open: nQs
  registro_de_4_bits registro_de_4_bits_3 (
    .D(in_3), .WE(decoder_1_out2), .Reloj(clock_1_out), .Qs(out_6));  // open: nQs
  registro_de_4_bits registro_de_4_bits_4 (
    .D(in_3), .WE(decoder_1_out3), .Reloj(clock_1_out), .Qs(out_7));  // open: nQs
endmodule

module flipflop (
  input  Bit_de_entrada,
  input  Reloj,
  input  WE,
  output Q,
  output nQ
);

  wire and_1_out, nand_1_out, nand_2_out, not_1_out;

  and and_1 (and_1_out, Reloj, WE);
  not not_1 (not_1_out, Bit_de_entrada);
  nand nand_1 (nand_1_out, Bit_de_entrada, and_1_out);
  nand nand_2 (nand_2_out, and_1_out, not_1_out);
  nand nand_3 (Q, nand_1_out, nQ);
  nand nand_4 (nQ, Q, nand_2_out);
endmodule

module registro_de_4_bits (
  input  [3:0] D,
  input  WE,
  input  Reloj,
  output [3:0] nQs,
  output [3:0] Qs
);

  flipflop flipflop_1 (.Bit_de_entrada(D[3]), .Reloj(Reloj), .WE(WE), .Q(Qs[3]), .nQ(nQs[3]));
  flipflop flipflop_2 (.Bit_de_entrada(D[2]), .Reloj(Reloj), .WE(WE), .Q(Qs[2]), .nQ(nQs[2]));
  flipflop flipflop_3 (.Bit_de_entrada(D[1]), .Reloj(Reloj), .WE(WE), .Q(Qs[1]), .nQ(nQs[1]));
  flipflop flipflop_4 (.Bit_de_entrada(D[0]), .Reloj(Reloj), .WE(WE), .Q(Qs[0]), .nQ(nQs[0]));
endmodule
