// Logisim project Aricmetica.circ as structural Verilog: 6 circuits, main circuit Multiplicador
module Multiplicador (
  input  [31:0] in_1,
  input  [31:0] in_2,
  output Overflow,
  output [31:0] out_4
);

  wire adder_1_cout, adder_2_cout, adder_3_cout, adder_4_cout, adder_5_cout, adder_6_cout, adder_7_cout,
       adder_8_cout, adder_9_cout, adder_10_cout, adder_11_cout, adder_12_cout, adder_13_cout, adder_14_cout,
       adder_15_cout, adder_16_cout, adder_17_cout, adder_18_cout, adder_19_cout, adder_20_cout,
       adder_21_cout, adder_22_cout, adder_23_cout, adder_24_cout, adder_25_cout, adder_26_cout,
       adder_27_cout, adder_28_cout, adder_29_cout, adder_30_cout, adder_31_cout, bitselector_1_out,
       bitselector_2_out, bitselector_3_out, bitselector_4_out, bitselector_5_out, bitselector_6_out,
       bitselector_7_out, bitselector_8_out, bitselector_9_out, bitselector_10_out, bitselector_11_out,
       bitselector_12_out, bitselector_13_out, bitselector_14_out, bitselector_15_out, bitselector_16_out,
       bitselector_17_out, bitselector_18_out, bitselector_19_out, bitselector_20_out, bitselector_21_out,
       bitselector_22_out, bitselector_23_out, bitselector_24_out, bitselector_25_out, bitselector_26_out,
       bitselector_27_out, bitselector_28_out, bitselector_29_out, bitselector_30_out, bitselector_31_out,
       bitselector_32_out, or_1_out, or_3_out;
  wire [4:0] controlled_buffer_1_out, controlled_buffer_2_out, controlled_buffer_3_out,
       controlled_buffer_4_out, controlled_buffer_5_out, controlled_buffer_6_out, controlled_buffer_7_out,
       controlled_buffer_8_out, controlled_buffer_9_out, controlled_buffer_10_out, controlled_buffer_11_out,
       controlled_buffer_12_out, controlled_buffer_13_out, controlled_buffer_14_out,
       controlled_buffer_15_out, controlled_buffer_16_out, controlled_buffer_17_out,
       controlled_buffer_18_out, controlled_buffer_19_out, controlled_buffer_20_out,
       controlled_buffer_21_out, controlled_buffer_22_out, controlled_buffer_23_out,
       controlled_buffer_24_out, controlled_buffer_25_out, controlled_buffer_26_out,
       controlled_buffer_27_out, controlled_buffer_28_out, controlled_buffer_29_out,
       controlled_buffer_30_out, controlled_buffer_31_out, controlled_buffer_32_out;
  wire [31:0] adder_1_out, adder_2_out, adder_3_out, adder_4_out, adder_5_out, adder_6_out, adder_7_out,
       adder_8_out, adder_9_out, adder_10_out, adder_11_out, adder_12_out, adder_13_out, adder_14_out,
       adder_15_out, adder_16_out, adder_17_out, adder_18_out, adder_19_out, adder_20_out, adder_21_out,
       adder_22_out, adder_23_out, adder_24_out, adder_25_out, adder_26_out, adder_27_out, adder_28_out,
       adder_29_out, adder_30_out, forczero_1_out, forczero_2_out, forczero_3_out, forczero_4_out,
       forczero_5_out, forczero_6_out, forczero_7_out, forczero_8_out, forczero_9_out, forczero_10_out,
       forczero_11_out, forczero_12_out, forczero_13_out, forczero_14_out, forczero_15_out, forczero_16_out,
       forczero_17_out, forczero_18_out, forczero_19_out, forczero_20_out, forczero_21_out, forczero_22_out,
       forczero_23_out, forczero_24_out, forczero_25_out, forczero_26_out, forczero_27_out, forczero_28_out,
       forczero_29_out, forczero_30_out, forczero_31_out, forczero_32_out, shifter_1_out, shifter_2_out,
       shifter_3_out, shifter_4_out, shifter_5_out, shifter_6_out, shifter_7_out, shifter_8_out,
       shifter_9_out, shifter_10_out, shifter_11_out, shifter_12_out, shifter_13_out, shifter_14_out,
       shifter_15_out, shifter_16_out, shifter_17_out, shifter_18_out, shifter_19_out, shifter_20_out,
       shifter_21_out, shifter_22_out, shifter_23_out, shifter_24_out, shifter_25_out, shifter_26_out,
       shifter_27_out, shifter_28_out, shifter_29_out, shifter_30_out, shifter_31_out, shifter_32_out;

  BitSelector #(.width(32)) bitselector_1 (.in(in_2), .out(bitselector_1_out), .sel({5{1'b0}}));
  assign controlled_buffer_1_out = bitselector_1_out ? {5{1'b0}} : 5'bz;  // Controlled_Buffer controlled_buffer_1
  BitSelector #(.width(32)) bitselector_2 (.in(in_2), .out(bitselector_2_out), .sel(5'b00001));
  assign controlled_buffer_2_out = bitselector_2_out ? 5'b00001 : 5'bz;  // Controlled_Buffer controlled_buffer_2
  BitSelector #(.width(32)) bitselector_3 (.in(in_2), .out(bitselector_3_out), .sel(5'b00010));
  assign controlled_buffer_3_out = bitselector_3_out ? 5'b00010 : 5'bz;  // Controlled_Buffer controlled_buffer_3
  BitSelector #(.width(32)) bitselector_4 (.in(in_2), .out(bitselector_4_out), .sel(5'b00011));
  assign controlled_buffer_4_out = bitselector_4_out ? 5'b00011 : 5'bz;  // Controlled_Buffer controlled_buffer_4
  BitSelector #(.width(32)) bitselector_5 (.in(in_2), .out(bitselector_5_out), .sel(5'b00100));
  assign controlled_buffer_5_out = bitselector_5_out ? 5'b00100 : 5'bz;  // Controlled_Buffer controlled_buffer_5
  BitSelector #(.width(32)) bitselector_6 (.in(in_2), .out(bitselector_6_out), .sel(5'b00101));
  assign controlled_buffer_6_out = bitselector_6_out ? 5'b00101 : 5'bz;  // Controlled_Buffer controlled_buffer_6
  BitSelector #(.width(32)) bitselector_7 (.in(in_2), .out(bitselector_7_out), .sel(5'b00110));
  assign controlled_buffer_7_out = bitselector_7_out ? 5'b00110 : 5'bz;  // Controlled_Buffer controlled_buffer_7
  BitSelector #(.width(32)) bitselector_8 (.in(in_2), .out(bitselector_8_out), .sel(5'b00111));
  assign controlled_buffer_8_out = bitselector_8_out ? 5'b00111 : 5'bz;  // Controlled_Buffer controlled_buffer_8
  BitSelector #(.width(32)) bitselector_9 (.in(in_2), .out(bitselector_9_out), .sel(5'b01000));
  assign controlled_buffer_9_out = bitselector_9_out ? 5'b01000 : 5'bz;  // Controlled_Buffer controlled_buffer_9
  BitSelector #(.width(32)) bitselector_10 (.in(in_2), .out(bitselector_10_out), .sel(5'b01001));
  assign controlled_buffer_10_out = bitselector_10_out ? 5'b01001 : 5'bz;  // Controlled_Buffer controlled_buffer_10
  BitSelector #(.width(32)) bitselector_11 (.in(in_2), .out(bitselector_11_out), .sel(5'b10000));
  assign controlled_buffer_11_out = bitselector_11_out ? 5'b10000 : 5'bz;  // Controlled_Buffer controlled_buffer_11
  BitSelector #(.width(32)) bitselector_12 (.in(in_2), .out(bitselector_12_out), .sel(5'b01011));
  assign controlled_buffer_12_out = bitselector_12_out ? 5'b01011 : 5'bz;  // Controlled_Buffer controlled_buffer_12
  BitSelector #(.width(32)) bitselector_13 (.in(in_2), .out(bitselector_13_out), .sel(5'b01100));
  assign controlled_buffer_13_out = bitselector_13_out ? 5'b01100 : 5'bz;  // Controlled_Buffer controlled_buffer_13
  BitSelector #(.width(32)) bitselector_14 (.in(in_2), .out(bitselector_14_out), .sel(5'b10011));
  assign controlled_buffer_14_out = bitselector_14_out ? 5'b10011 : 5'bz;  // Controlled_Buffer controlled_buffer_14
  BitSelector #(.width(32)) bitselector_15 (.in(in_2), .out(bitselector_15_out), .sel(5'b01110));
  assign controlled_buffer_15_out = bitselector_15_out ? 5'b01110 : 5'bz;  // Controlled_Buffer controlled_buffer_15
  BitSelector #(.width(32)) bitselector_16 (.in(in_2), .out(bitselector_16_out), .sel(5'b01111));
  assign controlled_buffer_16_out = bitselector_16_out ? 5'b01111 : 5'bz;  // Controlled_Buffer controlled_buffer_16
  Shifter #(.width(32)) shifter_1 (.in(in_1), .\dist (controlled_buffer_1_out), .out(shifter_1_out));
  Shifter #(.width(32)) shifter_2 (.in(in_1), .\dist (controlled_buffer_2_out), .out(shifter_2_out));
  Shifter #(.width(32)) shifter_3 (.in(in_1), .\dist (controlled_buffer_3_out), .out(shifter_3_out));
  Shifter #(.width(32)) shifter_4 (.in(in_1), .\dist (controlled_buffer_4_out), .out(shifter_4_out));
  Shifter #(.width(32)) shifter_5 (.in(in_1), .\dist (controlled_buffer_5_out), .out(shifter_5_out));
  Shifter #(.width(32)) shifter_6 (.in(in_1), .\dist (controlled_buffer_6_out), .out(shifter_6_out));
  Shifter #(.width(32)) shifter_7 (.in(in_1), .\dist (controlled_buffer_7_out), .out(shifter_7_out));
  Shifter #(.width(32)) shifter_8 (.in(in_1), .\dist (controlled_buffer_8_out), .out(shifter_8_out));
  Shifter #(.width(32)) shifter_9 (.in(in_1), .\dist (controlled_buffer_9_out), .out(shifter_9_out));
  Shifter #(.width(32)) shifter_10 (.in(in_1), .\dist (controlled_buffer_10_out), .out(shifter_10_out));
  Shifter #(.width(32)) shifter_11 (.in(in_1), .\dist (controlled_buffer_11_out), .out(shifter_11_out));
  Shifter #(.width(32)) shifter_12 (.in(in_1), .\dist (controlled_buffer_12_out), .out(shifter_12_out));
  Shifter #(.width(32)) shifter_13 (.in(in_1), .\dist (controlled_buffer_13_out), .out(shifter_13_out));
  Shifter #(.width(32)) shifter_14 (.in(in_1), .\dist (controlled_buffer_14_out), .out(shifter_14_out));
  Shifter #(.width(32)) shifter_15 (.in(in_1), .\dist (controlled_buffer_15_out), .out(shifter_15_out));
  Shifter #(.width(32)) shifter_16 (.in(in_1), .\dist (controlled_buffer_16_out), .out(shifter_16_out));
  ForcZero forczero_1 (.Input(shifter_1_out), .Out(forczero_1_out), .Enabler(bitselector_1_out));
  ForcZero forczero_2 (.Input(shifter_2_out), .Out(forczero_2_out), .Enabler(bitselector_2_out));
  ForcZero forczero_3 (.Input(shifter_3_out), .Out(forczero_3_out), .Enabler(bitselector_3_out));
  ForcZero forczero_4 (.Input(shifter_4_out), .Out(forczero_4_out), .Enabler(bitselector_4_out));
  ForcZero forczero_5 (.Input(shifter_5_out), .Out(forczero_5_out), .Enabler(bitselector_5_out));
  ForcZero forczero_6 (.Input(shifter_6_out), .Out(forczero_6_out), .Enabler(bitselector_6_out));
  ForcZero forczero_7 (.Input(shifter_7_out), .Out(forczero_7_out), .Enabler(bitselector_7_out));
  ForcZero forczero_8 (.Input(shifter_8_out), .Out(forczero_8_out), .Enabler(bitselector_8_out));
  ForcZero forczero_9 (.Input(shifter_9_out), .Out(forczero_9_out), .Enabler(bitselector_9_out));
  ForcZero forczero_10 (.Input(shifter_10_out), .Out(forczero_10_out), .Enabler(bitselector_10_out));
  ForcZero forczero_11 (.Input(shifter_11_out), .Out(forczero_11_out), .Enabler(bitselector_11_out));
  ForcZero forczero_12 (.Input(shifter_12_out), .Out(forczero_12_out), .Enabler(bitselector_12_out));
  ForcZero forczero_13 (.Input(shifter_13_out), .Out(forczero_13_out), .Enabler(bitselector_13_out));
  ForcZero forczero_14 (.Input(shifter_14_out), .Out(forczero_14_out), .Enabler(bitselector_14_out));
  ForcZero forczero_15 (.Input(shifter_15_out), .Out(forczero_15_out), .Enabler(bitselector_15_out));
  ForcZero forczero_16 (.Input(shifter_16_out), .Out(forczero_16_out), .Enabler(bitselector_16_out));
  Adder #(.width(32)) adder_1 (
    .a(forczero_1_out), .b(forczero_2_out), .out(adder_1_out), .cout(adder_1_cout));  // open: cin
  Adder #(.width(32)) adder_2 (
    .a(adder_1_out), .b(forczero_3_out), .out(adder_2_out), .cout(adder_2_cout));  // open: cin
  Adder #(.width(32)) adder_3 (
    .a(adder_2_out), .b(forczero_4_out), .out(adder_3_out), .cout(adder_3_cout));  // open: cin
  Adder #(.width(32)) adder_4 (
    .a(adder_3_out), .b(forczero_5_out), .out(adder_4_out), .cout(adder_4_cout));  // open: cin
  Adder #(.width(32)) adder_5 (
    .a(adder_4_out), .b(forczero_6_out), .out(adder_5_out), .cout(adder_5_cout));  // open: cin
  Adder #(.width(32)) adder_6 (
    .a(adder_5_out), .b(forczero_7_out), .out(adder_6_out), .cout(adder_6_cout));  // open: cin
  Adder #(.width(32)) adder_7 (
    .a(adder_6_out), .b(forczero_8_out), .out(adder_7_out), .cout(adder_7_cout));  // open: cin
  Adder #(.width(32)) adder_8 (
    .a(adder_7_out), .b(forczero_9_out), .out(adder_8_out), .cout(adder_8_cout));  // open: cin
  Adder #(.width(32)) adder_9 (
    .a(adder_8_out), .b(forczero_10_out), .out(adder_9_out), .cout(adder_9_cout));  // open: cin
  Adder #(.width(32)) adder_10 (
    .a(adder_9_out), .b(forczero_11_out), .out(adder_10_out), .cout(adder_10_cout));  // open: cin
  Adder #(.width(32)) adder_11 (
    .a(adder_10_out), .b(forczero_12_out), .out(adder_11_out), .cout(adder_11_cout));  // open: cin
  Adder #(.width(32)) adder_12 (
    .a(adder_11_out), .b(forczero_13_out), .out(adder_12_out), .cout(adder_12_cout));  // open: cin
  Adder #(.width(32)) adder_13 (
    .a(adder_12_out), .b(forczero_14_out), .out(adder_13_out), .cout(adder_13_cout));  // open: cin
  Adder #(.width(32)) adder_14 (
    .a(adder_13_out), .b(forczero_15_out), .out(adder_14_out), .cout(adder_14_cout));  // open: cin
  Adder #(.width(32)) adder_15 (
    .a(adder_14_out), .b(forczero_16_out), .out(adder_15_out), .cout(adder_15_cout));  // open: cin
  or or_1 (or_1_out, adder_1_cout, adder_2_cout, adder_3_cout, adder_4_cout, adder_5_cout, adder_6_cout, adder_7_cout, adder_8_cout, adder_9_cout, adder_10_cout, adder_11_cout, adder_12_cout, adder_13_cout, adder_14_cout, adder_15_cout);
  BitSelector #(.width(32)) bitselector_17 (.in(in_2), .out(bitselector_17_out), .sel(5'b10000));
  BitSelector #(.width(32)) bitselector_18 (.in(in_2), .out(bitselector_18_out), .sel(5'b10001));
  BitSelector #(.width(32)) bitselector_19 (.in(in_2), .out(bitselector_19_out), .sel(5'b10010));
  BitSelector #(.width(32)) bitselector_20 (.in(in_2), .out(bitselector_20_out), .sel(5'b10011));
  BitSelector #(.width(32)) bitselector_21 (.in(in_2), .out(bitselector_21_out), .sel(5'b10100));
  BitSelector #(.width(32)) bitselector_22 (.in(in_2), .out(bitselector_22_out), .sel(5'b10101));
  BitSelector #(.width(32)) bitselector_23 (.in(in_2), .out(bitselector_23_out), .sel(5'b10110));
  BitSelector #(.width(32)) bitselector_24 (.in(in_2), .out(bitselector_24_out), .sel(5'b10111));
  BitSelector #(.width(32)) bitselector_25 (.in(in_2), .out(bitselector_25_out), .sel(5'b11000));
  BitSelector #(.width(32)) bitselector_26 (.in(in_2), .out(bitselector_26_out), .sel(5'b11001));
  BitSelector #(.width(32)) bitselector_27 (.in(in_2), .out(bitselector_27_out), .sel(5'b11010));
  BitSelector #(.width(32)) bitselector_28 (.in(in_2), .out(bitselector_28_out), .sel(5'b11011));
  BitSelector #(.width(32)) bitselector_29 (.in(in_2), .out(bitselector_29_out), .sel(5'b11100));
  BitSelector #(.width(32)) bitselector_30 (.in(in_2), .out(bitselector_30_out), .sel(5'b11101));
  BitSelector #(.width(32)) bitselector_31 (.in(in_2), .out(bitselector_31_out), .sel(5'b11110));
  BitSelector #(.width(32)) bitselector_32 (.in(in_2), .out(bitselector_32_out), .sel({5{1'b1}}));
  or or_2 (Overflow, or_1_out, or_3_out);
  assign controlled_buffer_17_out = bitselector_17_out ? 5'b10000 : 5'bz;  // Controlled_Buffer controlled_buffer_17
  assign controlled_buffer_18_out = bitselector_18_out ? 5'b10001 : 5'bz;  // Controlled_Buffer controlled_buffer_18
  assign controlled_buffer_19_out = bitselector_19_out ? 5'b10010 : 5'bz;  // Controlled_Buffer controlled_buffer_19
  assign controlled_buffer_20_out = bitselector_20_out ? 5'b10011 : 5'bz;  // Controlled_Buffer controlled_buffer_20
  assign controlled_buffer_21_out = bitselector_21_out ? 5'b10100 : 5'bz;  // Controlled_Buffer controlled_buffer_21
  assign controlled_buffer_22_out = bitselector_22_out ? 5'b10101 : 5'bz;  // Controlled_Buffer controlled_buffer_22
  assign controlled_buffer_23_out = bitselector_23_out ? 5'b10110 : 5'bz;  // Controlled_Buffer controlled_buffer_23
  assign controlled_buffer_24_out = bitselector_24_out ? 5'b10111 : 5'bz;  // Controlled_Buffer controlled_buffer_24
  assign controlled_buffer_25_out = bitselector_25_out ? 5'b11000 : 5'bz;  // Controlled_Buffer controlled_buffer_25
  assign controlled_buffer_26_out = bitselector_26_out ? 5'b11001 : 5'bz;  // Controlled_Buffer controlled_buffer_26
  assign controlled_buffer_27_out = bitselector_27_out ? 5'b11010 : 5'bz;  // Controlled_Buffer controlled_buffer_27
  assign controlled_buffer_28_out = bitselector_28_out ? 5'b11011 : 5'bz;  // Controlled_Buffer controlled_buffer_28
  assign controlled_buffer_29_out = bitselector_29_out ? 5'b11100 : 5'bz;  // Controlled_Buffer controlled_buffer_29
  assign controlled_buffer_30_out = bitselector_30_out ? 5'b11101 : 5'bz;  // Controlled_Buffer controlled_buffer_30
  assign controlled_buffer_31_out = bitselector_31_out ? 5'b11110 : 5'bz;  // Controlled_Buffer controlled_buffer_31
  assign controlled_buffer_32_out = bitselector_32_out ? {5{1'b1}} : 5'bz;  // Controlled_Buffer controlled_buffer_32
  Shifter #(.width(32)) shifter_17 (.in(in_1), .\dist (controlled_buffer_17_out), .out(shifter_17_out));
  Shifter #(.width(32)) shifter_18 (.in(in_1), .\dist (controlled_buffer_18_out), .out(shifter_18_out));
  Shifter #(.width(32)) shifter_19 (.in(in_1), .\dist (controlled_buffer_19_out), .out(shifter_19_out));
  Shifter #(.width(32)) shifter_20 (.in(in_1), .\dist (controlled_buffer_20_out), .out(shifter_20_out));
  Shifter #(.width(32)) shifter_21 (.in(in_1), .\dist (controlled_buffer_21_out), .out(shifter_21_out));
  Shifter #(.width(32)) shifter_22 (.in(in_1), .\dist (controlled_buffer_22_out), .out(shifter_22_out));
  Shifter #(.width(32)) shifter_23 (.in(in_1), .\dist (controlled_buffer_23_out), .out(shifter_23_out));
  Shifter #(.width(32)) shifter_24 (.in(in_1), .\dist (controlled_buffer_24_out), .out(shifter_24_out));
  Shifter #(.width(32)) shifter_25 (.in(in_1), .\dist (controlled_buffer_25_out), .out(shifter_25_out));
  Shifter #(.width(32)) shifter_26 (.in(in_1), .\dist (controlled_buffer_26_out), .out(shifter_26_out));
  Shifter #(.width(32)) shifter_27 (.in(in_1), .\dist (controlled_buffer_27_out), .out(shifter_27_out));
  Shifter #(.width(32)) shifter_28 (.in(in_1), .\dist (controlled_buffer_28_out), .out(shifter_28_out));
  Shifter #(.width(32)) shifter_29 (.in(in_1), .\dist (controlled_buffer_29_out), .out(shifter_29_out));
  Shifter #(.width(32)) shifter_30 (.in(in_1), .\dist (controlled_buffer_30_out), .out(shifter_30_out));
  Shifter #(.width(32)) shifter_31 (.in(in_1), .\dist (controlled_buffer_31_out), .out(shifter_31_out));
  Shifter #(.width(32)) shifter_32 (.in(in_1), .\dist (controlled_buffer_32_out), .out(shifter_32_out));
  ForcZero forczero_17 (.Input(shifter_17_out), .Out(forczero_17_out), .Enabler(bitselector_17_out));
  ForcZero forczero_18 (.Input(shifter_18_out), .Out(forczero_18_out), .Enabler(bitselector_18_out));
  ForcZero forczero_19 (.Input(shifter_19_out), .Out(forczero_19_out), .Enabler(bitselector_19_out));
  ForcZero forczero_20 (.Input(shifter_20_out), .Out(forczero_20_out), .Enabler(bitselector_20_out));
  ForcZero forczero_21 (.Input(shifter_21_out), .Out(forczero_21_out), .Enabler(bitselector_21_out));
  ForcZero forczero_22 (.Input(shifter_22_out), .Out(forczero_22_out), .Enabler(bitselector_22_out));
  ForcZero forczero_23 (.Input(shifter_23_out), .Out(forczero_23_out), .Enabler(bitselector_23_out));
  ForcZero forczero_24 (.Input(shifter_24_out), .Out(forczero_24_out), .Enabler(bitselector_24_out));
  ForcZero forczero_25 (.Input(shifter_25_out), .Out(forczero_25_out), .Enabler(bitselector_25_out));
  ForcZero forczero_26 (.Input(shifter_26_out), .Out(forczero_26_out), .Enabler(bitselector_26_out));
  ForcZero forczero_27 (.Input(shifter_27_out), .Out(forczero_27_out), .Enabler(bitselector_27_out));
  ForcZero forczero_28 (.Input(shifter_28_out), .Out(forczero_28_out), .Enabler(bitselector_28_out));
  ForcZero forczero_29 (.Input(shifter_29_out), .Out(forczero_29_out), .Enabler(bitselector_29_out));
  ForcZero forczero_30 (.Input(shifter_30_out), .Out(forczero_30_out), .Enabler(bitselector_30_out));
  ForcZero forczero_31 (.Input(shifter_31_out), .Out(forczero_31_out), .Enabler(bitselector_31_out));
  ForcZero forczero_32 (.Input(shifter_32_out), .Out(forczero_32_out), .Enabler(bitselector_32_out));
  Adder #(.width(32)) adder_16 (
    .a(forczero_17_out), .b(forczero_18_out), .out(adder_16_out), .cout(adder_16_cout));  // open: cin
  Adder #(.width(32)) adder_17 (
    .a(adder_16_out), .b(forczero_19_out), .out(adder_17_out), .cout(adder_17_cout));  // open: cin
  Adder #(.width(32)) adder_18 (
    .a(adder_17_out), .b(forczero_20_out), .out(adder_18_out), .cout(adder_18_cout));  // open: cin
  Adder #(.width(32)) adder_19 (
    .a(adder_18_out), .b(forczero_21_out), .out(adder_19_out), .cout(adder_19_cout));  // open: cin
  Adder #(.width(32)) adder_20 (
    .a(adder_19_out), .b(forczero_22_out), .out(adder_20_out), .cout(adder_20_cout));  // open: cin
  Adder #(.width(32)) adder_21 (
    .a(adder_20_out), .b(forczero_23_out), .out(adder_21_out), .cout(adder_21_cout));  // open: cin
  Adder #(.width(32)) adder_22 (
    .a(adder_21_out), .b(forczero_24_out), .out(adder_22_out), .cout(adder_22_cout));  // open: cin
  Adder #(.width(32)) adder_23 (
    .a(adder_22_out), .b(forczero_25_out), .out(adder_23_out), .cout(adder_23_cout));  // open: cin
  Adder #(.width(32)) adder_24 (
    .a(adder_23_out), .b(forczero_26_out), .out(adder_24_out), .cout(adder_24_cout));  // open: cin
  Adder #(.width(32)) adder_25 (
    .a(adder_24_out), .b(forczero_27_out), .out(adder_25_out), .cout(adder_25_cout));  // open: cin
  Adder #(.width(32)) adder_26 (
    .a(adder_25_out), .b(forczero_28_out), .out(adder_26_out), .cout(adder_26_cout));  // open: cin
  Adder #(.width(32)) adder_27 (
    .a(adder_26_out), .b(forczero_29_out), .out(adder_27_out), .cout(adder_27_cout));  // open: cin
  Adder #(.width(32)) adder_28 (
    .a(adder_27_out), .b(forczero_30_out), .out(adder_28_out), .cout(adder_28_cout));  // open: cin
  Adder #(.width(32)) adder_29 (
    .a(adder_28_out), .b(forczero_31_out), .out(adder_29_out), .cout(adder_29_cout));  // open: cin
  Adder #(.width(32)) adder_30 (
    .a(adder_29_out), .b(forczero_32_out), .out(adder_30_out), .cout(adder_30_cout));  // open: cin
  Adder #(.width(32)) adder_31 (.a(adder_30_out), .b(adder_15_out), .out(out_4), .cout(adder_31_cout));  // open: cin
  or or_3 (or_3_out, adder_16_cout, adder_17_cout, adder_18_cout, adder_19_cout, adder_20_cout, adder_21_cout, adder_22_cout, adder_23_cout, adder_24_cout, adder_25_cout, adder_26_cout, adder_27_cout, adder_28_cout, adder_29_cout, adder_30_cout, adder_31_cout);
endmodule

module ForcZero (
  input  Enabler,
  input  [31:0] Input,
  output [31:0] Out
);

  Demultiplexer #(.width(32), .disabled(0), .enable("false")) demultiplexer_1 (
    .out1(Out), .in(Input), .sel(Enabler));  // open: out0
endmodule

module Divisor (
  input  [31:0] Dividendo,
  input  [31:0] Divisor,
  input  Enable_Clock,
  output [31:0] Result,
  output Ready
);

  wire and_1_out, clock_1_out, not_1_out;
  wire [31:0] adder_1_out, counter_1_q, multiplicador_1_out_4;

  Counter #(.width(32), .max('hffffffff), .ongoal("stay")) counter_1 (
    .Q(counter_1_q), .clk(and_1_out), .clr(Enable_Clock));  // open: load, D, count, carry
  and and_1 (and_1_out, clock_1_out, not_1_out);
  Clock clock_1 (.out(clock_1_out));
  Adder #(.width(32)) adder_1 (.a(32'h1), .b(counter_1_q), .out(adder_1_out));  // open: cin, cout
  Multiplicador multiplicador_1 (.in_1(Divisor), .in_2(adder_1_out), .out_4(multiplicador_1_out_4));  // open: Overflow
  not not_1 (not_1_out, Ready);
  Subtractor #(.width(32)) subtractor_1 (.a(Dividendo), .b(multiplicador_1_out_4), .bout(Ready));  // open: out, bin
  _32bit_flipflop u_32bit_flipflop_1 (.in(counter_1_q), .Enable(Ready), .out(Result));
endmodule

module _32bit_flipflop (
  input  [31:0] in,
  input  Enable,
  output [31:0] out
);

  // _4bit_flipflop 4bit_flipflop_1: pin names not known; wires that end beside it: in[3:0], Enable, out[3:0]
  // _4bit_flipflop 4bit_flipflop_2: pin names not known; wires that end beside it: in[7:4], Enable, out[7:4]
  // _4bit_flipflop 4bit_flipflop_3: pin names not known; wires that end beside it: in[11:8], Enable, out[11:8]
  // _4bit_flipflop 4bit_flipflop_4: pin names not known; wires that end beside it: in[15:12], Enable, out[15:12]
  // _4bit_flipflop 4bit_flipflop_5: pin names not known; wires that end beside it: in[19:16], Enable, out[19:16]
  // _4bit_flipflop 4bit_flipflop_6: pin names not known; wires that end beside it: in[23:20], Enable, out[23:20]
  // _4bit_flipflop 4bit_flipflop_7: pin names not known; wires that end beside it: in[27:24], Enable, out[27:24]
  // _4bit_flipflop 4bit_flipflop_8: pin names not known; wires that end beside it: in[31:28], Enable, out[31:28]
endmodule

module MultiplicadorBarato (
  input  [31:0] Coeficiente,
  input  [31:0] Coeficiente_2,
  input  Enable_Clock,
  output [31:0] out_4
);

  wire and_1_out, bitselector_1_out, clock_1_out, counter_1_carry, not_1_out, not_2_out;
  wire [4:0] controlled_buffer_1_out, counter_1_q;
  wire [31:0] adder_1_out, controlled_buffer_2_out, forczero_1_out, shifter_1_out;

  Clock clock_1 (.out(clock_1_out));
  Counter #(.width(5), .max('h1f), .ongoal("stay")) counter_1 (
    .Q(counter_1_q), .carry(counter_1_carry), .clk(clock_1_out), .clr(Enable_Clock));  // open: load, D, count
  BitSelector #(.width(32)) bitselector_1 (.in(Coeficiente_2), .out(bitselector_1_out), .sel(counter_1_q));
  assign controlled_buffer_1_out = bitselector_1_out ? counter_1_q : 5'bz;  // Controlled_Buffer controlled_buffer_1
  not not_1 (not_1_out, counter_1_carry);
  Shifter #(.width(32), .shift("lr")) shifter_1 (
    .in(Coeficiente), .\dist (controlled_buffer_1_out), .out(shifter_1_out));
  ForcZero forczero_1 (.Input(shifter_1_out), .Out(forczero_1_out), .Enabler(bitselector_1_out));
  Adder #(.width(32)) adder_1 (.a(out_4), .b(forczero_1_out), .out(adder_1_out));  // open: cin, cout
  assign controlled_buffer_2_out = Enable_Clock ? {32{1'b0}} : 32'bz;  // Controlled_Buffer controlled_buffer_2
  and and_1 (and_1_out, not_1_out, clock_1_out);
  assign controlled_buffer_2_out = not_2_out ? adder_1_out : 32'bz;  // Controlled_Buffer controlled_buffer_3
  not not_2 (not_2_out, Enable_Clock);
  _32bit_flipflop u_32bit_flipflop_1 (.in(controlled_buffer_2_out), .Enable(and_1_out), .out(out_4));
  // Flip_flop_D flip_flop_d_1: pin names not known
endmodule

module Custom_FlipFlop (
  input  reset,
  input  Enable,
  input  in_3,
  output out_4,
  output out_5
);

  wire and_1_out;

  and and_1 (and_1_out, reset, Enable);
  nor nor_1 (out_4, and_1_out, out_5);
  nor nor_2 (out_5, out_4, in_3);
endmodule
