// Logisim project flipFlops.circ as structural Verilog: 2 circuits, main circuit SR
module SR (
  input  RESET,
  input  SET,
  input  RESET_2,
  input  SET_2,
  input  RESET_3,
  input  ENABLE,
  input  SET_3,
  output Q,
  output Q_prime,
  output Q_2,
  output Q_prime_2,
  output Q_3,
  output Q_prime_3
);

  wire and_1_out, and_2_out;

  and and_1 (and_1_out, RESET_3, ENABLE);
  and and_2 (and_2_out, ENABLE, SET_3);
  nor nor_1 (Q, RESET, Q_prime);
  nor nor_2 (Q_prime, Q, SET);
  nand nand_1 (Q_2, RESET_2, Q_prime_2);
  nand nand_2 (Q_prime_2, Q_2, SET_2);
  nor nor_3 (Q_3, and_1_out, Q_prime_3);
  nor nor_4 (Q_prime_3, Q_3, and_2_out);

  // Notes on the sheet:
  //   SR
  //   FLIP FLOPS
endmodule

module D (
  input  ENABLE,
  input  D,
  output out_3,
  output out_4
);

  wire and_1_out, and_2_out, not_1_out;

  not not_1 (not_1_out, D);
  and and_1 (and_1_out, not_1_out, ENABLE);
  and and_2 (and_2_out, ENABLE, D);
  nor nor_1 (out_3, and_1_out, out_4);
  nor nor_2 (out_4, out_3, and_2_out);
endmodule
